// Logisim project ALU.circ as structural Verilog
module _2COMP (
  input  ON_OFF,
  input  In___0,
  input  In___1,
  input  In___2,
  input  In___3,
  input  In___4,
  input  In___5,
  input  In___6,
  input  In___7,
  output Out___0,
  output Out___1,
  output Out___2,
  output Out___3,
  output Out___4,
  output Out___5,
  output Out___6,
  output Out___7
);

  wire adder_1_cout, adder_1_out, adder_2_cout, adder_2_out, adder_3_cout, adder_3_out, adder_4_cout,
       adder_4_out, adder_5_cout, adder_5_out, adder_6_cout, adder_6_out, adder_7_out, and_1_out, and_2_out,
       and_3_out, and_4_out, and_5_out, and_6_out, and_7_out, not_1_out, not_2_out, not_3_out, not_4_out,
       not_5_out, not_6_out, not_7_out, not_8_out;

  not not_1 (not_1_out, In___1);
  and and_1 (and_1_out, ON_OFF, not_1_out);
  not not_2 (not_2_out, In___2);
  not not_3 (not_3_out, In___0);
  Adder #(.width(1)) adder_1 (.a(not_3_out), .b(and_1_out), .out(adder_1_out), .cout(adder_1_cout));  // open: cin
  and and_2 (and_2_out, ON_OFF, not_2_out);
  and and_3 (and_3_out, ON_OFF, not_4_out);
  not not_4 (not_4_out, In___3);
  not not_5 (not_5_out, In___4);
  Adder #(.width(1)) adder_2 (.a(adder_1_cout), .b(and_2_out), .out(adder_2_out), .cout(adder_2_cout));  // open: cin
  and and_4 (and_4_out, ON_OFF, not_5_out);
  not not_6 (not_6_out, In___5);
  Multiplexer #(.enable("false")) multiplexer_1 (.in0(In___1), .in1(adder_1_out), .out(Out___1), .sel(ON_OFF));
  Multiplexer #(.enable("false")) multiplexer_2 (.in0(In___2), .in1(adder_2_out), .out(Out___2), .sel(ON_OFF));
  Adder #(.width(1)) adder_3 (.a(adder_2_cout), .b(and_3_out), .out(adder_3_out), .cout(adder_3_cout));  // open: cin
  Adder #(.width(1)) adder_4 (.a(adder_3_cout), .b(and_4_out), .out(adder_4_out), .cout(adder_4_cout));  // open: cin
  and and_5 (and_5_out, ON_OFF, not_6_out);
  not not_7 (not_7_out, In___6);
  Multiplexer #(.enable("false")) multiplexer_3 (.in0(In___3), .in1(adder_3_out), .out(Out___3), .sel(ON_OFF));
  Adder #(.width(1)) adder_5 (.a(adder_4_cout), .b(and_5_out), .out(adder_5_out), .cout(adder_5_cout));  // open: cin
  and and_6 (and_6_out, ON_OFF, not_7_out);
  and and_7 (and_7_out, ON_OFF, not_8_out);
  not not_8 (not_8_out, In___7);
  Multiplexer #(.enable("false")) multiplexer_4 (.in0(In___4), .in1(adder_4_out), .out(Out___4), .sel(ON_OFF));
  Adder #(.width(1)) adder_6 (.a(adder_5_cout), .b(and_6_out), .out(adder_6_out), .cout(adder_6_cout));  // open: cin
  Adder #(.width(1)) adder_7 (.a(adder_6_cout), .b(and_7_out), .out(adder_7_out));  // open: cin, cout
  Multiplexer #(.enable("false")) multiplexer_5 (.in0(In___5), .in1(adder_5_out), .out(Out___5), .sel(ON_OFF));
  Multiplexer #(.enable("false")) multiplexer_6 (.in0(In___6), .in1(adder_6_out), .out(Out___6), .sel(ON_OFF));
  Multiplexer #(.enable("false")) multiplexer_7 (.in0(In___7), .in1(adder_7_out), .out(Out___7), .sel(ON_OFF));

  assign Out___0 = In___0;
endmodule

module ALU (
  input  MULTIPLY,
  input  R___0,
  input  R___1,
  input  R___2,
  input  R___3,
  input  R___4,
  input  R___5,
  input  R___6,
  input  R___7,
  input  SUBTRACT,
  input  L___0,
  input  L___1,
  input  L___2,
  input  L___3,
  input  L___4,
  input  L___5,
  input  L___6,
  input  L___7,
  output A___0,
  output A___1,
  output A___2,
  output A___3,
  output A___4,
  output A___5,
  output A___6,
  output A___7,
  output Zero,
  output Overflow,
  output Negative
);

  wire adder_1_cout, adder_1_out, adder_2_cout, adder_2_out, adder_3_cout, adder_3_out, adder_4_cout,
       adder_4_out, adder_5_cout, adder_5_out, adder_6_cout, adder_6_out, adder_7_cout, adder_7_out,
       adder_8_cout, adder_8_out, adder_9_cout, adder_9_out, adder_10_cout, adder_10_out, adder_11_out,
       adder_12_cout, adder_12_out, adder_13_cout, adder_13_out, adder_14_cout, adder_14_out, adder_15_out,
       adder_16_cout, adder_16_out, adder_17_out, adder_18_cout, adder_18_out, adder_19_cout, adder_19_out,
       adder_20_cout, adder_20_out, adder_21_out, adder_22_out, adder_23_cout, adder_23_out, adder_24_cout,
       adder_24_out, adder_25_cout, adder_25_out, adder_26_cout, adder_26_out, adder_27_cout, adder_27_out,
       adder_28_cout, adder_28_out, adder_29_cout, adder_29_out, adder_30_out, adder_31_cout, adder_31_out,
       adder_32_cout, adder_32_out, adder_33_cout, adder_33_out, adder_34_cout, adder_34_out, adder_35_cout,
       adder_35_out, adder_36_out, and_1_out, and_2_out, and_3_out, and_4_out, and_5_out, and_6_out,
       and_7_out, and_8_out, and_9_out, and_10_out, and_11_out, and_12_out, and_13_out, and_14_out,
       and_15_out, and_16_out, and_17_out, and_18_out, and_19_out, and_20_out, and_21_out, and_22_out,
       and_23_out, and_24_out, and_25_out, and_27_out, and_28_out, and_29_out, and_30_out, and_31_out,
       and_32_out, and_33_out, and_34_out, and_35_out, and_36_out, and_37_out, and_38_out, and_39_out,
       and_40_out, and_41_out, and_42_out, and_43_out, and_45_out, and_46_out, and_47_out, and_48_out,
       and_50_out, and_51_out, and_52_out, and_53_out, and_54_out, and_55_out, and_56_out, and_57_out,
       n2comp_1_out___0, n2comp_1_out___1, n2comp_1_out___2, n2comp_1_out___3, n2comp_1_out___4,
       n2comp_1_out___5, n2comp_1_out___6, n2comp_1_out___7, n2comp_2_out___0, n2comp_2_out___1,
       n2comp_2_out___2, n2comp_2_out___3, n2comp_2_out___4, n2comp_2_out___5, n2comp_2_out___6,
       n2comp_2_out___7, not_1_out, not_2_out, not_3_out, not_4_out, not_5_out, not_6_out, not_7_out,
       not_8_out, not_9_out, not_10_out, not_11_out, not_12_out, not_13_out, not_14_out, not_15_out,
       not_16_out, not_17_out, not_18_out, not_19_out, or_1_out, or_2_out, or_3_out, or_4_out, or_5_out,
       or_6_out, or_7_out, or_8_out, or_9_out;

  not not_1 (not_1_out, MULTIPLY);
  not not_2 (not_2_out, R___7);
  and and_1 (and_1_out, L___7, not_2_out);
  or or_1 (or_1_out, L___7, not_2_out);
  not not_3 (not_3_out, and_1_out);
  and and_2 (and_2_out, not_3_out, or_1_out, and_3_out);
  not not_4 (not_4_out, R___6);
  and and_3 (and_3_out, L___6, not_4_out);
  or or_2 (or_2_out, L___6, not_4_out);
  not not_5 (not_5_out, and_2_out);
  and and_4 (and_4_out, not_5_out, or_2_out, and_5_out);
  or or_3 (or_3_out, and_15_out, and_13_out, and_11_out, and_9_out, and_6_out, and_4_out, and_2_out, and_1_out);
  not not_6 (not_6_out, R___5);
  and and_5 (and_5_out, L___5, not_6_out);
  or or_4 (or_4_out, L___5, not_6_out);
  not not_7 (not_7_out, and_4_out);
  and and_6 (and_6_out, not_7_out, or_4_out, and_8_out);
  not not_8 (not_8_out, R___4);
  not not_9 (not_9_out, R___3);
  and and_7 (and_7_out, L___3, not_9_out);
  and and_8 (and_8_out, L___4, not_8_out);
  or or_5 (or_5_out, L___4, not_8_out);
  not not_10 (not_10_out, and_6_out);
  and and_9 (and_9_out, not_10_out, or_5_out, and_7_out);
  not not_11 (not_11_out, R___2);
  or or_6 (or_6_out, L___3, not_9_out);
  and and_10 (and_10_out, L___2, not_11_out);
  or or_7 (or_7_out, L___2, not_11_out);
  not not_12 (not_12_out, and_9_out);
  and and_11 (and_11_out, not_12_out, or_6_out, and_10_out);
  not not_13 (not_13_out, R___0);
  not not_14 (not_14_out, R___1);
  or or_8 (or_8_out, L___1, not_14_out);
  and and_12 (and_12_out, L___1, not_14_out);
  not not_15 (not_15_out, and_11_out);
  and and_13 (and_13_out, not_15_out, or_7_out, and_12_out);
  and and_14 (and_14_out, L___0, not_13_out);
  not not_16 (not_16_out, and_13_out);
  and and_15 (and_15_out, not_16_out, or_8_out, and_14_out);
  _2COMP u_2comp_1 (
    .ON_OFF(SUBTRACT), .In___0(L___0), .In___1(L___1), .In___2(L___2), .In___3(L___3), .In___4(L___4),
    .In___5(L___5), .In___6(L___6), .In___7(L___7), .Out___0(n2comp_1_out___0), .Out___1(n2comp_1_out___1),
    .Out___2(n2comp_1_out___2), .Out___3(n2comp_1_out___3), .Out___4(n2comp_1_out___4),
    .Out___5(n2comp_1_out___5), .Out___6(n2comp_1_out___6), .Out___7(n2comp_1_out___7));
  and and_16 (and_16_out, SUBTRACT, or_3_out);
  Adder #(.width(1)) adder_1 (.a(R___0), .b(n2comp_1_out___0), .out(adder_1_out), .cout(adder_1_cout));  // open: cin
  Adder #(.width(1)) adder_2 (
    .a(R___1), .b(n2comp_1_out___1), .out(adder_2_out), .cin(adder_1_cout), .cout(adder_2_cout));
  Adder #(.width(1)) adder_3 (
    .a(R___2), .b(n2comp_1_out___2), .out(adder_3_out), .cin(adder_2_cout), .cout(adder_3_cout));
  Adder #(.width(1)) adder_4 (
    .a(R___3), .b(n2comp_1_out___3), .out(adder_4_out), .cin(adder_3_cout), .cout(adder_4_cout));
  Adder #(.width(1)) adder_5 (
    .a(R___4), .b(n2comp_1_out___4), .out(adder_5_out), .cin(adder_4_cout), .cout(adder_5_cout));
  Adder #(.width(1)) adder_6 (
    .a(R___5), .b(n2comp_1_out___5), .out(adder_6_out), .cin(adder_5_cout), .cout(adder_6_cout));
  Adder #(.width(1)) adder_7 (
    .a(R___6), .b(n2comp_1_out___6), .out(adder_7_out), .cin(adder_6_cout), .cout(adder_7_cout));
  Adder #(.width(1)) adder_8 (
    .a(R___7), .b(n2comp_1_out___7), .out(adder_8_out), .cin(adder_7_cout), .cout(adder_8_cout));
  not not_17 (not_17_out, not_1_out);
  not not_18 (not_18_out, SUBTRACT);
  and and_17 (and_17_out, R___0, L___0);
  and and_18 (and_18_out, L___0, R___1);
  and and_19 (and_19_out, R___4, L___0);
  and and_20 (and_20_out, R___3, L___1);
  and and_21 (and_21_out, R___6, L___0);
  and and_22 (and_22_out, R___5, L___1);
  and and_23 (and_23_out, R___7, L___0);
  and and_24 (and_24_out, R___6, L___1);
  Multiplexer #(.enable("false")) multiplexer_1 (
    .in0(n2comp_2_out___5), .in1(adder_6_out), .out(A___5), .sel(not_1_out));
  Multiplexer #(.enable("false")) multiplexer_2 (
    .in0(n2comp_2_out___6), .in1(adder_7_out), .out(A___6), .sel(not_1_out));
  Multiplexer #(.enable("false")) multiplexer_3 (
    .in0(n2comp_2_out___7), .in1(adder_8_out), .out(A___7), .sel(not_1_out));
  and and_25 (and_25_out, SUBTRACT, not_17_out);
  and and_26 (Overflow, adder_8_cout, not_1_out, not_18_out);
  and and_27 (and_27_out, L___1, R___0);
  and and_28 (and_28_out, R___2, L___2);
  and and_29 (and_29_out, R___4, L___2);
  and and_30 (and_30_out, R___5, L___2);
  Multiplexer #(.enable("false")) multiplexer_4 (
    .in0(n2comp_2_out___1), .in1(adder_2_out), .out(A___1), .sel(not_1_out));
  Multiplexer #(.enable("false")) multiplexer_5 (
    .in0(n2comp_2_out___2), .in1(adder_3_out), .out(A___2), .sel(not_1_out));
  Multiplexer #(.enable("false")) multiplexer_6 (
    .in0(n2comp_2_out___3), .in1(adder_4_out), .out(A___3), .sel(not_1_out));
  Multiplexer #(.enable("false")) multiplexer_7 (
    .in0(n2comp_2_out___4), .in1(adder_5_out), .out(A___4), .sel(not_1_out));
  and and_31 (and_31_out, SUBTRACT, Zero, not_17_out);
  or or_9 (or_9_out, and_25_out, and_16_out);
  Adder #(.width(1)) adder_9 (.a(and_18_out), .b(and_27_out), .out(adder_9_out), .cout(adder_9_cout));  // open: cin
  and and_32 (and_32_out, R___2, L___0);
  Adder #(.width(1)) adder_10 (
    .a(and_20_out), .b(and_28_out), .out(adder_10_out), .cin(and_19_out), .cout(adder_10_cout));
  and and_33 (and_33_out, R___1, L___3);
  and and_34 (and_34_out, R___3, L___3);
  Adder #(.width(1)) adder_11 (.a(and_24_out), .b(and_30_out), .out(adder_11_out), .cin(and_23_out));  // open: cout
  and and_35 (and_35_out, R___4, L___3);
  Multiplexer #(.enable("false")) multiplexer_8 (
    .in0(n2comp_2_out___0), .in1(adder_1_out), .out(A___0), .sel(not_1_out));
  Adder #(.width(1)) adder_12 (
    .a(and_32_out), .b(and_36_out), .out(adder_12_out), .cin(adder_9_cout), .cout(adder_12_cout));
  and and_36 (and_36_out, L___1, R___1);
  and and_37 (and_37_out, R___0, L___2);
  and and_38 (and_38_out, R___0, L___4);
  and and_39 (and_39_out, R___5, L___0);
  and and_40 (and_40_out, R___2, L___4);
  and and_41 (and_41_out, R___1, L___5);
  and and_42 (and_42_out, R___3, L___4);
  and and_43 (and_43_out, R___2, L___5);
  and and_44 (Zero, ~A___0, ~A___1, ~A___2, ~A___3, ~A___4, ~A___5, ~A___6, ~A___7, ~Overflow);  // AND_Gate
  not not_19 (not_19_out, and_31_out);
  Adder #(.width(1)) adder_13 (
    .a(adder_12_out), .b(and_37_out), .out(adder_13_out), .cout(adder_13_cout));  // open: cin
  and and_45 (and_45_out, R___3, L___0);
  Adder #(.width(1)) adder_14 (
    .a(and_33_out), .b(and_38_out), .out(adder_14_out), .cin(adder_10_out), .cout(adder_14_cout));
  and and_46 (and_46_out, R___4, L___1);
  and and_47 (and_47_out, R___0, L___6);
  Adder #(.width(1)) adder_15 (.a(and_35_out), .b(and_42_out), .out(adder_15_out), .cin(adder_11_out));  // open: cout
  and and_48 (and_48_out, R___1, L___6);
  and and_49 (Negative, not_19_out, or_9_out);
  and and_50 (and_50_out, R___2, L___1);
  and and_51 (and_51_out, R___3, L___2);
  Adder #(.width(1)) adder_16 (
    .a(and_41_out), .b(and_47_out), .out(adder_16_out), .cin(and_40_out), .cout(adder_16_cout));
  Adder #(.width(1)) adder_17 (
    .a(adder_16_cout), .b(adder_15_out), .out(adder_17_out), .cin(adder_20_cout));  // open: cout
  and and_52 (and_52_out, R___0, L___7);
  and and_53 (and_53_out, R___1, L___2);
  and and_54 (and_54_out, R___0, L___3);
  Adder #(.width(1)) adder_18 (
    .a(and_39_out), .b(and_46_out), .out(adder_18_out), .cin(adder_14_cout), .cout(adder_18_cout));
  and and_55 (and_55_out, R___2, L___3);
  and and_56 (and_56_out, R___1, L___4);
  Adder #(.width(1)) adder_19 (
    .a(and_22_out), .b(adder_20_out), .out(adder_19_out), .cin(and_21_out), .cout(adder_19_cout));
  Adder #(.width(1)) adder_20 (
    .a(and_34_out), .b(adder_16_out), .out(adder_20_out), .cin(and_29_out), .cout(adder_20_cout));
  Adder #(.width(1)) adder_21 (
    .a(adder_19_cout), .b(adder_17_out), .out(adder_21_out), .cin(adder_29_cout));  // open: cout
  Adder #(.width(1)) adder_22 (.a(and_48_out), .b(and_52_out), .out(adder_22_out), .cin(and_43_out));  // open: cout
  Adder #(.width(1)) adder_23 (
    .a(adder_13_cout), .b(adder_12_cout), .out(adder_23_out), .cout(adder_23_cout));  // open: cin
  Adder #(.width(1)) adder_24 (
    .a(and_45_out), .b(and_50_out), .out(adder_24_out), .cin(adder_23_out), .cout(adder_24_cout));
  Adder #(.width(1)) adder_25 (
    .a(and_53_out), .b(and_54_out), .out(adder_25_out), .cin(adder_24_out), .cout(adder_25_cout));
  Adder #(.width(1)) adder_26 (
    .a(adder_24_cout), .b(adder_23_cout), .out(adder_26_out), .cin(adder_25_cout), .cout(adder_26_cout));
  Adder #(.width(1)) adder_27 (
    .a(and_51_out), .b(and_55_out), .out(adder_27_out), .cin(adder_10_cout), .cout(adder_27_cout));
  Adder #(.width(1)) adder_28 (
    .a(adder_18_out), .b(and_56_out), .out(adder_28_out), .cin(adder_32_out), .cout(adder_28_cout));
  and and_57 (and_57_out, R___0, L___5);
  Adder #(.width(1)) adder_29 (
    .a(adder_27_cout), .b(adder_19_out), .out(adder_29_out), .cin(adder_18_cout), .cout(adder_29_cout));
  Adder #(.width(1)) adder_30 (
    .a(adder_21_out), .b(adder_22_out), .out(adder_30_out), .cin(adder_34_cout));  // open: cout
  _2COMP u_2comp_2 (
    .ON_OFF(SUBTRACT), .In___0(and_17_out), .In___1(adder_9_out), .In___2(adder_13_out),
    .In___3(adder_25_out), .In___4(adder_31_out), .In___5(adder_33_out), .In___6(adder_35_out),
    .In___7(adder_36_out), .Out___0(n2comp_2_out___0), .Out___1(n2comp_2_out___1),
    .Out___2(n2comp_2_out___2), .Out___3(n2comp_2_out___3), .Out___4(n2comp_2_out___4),
    .Out___5(n2comp_2_out___5), .Out___6(n2comp_2_out___6), .Out___7(n2comp_2_out___7));
  Adder #(.width(1)) adder_31 (
    .a(adder_14_out), .b(adder_26_out), .out(adder_31_out), .cout(adder_31_cout));  // open: cin
  Adder #(.width(1)) adder_32 (
    .a(adder_31_cout), .b(adder_27_out), .out(adder_32_out), .cin(adder_26_cout), .cout(adder_32_cout));
  Adder #(.width(1)) adder_33 (
    .a(adder_28_out), .b(and_57_out), .out(adder_33_out), .cout(adder_33_cout));  // open: cin
  Adder #(.width(1)) adder_34 (
    .a(adder_32_cout), .b(adder_29_out), .out(adder_34_out), .cin(adder_28_cout), .cout(adder_34_cout));
  Adder #(.width(1)) adder_35 (
    .a(adder_33_cout), .b(adder_34_out), .out(adder_35_out), .cout(adder_35_cout));  // open: cin
  Adder #(.width(1)) adder_36 (.a(adder_35_cout), .b(adder_30_out), .out(adder_36_out));  // open: cin, cout

  // Notes on the sheet:
  //   Note: Overflow does not get triggered when subtracting or multiplying
  //   Zero does not check past the first 8 bits with multiplication
endmodule
