// Logisim project HAL.circ as structural Verilog: 48 circuits, main circuit main
module main (
  input  in_1,
  input  _0,
  input  _1,
  input  _2,
  input  _3,
  input  _4,
  input  _5,
  input  _6,
  input  _7,
  input  _8,
  input  _9,
  input  in_12,
  input  in_13,
  input  in_14,
  input  Number_in_ROM,
  input  in_16,
  input  in_17,
  input  in_18,
  input  in_19,
  input  in_20,
  input  in_21,
  output finished,
  output zero,
  output overflow,
  output negative
);

  wire actual_load_from_ram_1_ar_input, actual_load_from_ram_1_mar_input, actual_load_from_ram_1_mar_output,
       actual_load_from_ram_1_mbr_input, actual_load_from_ram_1_mbr_output, actual_load_from_ram_1_out_8,
       actual_load_from_ram_1_out_9, actual_load_from_ram_1_out_10, actual_load_from_ram_1_out_11,
       actual_load_from_ram_1_out_12, actual_load_from_ram_1_out_13, actual_load_from_ram_1_out_15,
       actual_load_from_ram_1_output_from_ram, actual_load_from_ram_1_output_ram,
       actual_load_from_ram_1_r1_input, actual_load_from_ram_1_r2_input, add_sub_1_alu_output,
       add_sub_1_l_input, add_sub_1_out_6, add_sub_1_out_7, add_sub_1_out_8, add_sub_1_out_12,
       add_sub_1_r1_output, add_sub_1_r2_input, add_sub_1_r2_output, add_sub_1_r_input, alu_1_a___0,
       alu_1_a___1, alu_1_a___2, alu_1_a___3, alu_1_a___4, alu_1_a___5, alu_1_a___6, alu_1_a___7,
       alu_1_negative, alu_1_overflow, alu_1_zero, and_1_out, beq_bnq_1_out_26, beq_bnq_1_out_27,
       beq_bnq_1_out_28, beq_bnq_1_out_29, beq_bnq_1_out_30, beq_bnq_1_out_31, beq_bnq_1_out_32,
       choose_inst_1_out_4, clock_1_out, display_1_mbr_output, display_1_out_4, display_1_out_5,
       display_1_out_6, display_1_out_7, display_1_out_8, display_1_out_9, display_1_out_11,
       display_1_out_12, either_1_out_9, either_1_out_10, either_1_out_11, either_1_out_12,
       general_register_1_out_13, general_register_1_out_14, general_register_1_out_15,
       general_register_1_out_16, general_register_1_out_17, general_register_1_out_18,
       general_register_1_out_19, general_register_1_out_20, general_register_1_out_21,
       general_register_1_out_22, general_register_1_out_23, general_register_1_out_24,
       general_register_1_out_25, general_register_1_out_26, general_register_1_out_27,
       general_register_1_out_28, get_input_1_input_output, get_input_1_mbr_input, get_input_1_mbr_output,
       get_input_1_mbr_r_c, get_input_1_out_4, get_input_1_out_5, get_input_1_r1_input, get_input_1_r2_input,
       get_next_instruction_1_ar_input, get_next_instruction_1_ir_input, get_next_instruction_1_mar_input,
       get_next_instruction_1_mar_output, get_next_instruction_1_mar_r_c, get_next_instruction_1_mbr_input,
       get_next_instruction_1_mbr_output, get_next_instruction_1_out_3, get_next_instruction_1_out_4,
       get_next_instruction_1_output_from_ram, get_next_instruction_1_pc_output,
       get_next_instruction_1_ram_output, input_pins_1_out_14, input_pins_1_out_15, input_pins_1_out_16,
       input_pins_1_out_17, instruction_chooser_1_out_11, instruction_chooser_1_out_12,
       instruction_chooser_1_out_13, instruction_chooser_1_out_14, instruction_chooser_1_out_15,
       instruction_chooser_1_out_16, instruction_chooser_1_out_17, instruction_chooser_1_out_18,
       instruction_chooser_1_out_19, instruction_chooser_1_out_20, instruction_chooser_1_out_21,
       instruction_chooser_1_out_22, instruction_chooser_1_out_23, instruction_chooser_1_out_24,
       instruction_chooser_1_out_25, instruction_chooser_1_out_26, ir_1_out_12, ir_1_out_13, ir_1_out_14,
       ir_1_out_15, ir_1_out_16, ir_1_out_17, ir_1_out_18, ir_1_out_19, L_out_13, L_out_14, L_out_15,
       L_out_16, L_out_17, L_out_18, L_out_19, L_out_20, load_from_ram_1_ar_input, load_from_ram_1_dr_input,
       load_from_ram_1_mar_input, load_from_ram_1_mar_output, load_from_ram_1_mbr_input,
       load_from_ram_1_mbr_ouput, load_from_ram_1_mbr_r_c, load_from_ram_1_out_8, load_from_ram_1_out_9,
       load_from_ram_1_out_10, load_from_ram_1_out_11, load_from_ram_1_out_12, load_from_ram_1_out_13,
       load_from_ram_1_out_15, load_from_ram_1_output_ram, load_from_ram_1_r1_output,
       load_from_ram_1_r2_ouput, load_from_ram_1_ram_r, mar_1_out_14, mar_1_out_15, mar_1_out_16,
       mar_1_out_17, mbr_1_out_22, mbr_1_out_23, mbr_1_out_24, mbr_1_out_25, mbr_1_out_26, mbr_1_out_27,
       mbr_1_out_28, mbr_1_out_29, mult_1_alu_output, mult_1_out_8, mult_1_out_9, mult_1_out_10,
       mult_1_out_11, mult_1_out_12, mult_1_out_13, mult_1_out_14, mult_1_out_15, mult_1_out_16,
       mult_1_out_17, mult_1_out_18, mult_1_out_19, mult_1_out_20, multiple_or_2_1_out_6, n3_or_1_out_4,
       n3_or_2_out_4, n3_or_3_out_4, n4_or_1_out_5, n4_or_2_out_5, not_1_out, not_2_out, not_3_out,
       number_to_digits_1_out_9, number_to_digits_1_out_10, number_to_digits_1_out_11,
       number_to_digits_1_out_12, number_to_digits_1_out_13, number_to_digits_1_out_14,
       number_to_digits_1_out_15, number_to_digits_1_out_16, number_to_digits_1_out_17,
       number_to_digits_1_out_18, number_to_digits_1_out_19, number_to_digits_1_out_20,
       number_to_display_1_out_5, number_to_display_1_out_6, number_to_display_1_out_7,
       number_to_display_1_out_8, number_to_display_1_out_9, number_to_display_1_out_10,
       number_to_display_1_out_11, number_to_display_1_out_12, number_to_display_2_out_5,
       number_to_display_2_out_6, number_to_display_2_out_7, number_to_display_2_out_8,
       number_to_display_2_out_9, number_to_display_2_out_10, number_to_display_2_out_11,
       number_to_display_2_out_12, number_to_display_3_out_5, number_to_display_3_out_6,
       number_to_display_3_out_7, number_to_display_3_out_8, number_to_display_3_out_9,
       number_to_display_3_out_10, number_to_display_3_out_11, number_to_display_3_out_12, out_reg_1_out_12,
       out_reg_1_out_13, out_reg_1_out_14, out_reg_1_out_15, out_reg_1_out_16, out_reg_1_out_17,
       out_reg_1_out_18, out_reg_1_out_19, output_alu_1_out_12, output_alu_1_out_13, output_alu_1_out_14,
       output_alu_1_out_15, output_alu_1_out_16, output_alu_1_out_17, output_alu_1_out_18,
       output_alu_1_out_19, output_merger_1_out_50, output_merger_1_out_51, output_merger_1_out_52,
       output_merger_1_out_53, output_merger_1_out_54, output_merger_1_out_55, output_merger_1_out_56,
       output_merger_1_out_57, output_merger_1_out_58, output_merger_1_out_59, output_merger_1_out_60,
       output_merger_1_out_61, output_merger_1_out_62, output_merger_1_out_63, output_merger_1_out_64,
       output_merger_1_out_65, pc_1_out_11, pc_1_out_12, pc_1_out_13, pc_1_out_14, program_rom_1_out_9,
       program_rom_1_out_10, program_rom_1_out_11, program_rom_1_out_12, program_rom_1_out_13,
       program_rom_1_out_14, program_rom_1_out_15, program_rom_1_out_16, program_rom_1_out_17,
       program_rom_1_out_18, program_rom_1_out_19, program_rom_1_out_20, program_rom_1_out_21,
       program_rom_1_out_22, program_rom_1_out_23, program_rom_1_out_24, program_rom_1_out_25,
       program_rom_1_out_26, program_rom_1_out_27, program_rom_1_out_28, program_rom_1_out_29,
       program_rom_1_out_30, program_rom_1_out_31, program_rom_1_out_32, program_rom_1_out_33,
       program_rom_1_out_34, program_rom_1_out_35, program_rom_1_out_36, program_rom_1_out_37,
       program_rom_1_out_38, program_rom_1_out_39, program_rom_1_out_40, program_rom_1_out_41,
       program_rom_1_out_42, program_rom_1_out_43, program_rom_1_out_44, program_rom_1_out_45,
       program_rom_1_out_46, program_rom_1_out_47, program_rom_1_out_48, program_rom_1_out_49,
       program_rom_1_out_50, program_rom_1_out_51, program_rom_1_out_52, program_rom_1_out_53,
       program_rom_1_out_54, program_rom_1_out_55, program_rom_1_out_56, program_rom_1_out_57,
       program_rom_1_out_58, program_rom_1_out_59, program_rom_1_out_60, program_rom_1_out_61,
       program_rom_1_out_62, program_rom_1_out_63, program_rom_1_out_64, program_rom_1_out_65,
       program_rom_1_out_66, program_rom_1_out_67, program_rom_1_out_68, program_rom_1_out_69,
       program_rom_1_out_70, program_rom_1_out_71, program_rom_1_out_72, program_rom_1_out_73,
       program_rom_1_out_74, program_rom_1_out_75, program_rom_1_out_76, program_rom_1_out_77,
       program_rom_1_out_78, program_rom_1_out_79, program_rom_1_out_80, program_rom_1_out_81,
       program_rom_1_out_82, program_rom_1_out_83, program_rom_1_out_84, program_rom_1_out_85,
       program_rom_1_out_86, program_rom_1_out_87, program_rom_1_out_88, program_rom_1_out_89,
       program_rom_1_out_90, program_rom_1_out_91, program_rom_1_out_92, program_rom_1_out_93,
       program_rom_1_out_94, program_rom_1_out_95, program_rom_1_out_96, program_rom_1_out_97,
       program_rom_1_out_98, program_rom_1_out_99, program_rom_1_out_100, program_rom_1_out_101,
       program_rom_1_out_102, program_rom_1_out_103, program_rom_1_out_104, program_rom_1_out_105,
       program_rom_1_out_106, program_rom_1_out_107, program_rom_1_out_108, program_rom_1_out_109,
       program_rom_1_out_110, program_rom_1_out_111, program_rom_1_out_112, program_rom_1_out_113,
       program_rom_1_out_114, program_rom_1_out_115, program_rom_1_out_116, program_rom_1_out_117,
       program_rom_1_out_118, program_rom_1_out_119, program_rom_1_out_120, program_rom_1_out_121,
       program_rom_1_out_122, program_rom_1_out_123, program_rom_1_out_124, program_rom_1_out_125,
       program_rom_1_out_126, program_rom_1_out_127, program_rom_1_out_128, program_rom_1_out_129,
       program_rom_1_out_130, program_rom_1_out_131, program_rom_1_out_132, program_rom_1_out_133,
       program_rom_1_out_134, program_rom_1_out_135, program_rom_1_out_136, R2_out_13, R2_out_14, R2_out_15,
       R2_out_16, R2_out_17, R2_out_18, R2_out_19, R2_out_20, R2_out_21, R2_out_22, R2_out_23, R2_out_24,
       R2_out_25, R2_out_26, R2_out_27, R2_out_28, R_out_13, R_out_14, R_out_15, R_out_16, R_out_17,
       R_out_18, R_out_19, R_out_20, ram_1_out_148, ram_1_out_149, ram_1_out_150, ram_1_out_151,
       ram_1_out_152, ram_1_out_153, ram_1_out_154, ram_1_out_155, ram_output_1_out_10, ram_output_1_out_11,
       ram_output_1_out_12, ram_output_1_out_13, ram_output_1_out_14, ram_output_1_out_15,
       ram_output_1_out_16, ram_output_1_out_17, small_and_1_out_3, small_and_2_out_3, small_or_1_out_3,
       small_or_2_out_3, small_or_3_out_3, small_or_4_out_3, small_or_5_out_3, small_or_6_out_3,
       small_or_7_out_3, small_or_8_out_3, small_or_9_out_3, small_or_10_out_3, small_or_11_out_3,
       small_or_12_out_3, small_or_13_out_3, small_or_14_out_3, small_or_15_out_3, small_or_16_out_3,
       small_or_17_out_3, small_or_18_out_3, small_or_19_out_3, small_or_20_out_3, small_or_21_out_3,
       small_or_22_out_3, small_or_23_out_3, small_or_24_out_3, small_or_25_out_3, small_or_26_out_3,
       small_or_27_out_3, switch_1_out_4, switch_choose_1_out_8, system_bus_chooser_1_out_21,
       system_bus_chooser_1_out_22, system_bus_chooser_1_out_23, system_bus_chooser_1_out_24,
       system_bus_chooser_1_out_25, system_bus_chooser_1_out_26, system_bus_chooser_1_out_27,
       system_bus_chooser_1_out_28;

  number_to_display number_to_display_1 (
    .out_5(number_to_display_1_out_5), .out_6(number_to_display_1_out_6), .out_7(number_to_display_1_out_7),
    .out_8(number_to_display_1_out_8), .out_9(number_to_display_1_out_9),
    .out_10(number_to_display_1_out_10), .out_11(number_to_display_1_out_11),
    .out_12(number_to_display_1_out_12), .in_1(number_to_digits_1_out_9), .in_2(number_to_digits_1_out_10),
    .in_3(number_to_digits_1_out_11), .in_4(number_to_digits_1_out_12));
  _7_Segment_Display u_7_segment_display_1 (
    .g(number_to_display_1_out_5), .f(number_to_display_1_out_6), .a(number_to_display_1_out_7),
    .b(number_to_display_1_out_8), .e(number_to_display_1_out_9), .d(number_to_display_1_out_10),
    .c(number_to_display_1_out_11), .dp(number_to_display_1_out_12));
  number_to_display number_to_display_2 (
    .out_5(number_to_display_2_out_5), .out_6(number_to_display_2_out_6), .out_7(number_to_display_2_out_7),
    .out_8(number_to_display_2_out_8), .out_9(number_to_display_2_out_9),
    .out_10(number_to_display_2_out_10), .out_11(number_to_display_2_out_11),
    .out_12(number_to_display_2_out_12), .in_1(number_to_digits_1_out_13), .in_2(number_to_digits_1_out_14),
    .in_3(number_to_digits_1_out_15), .in_4(number_to_digits_1_out_16));
  number_to_digits number_to_digits_1 (
    .out_9(number_to_digits_1_out_9), .out_10(number_to_digits_1_out_10), .out_11(number_to_digits_1_out_11),
    .out_12(number_to_digits_1_out_12), .out_13(number_to_digits_1_out_13),
    .out_14(number_to_digits_1_out_14), .out_15(number_to_digits_1_out_15),
    .out_16(number_to_digits_1_out_16), .out_17(number_to_digits_1_out_17),
    .out_18(number_to_digits_1_out_18), .out_19(number_to_digits_1_out_19),
    .out_20(number_to_digits_1_out_20), .in_1(out_reg_1_out_12), .in_2(out_reg_1_out_13),
    .in_3(out_reg_1_out_14), .in_4(out_reg_1_out_15), .in_5(out_reg_1_out_16), .in_6(out_reg_1_out_17),
    .in_7(out_reg_1_out_18), .in_8(out_reg_1_out_19));
  out_reg out_reg_1 (
    .in_3(output_merger_1_out_58), .in_4(output_merger_1_out_59), .in_5(output_merger_1_out_60),
    .in_6(output_merger_1_out_61), .in_7(output_merger_1_out_62), .in_8(output_merger_1_out_63),
    .in_9(output_merger_1_out_64), .in_10(output_merger_1_out_65), .in_1(display_1_out_11),
    .in_2(clock_1_out), .in_11(in_1), .out_12(out_reg_1_out_12), .out_13(out_reg_1_out_13),
    .out_14(out_reg_1_out_14), .out_15(out_reg_1_out_15), .out_16(out_reg_1_out_16),
    .out_17(out_reg_1_out_17), .out_18(out_reg_1_out_18), .out_19(out_reg_1_out_19));
  RAM ram_1 (
    .out_148(ram_1_out_148), .out_149(ram_1_out_149), .out_150(ram_1_out_150), .out_151(ram_1_out_151),
    .out_152(ram_1_out_152), .out_153(ram_1_out_153), .out_154(ram_1_out_154), .out_155(ram_1_out_155),
    .in_2(output_merger_1_out_58), .in_3(output_merger_1_out_59), .in_4(output_merger_1_out_60),
    .in_5(output_merger_1_out_61), .in_6(output_merger_1_out_62), .in_13(output_merger_1_out_62),
    .in_7(output_merger_1_out_63), .in_14(output_merger_1_out_63), .in_8(output_merger_1_out_64),
    .in_15(output_merger_1_out_64), .in_9(output_merger_1_out_65), .in_16(output_merger_1_out_65),
    .in_23(load_from_ram_1_ram_r), .CLK(clock_1_out), .A_DATA(load_from_ram_1_dr_input),
    .in_18(small_or_21_out_3), .in_28(in_1), .accept(in_12), .download(in_13), .in_50(program_rom_1_out_58),
    .in_51(program_rom_1_out_60), .in_52(program_rom_1_out_62), .in_53(program_rom_1_out_64),
    .in_54(program_rom_1_out_66), .in_55(program_rom_1_out_68), .in_56(program_rom_1_out_70),
    .in_57(program_rom_1_out_72), .in_66(program_rom_1_out_26), .in_67(program_rom_1_out_28),
    .in_68(program_rom_1_out_30), .in_69(program_rom_1_out_32), .in_70(program_rom_1_out_34),
    .in_71(program_rom_1_out_36), .in_72(program_rom_1_out_38), .in_73(program_rom_1_out_40),
    .in_82(program_rom_1_out_121), .in_83(program_rom_1_out_123), .in_84(program_rom_1_out_125),
    .in_85(program_rom_1_out_127), .in_86(program_rom_1_out_129), .in_87(program_rom_1_out_131),
    .in_88(program_rom_1_out_133), .in_89(program_rom_1_out_135), .in_98(program_rom_1_out_89),
    .in_99(program_rom_1_out_91), .in_100(program_rom_1_out_93), .in_101(program_rom_1_out_95),
    .in_102(program_rom_1_out_97), .in_103(program_rom_1_out_99), .in_104(program_rom_1_out_101),
    .in_105(program_rom_1_out_103), .in_114(program_rom_1_out_57), .in_115(program_rom_1_out_59),
    .in_116(program_rom_1_out_61), .in_117(program_rom_1_out_63), .in_118(program_rom_1_out_65),
    .in_119(program_rom_1_out_67), .in_120(program_rom_1_out_69), .in_121(program_rom_1_out_71),
    .in_130(program_rom_1_out_25), .in_131(program_rom_1_out_27), .in_132(program_rom_1_out_29),
    .in_133(program_rom_1_out_31), .in_134(program_rom_1_out_33), .in_135(program_rom_1_out_35),
    .in_136(program_rom_1_out_37), .in_137(program_rom_1_out_39), .in_58(program_rom_1_out_42),
    .in_59(program_rom_1_out_44), .in_60(program_rom_1_out_46), .in_61(program_rom_1_out_48),
    .in_62(program_rom_1_out_50), .in_63(program_rom_1_out_52), .in_64(program_rom_1_out_54),
    .in_65(program_rom_1_out_56), .in_74(program_rom_1_out_10), .in_75(program_rom_1_out_12),
    .in_76(program_rom_1_out_14), .in_77(program_rom_1_out_16), .in_78(program_rom_1_out_18),
    .in_79(program_rom_1_out_20), .in_80(program_rom_1_out_22), .in_81(program_rom_1_out_24),
    .in_90(program_rom_1_out_105), .in_91(program_rom_1_out_107), .in_92(program_rom_1_out_109),
    .in_93(program_rom_1_out_111), .in_94(program_rom_1_out_113), .in_95(program_rom_1_out_115),
    .in_96(program_rom_1_out_117), .in_97(program_rom_1_out_119), .in_106(program_rom_1_out_73),
    .in_107(program_rom_1_out_75), .in_108(program_rom_1_out_77), .in_109(program_rom_1_out_79),
    .in_110(program_rom_1_out_81), .in_111(program_rom_1_out_83), .in_112(program_rom_1_out_85),
    .in_113(program_rom_1_out_87), .in_122(program_rom_1_out_41), .in_123(program_rom_1_out_43),
    .in_124(program_rom_1_out_45), .in_125(program_rom_1_out_47), .in_126(program_rom_1_out_49),
    .in_127(program_rom_1_out_51), .in_128(program_rom_1_out_53), .in_129(program_rom_1_out_55),
    .in_138(program_rom_1_out_9), .in_139(program_rom_1_out_11), .in_140(program_rom_1_out_13),
    .in_141(program_rom_1_out_15), .in_142(program_rom_1_out_17), .in_143(program_rom_1_out_19),
    .in_144(program_rom_1_out_21), .in_145(program_rom_1_out_23), .in_42(program_rom_1_out_74),
    .in_43(program_rom_1_out_76), .in_44(program_rom_1_out_78), .in_45(program_rom_1_out_80),
    .in_46(program_rom_1_out_82), .in_47(program_rom_1_out_84), .in_48(program_rom_1_out_86),
    .in_49(program_rom_1_out_88), .in_34(program_rom_1_out_90), .in_35(program_rom_1_out_92),
    .in_36(program_rom_1_out_94), .in_37(program_rom_1_out_96), .in_38(program_rom_1_out_98),
    .in_39(program_rom_1_out_100), .in_40(program_rom_1_out_102), .in_41(program_rom_1_out_104),
    .in_10(program_rom_1_out_122), .in_11(program_rom_1_out_124), .in_12(program_rom_1_out_126),
    .in_17(program_rom_1_out_128), .in_19(program_rom_1_out_130), .in_20(program_rom_1_out_132),
    .in_21(program_rom_1_out_134), .in_22(program_rom_1_out_136), .in_24(program_rom_1_out_106),
    .in_25(program_rom_1_out_108), .in_26(program_rom_1_out_110), .in_27(program_rom_1_out_112),
    .in_29(program_rom_1_out_114), .in_30(program_rom_1_out_116), .in_31(program_rom_1_out_118),
    .in_33(program_rom_1_out_120));
  _7_Segment_Display u_7_segment_display_2 (
    .g(number_to_display_2_out_5), .f(number_to_display_2_out_6), .a(number_to_display_2_out_7),
    .b(number_to_display_2_out_8), .e(number_to_display_2_out_9), .d(number_to_display_2_out_10),
    .c(number_to_display_2_out_11), .dp(number_to_display_2_out_12));
  number_to_display number_to_display_3 (
    .out_5(number_to_display_3_out_5), .out_6(number_to_display_3_out_6), .out_7(number_to_display_3_out_7),
    .out_8(number_to_display_3_out_8), .out_9(number_to_display_3_out_9),
    .out_10(number_to_display_3_out_10), .out_11(number_to_display_3_out_11),
    .out_12(number_to_display_3_out_12), .in_1(number_to_digits_1_out_17), .in_2(number_to_digits_1_out_18),
    .in_3(number_to_digits_1_out_19), .in_4(number_to_digits_1_out_20));
  _7_Segment_Display u_7_segment_display_3 (
    .g(number_to_display_3_out_5), .f(number_to_display_3_out_6), .a(number_to_display_3_out_7),
    .b(number_to_display_3_out_8), .e(number_to_display_3_out_9), .d(number_to_display_3_out_10),
    .c(number_to_display_3_out_11), .dp(number_to_display_3_out_12));
  input_pins input_pins_1 (
    .in_12(clock_1_out), .in_1(_7), .in_4(_4), .in_7(_1), .in_2(_8), .in_5(_5), .in_8(_2), .in_10(_0),
    .in_3(_9), .in_6(_6), .in_9(_3), .out_14(input_pins_1_out_14), .out_15(input_pins_1_out_15),
    .out_16(input_pins_1_out_16), .out_17(input_pins_1_out_17), .in_13(get_input_1_input_output), .in_11(in_1));
  ram_output ram_output_1 (
    .in_2(ram_1_out_155), .in_3(ram_1_out_154), .in_4(ram_1_out_153), .in_5(ram_1_out_152),
    .in_6(ram_1_out_151), .in_7(ram_1_out_150), .in_8(ram_1_out_149), .in_9(ram_1_out_148),
    .out_10(ram_output_1_out_10), .out_11(ram_output_1_out_11), .out_12(ram_output_1_out_12),
    .out_13(ram_output_1_out_13), .out_14(ram_output_1_out_14), .out_15(ram_output_1_out_15),
    .out_16(ram_output_1_out_16), .out_17(ram_output_1_out_17), .in_1(small_or_9_out_3));
  system_bus_chooser system_bus_chooser_1 (
    .in_5(input_pins_1_out_14), .in_7(input_pins_1_out_15), .in_9(input_pins_1_out_16),
    .in_11(input_pins_1_out_17), .out_21(system_bus_chooser_1_out_21), .out_22(system_bus_chooser_1_out_22),
    .out_23(system_bus_chooser_1_out_23), .out_24(system_bus_chooser_1_out_24),
    .out_25(system_bus_chooser_1_out_25), .out_26(system_bus_chooser_1_out_26),
    .out_27(system_bus_chooser_1_out_27), .out_28(system_bus_chooser_1_out_28), .in_13(ram_output_1_out_17),
    .in_14(ram_output_1_out_16), .in_15(ram_output_1_out_15), .in_16(ram_output_1_out_14),
    .in_17(ram_output_1_out_13), .in_18(ram_output_1_out_12), .in_19(ram_output_1_out_11),
    .in_20(ram_output_1_out_10), .in_1(output_merger_1_out_58), .in_2(output_merger_1_out_59),
    .in_3(output_merger_1_out_60), .in_4(output_merger_1_out_61), .in_6(output_merger_1_out_62),
    .in_8(output_merger_1_out_63), .in_10(output_merger_1_out_64), .in_12(output_merger_1_out_65));
  Clock clock_1 (.out(clock_1_out));
  output_merger output_merger_1 (
    .in_5(mbr_1_out_22), .in_6(mbr_1_out_23), .in_7(mbr_1_out_24), .in_8(mbr_1_out_25), .in_9(mbr_1_out_26),
    .in_10(mbr_1_out_27), .in_11(mbr_1_out_28), .in_12(mbr_1_out_29), .in_1(pc_1_out_14), .in_2(pc_1_out_13),
    .in_3(pc_1_out_12), .in_4(pc_1_out_11), .in_25(output_alu_1_out_19), .in_26(output_alu_1_out_18),
    .in_27(output_alu_1_out_17), .in_28(output_alu_1_out_16), .in_29(output_alu_1_out_15),
    .in_30(output_alu_1_out_14), .in_31(output_alu_1_out_13), .in_32(output_alu_1_out_12), .in_33(R2_out_20),
    .in_34(R2_out_19), .in_35(R2_out_18), .in_36(R2_out_17), .in_37(R2_out_16), .in_38(R2_out_15),
    .in_39(R2_out_14), .in_40(R2_out_13), .in_17(general_register_1_out_20),
    .in_18(general_register_1_out_19), .in_19(general_register_1_out_18), .in_20(general_register_1_out_17),
    .in_21(general_register_1_out_16), .in_22(general_register_1_out_15), .in_23(general_register_1_out_14),
    .in_24(general_register_1_out_13), .out_58(output_merger_1_out_58), .out_59(output_merger_1_out_59),
    .out_60(output_merger_1_out_60), .out_61(output_merger_1_out_61), .out_62(output_merger_1_out_62),
    .out_63(output_merger_1_out_63), .out_64(output_merger_1_out_64), .out_65(output_merger_1_out_65),
    .out_50(output_merger_1_out_50), .in_13(mar_1_out_14), .in_14(mar_1_out_15), .in_15(mar_1_out_16),
    .in_16(mar_1_out_17), .in_41(mult_1_out_11), .in_42(mult_1_out_12), .in_43(mult_1_out_13),
    .in_44(mult_1_out_14), .out_51(output_merger_1_out_51), .out_52(output_merger_1_out_52),
    .out_53(output_merger_1_out_53), .out_54(output_merger_1_out_54), .out_55(output_merger_1_out_55),
    .out_56(output_merger_1_out_56), .out_57(output_merger_1_out_57), .in_45(n3_or_1_out_4),
    .in_46(either_1_out_9), .in_47(either_1_out_10), .in_48(either_1_out_11), .in_49(either_1_out_12));
  PROGRAM_ROM program_rom_1 (
    .out_9(program_rom_1_out_9), .out_11(program_rom_1_out_11), .out_13(program_rom_1_out_13),
    .out_15(program_rom_1_out_15), .out_17(program_rom_1_out_17), .out_19(program_rom_1_out_19),
    .out_21(program_rom_1_out_21), .out_23(program_rom_1_out_23), .out_25(program_rom_1_out_25),
    .out_27(program_rom_1_out_27), .out_29(program_rom_1_out_29), .out_31(program_rom_1_out_31),
    .out_33(program_rom_1_out_33), .out_35(program_rom_1_out_35), .out_37(program_rom_1_out_37),
    .out_39(program_rom_1_out_39), .out_41(program_rom_1_out_41), .out_43(program_rom_1_out_43),
    .out_45(program_rom_1_out_45), .out_47(program_rom_1_out_47), .out_49(program_rom_1_out_49),
    .out_51(program_rom_1_out_51), .out_53(program_rom_1_out_53), .out_55(program_rom_1_out_55),
    .out_57(program_rom_1_out_57), .out_59(program_rom_1_out_59), .out_61(program_rom_1_out_61),
    .out_63(program_rom_1_out_63), .out_65(program_rom_1_out_65), .out_67(program_rom_1_out_67),
    .out_69(program_rom_1_out_69), .out_71(program_rom_1_out_71), .out_73(program_rom_1_out_73),
    .out_75(program_rom_1_out_75), .out_77(program_rom_1_out_77), .out_79(program_rom_1_out_79),
    .out_81(program_rom_1_out_81), .out_83(program_rom_1_out_83), .out_85(program_rom_1_out_85),
    .out_87(program_rom_1_out_87), .out_89(program_rom_1_out_89), .out_91(program_rom_1_out_91),
    .out_93(program_rom_1_out_93), .out_95(program_rom_1_out_95), .out_97(program_rom_1_out_97),
    .out_99(program_rom_1_out_99), .out_101(program_rom_1_out_101), .out_103(program_rom_1_out_103),
    .out_105(program_rom_1_out_105), .out_107(program_rom_1_out_107), .out_109(program_rom_1_out_109),
    .out_111(program_rom_1_out_111), .out_113(program_rom_1_out_113), .out_115(program_rom_1_out_115),
    .out_117(program_rom_1_out_117), .out_119(program_rom_1_out_119), .out_121(program_rom_1_out_121),
    .out_123(program_rom_1_out_123), .out_125(program_rom_1_out_125), .out_127(program_rom_1_out_127),
    .out_129(program_rom_1_out_129), .out_131(program_rom_1_out_131), .out_133(program_rom_1_out_133),
    .out_135(program_rom_1_out_135), .out_10(program_rom_1_out_10), .out_12(program_rom_1_out_12),
    .out_14(program_rom_1_out_14), .out_16(program_rom_1_out_16), .out_18(program_rom_1_out_18),
    .out_20(program_rom_1_out_20), .out_22(program_rom_1_out_22), .out_24(program_rom_1_out_24),
    .out_26(program_rom_1_out_26), .out_28(program_rom_1_out_28), .out_30(program_rom_1_out_30),
    .out_32(program_rom_1_out_32), .out_34(program_rom_1_out_34), .out_36(program_rom_1_out_36),
    .out_38(program_rom_1_out_38), .out_40(program_rom_1_out_40), .out_42(program_rom_1_out_42),
    .out_44(program_rom_1_out_44), .out_46(program_rom_1_out_46), .out_48(program_rom_1_out_48),
    .out_50(program_rom_1_out_50), .out_52(program_rom_1_out_52), .out_54(program_rom_1_out_54),
    .out_56(program_rom_1_out_56), .out_58(program_rom_1_out_58), .out_60(program_rom_1_out_60),
    .out_62(program_rom_1_out_62), .out_64(program_rom_1_out_64), .out_66(program_rom_1_out_66),
    .out_68(program_rom_1_out_68), .out_70(program_rom_1_out_70), .out_72(program_rom_1_out_72),
    .out_74(program_rom_1_out_74), .out_76(program_rom_1_out_76), .out_78(program_rom_1_out_78),
    .out_80(program_rom_1_out_80), .out_82(program_rom_1_out_82), .out_84(program_rom_1_out_84),
    .out_86(program_rom_1_out_86), .out_88(program_rom_1_out_88), .out_90(program_rom_1_out_90),
    .out_92(program_rom_1_out_92), .out_94(program_rom_1_out_94), .out_96(program_rom_1_out_96),
    .out_98(program_rom_1_out_98), .out_100(program_rom_1_out_100), .out_102(program_rom_1_out_102),
    .out_104(program_rom_1_out_104), .out_106(program_rom_1_out_106), .out_108(program_rom_1_out_108),
    .out_110(program_rom_1_out_110), .out_112(program_rom_1_out_112), .out_114(program_rom_1_out_114),
    .out_116(program_rom_1_out_116), .out_118(program_rom_1_out_118), .out_120(program_rom_1_out_120),
    .out_122(program_rom_1_out_122), .out_124(program_rom_1_out_124), .out_126(program_rom_1_out_126),
    .out_128(program_rom_1_out_128), .out_130(program_rom_1_out_130), .out_132(program_rom_1_out_132),
    .out_134(program_rom_1_out_134), .out_136(program_rom_1_out_136), .in_1(in_14), .in_2(Number_in_ROM),
    .in_3(in_16), .in_4(in_17), .in_5(in_18), .in_6(in_19), .in_7(in_20), .in_8(in_21));
  MAR mar_1 (
    .\output (small_or_17_out_3), .clock(clock_1_out), .load(small_or_14_out_3),
    .in_7(system_bus_chooser_1_out_25), .in_8(system_bus_chooser_1_out_26),
    .in_9(system_bus_chooser_1_out_27), .in_10(system_bus_chooser_1_out_28), .out_14(mar_1_out_14),
    .out_15(mar_1_out_15), .out_16(mar_1_out_16), .out_17(mar_1_out_17), .in_3(output_merger_1_out_54),
    .in_4(output_merger_1_out_55), .in_5(output_merger_1_out_56), .in_6(output_merger_1_out_57),
    .in_1(small_or_15_out_3), .in_11(in_1));
  MBR mbr_1 (
    .\output (n4_or_1_out_5), .clock(clock_1_out), .load(n4_or_2_out_5), .in_1(n3_or_3_out_4),
    .in_2(system_bus_chooser_1_out_21), .in_3(system_bus_chooser_1_out_22),
    .in_4(system_bus_chooser_1_out_23), .in_5(system_bus_chooser_1_out_24),
    .in_6(system_bus_chooser_1_out_25), .in_7(system_bus_chooser_1_out_26),
    .in_8(system_bus_chooser_1_out_27), .in_9(system_bus_chooser_1_out_28), .in_10(output_merger_1_out_50),
    .in_11(output_merger_1_out_51), .in_12(output_merger_1_out_52), .in_13(output_merger_1_out_53),
    .in_14(output_merger_1_out_54), .in_15(output_merger_1_out_55), .in_16(output_merger_1_out_56),
    .in_17(output_merger_1_out_57), .out_22(mbr_1_out_22), .out_23(mbr_1_out_23), .out_24(mbr_1_out_24),
    .out_25(mbr_1_out_25), .out_26(mbr_1_out_26), .out_27(mbr_1_out_27), .out_28(mbr_1_out_28),
    .out_29(mbr_1_out_29), .in_20(in_1));
  and and_1 (and_1_out, clock_1_out, not_1_out);
  small_and small_and_1 (.in_1(and_1_out), .in_2(small_or_6_out_3), .out_3(small_and_1_out_3));
  general_register general_register_1 (
    .\output (small_or_1_out_3), .clock(clock_1_out), .load(small_or_4_out_3),
    .out_21(general_register_1_out_21), .out_22(general_register_1_out_22),
    .out_23(general_register_1_out_23), .out_24(general_register_1_out_24),
    .out_25(general_register_1_out_25), .out_26(general_register_1_out_26),
    .out_27(general_register_1_out_27), .out_28(general_register_1_out_28), .in_2(output_merger_1_out_57),
    .in_3(output_merger_1_out_56), .in_4(output_merger_1_out_55), .in_5(output_merger_1_out_54),
    .in_6(output_merger_1_out_53), .in_7(output_merger_1_out_52), .in_8(output_merger_1_out_51),
    .in_9(output_merger_1_out_50), .out_13(general_register_1_out_13), .out_14(general_register_1_out_14),
    .out_15(general_register_1_out_15), .out_16(general_register_1_out_16),
    .out_17(general_register_1_out_17), .out_18(general_register_1_out_18),
    .out_19(general_register_1_out_19), .out_20(general_register_1_out_20), .in_12(in_1));
  general_register R2 (
    .\output (small_or_3_out_3), .clock(clock_1_out), .load(small_or_2_out_3), .out_21(R2_out_21),
    .out_22(R2_out_22), .out_23(R2_out_23), .out_24(R2_out_24), .out_25(R2_out_25), .out_26(R2_out_26),
    .out_27(R2_out_27), .out_28(R2_out_28), .in_2(output_merger_1_out_57), .in_3(output_merger_1_out_56),
    .in_4(output_merger_1_out_55), .in_5(output_merger_1_out_54), .in_6(output_merger_1_out_53),
    .in_7(output_merger_1_out_52), .in_8(output_merger_1_out_51), .in_9(output_merger_1_out_50),
    .out_13(R2_out_13), .out_14(R2_out_14), .out_15(R2_out_15), .out_16(R2_out_16), .out_17(R2_out_17),
    .out_18(R2_out_18), .out_19(R2_out_19), .out_20(R2_out_20), .in_12(in_1));
  small_or small_or_1 (.in_1(small_or_5_out_3), .in_2(display_1_out_6), .out_3(small_or_1_out_3));
  byte_register R (
    .\output (1'b1), .clock(clock_1_out), .load(small_or_13_out_3), .in_2(output_merger_1_out_50),
    .in_3(output_merger_1_out_51), .in_4(output_merger_1_out_52), .in_5(output_merger_1_out_53),
    .in_6(output_merger_1_out_54), .in_7(output_merger_1_out_55), .in_8(output_merger_1_out_56),
    .in_9(output_merger_1_out_57), .out_13(R_out_13), .out_14(R_out_14), .out_15(R_out_15),
    .out_16(R_out_16), .out_17(R_out_17), .out_18(R_out_18), .out_19(R_out_19), .out_20(R_out_20),
    .in_12(in_1));
  byte_register L (
    .\output (1'b1), .clock(clock_1_out), .load(small_or_12_out_3), .in_2(output_merger_1_out_50),
    .in_3(output_merger_1_out_51), .in_4(output_merger_1_out_52), .in_5(output_merger_1_out_53),
    .in_6(output_merger_1_out_54), .in_7(output_merger_1_out_55), .in_8(output_merger_1_out_56),
    .in_9(output_merger_1_out_57), .out_13(L_out_13), .out_14(L_out_14), .out_15(L_out_15),
    .out_16(L_out_16), .out_17(L_out_17), .out_18(L_out_18), .out_19(L_out_19), .out_20(L_out_20),
    .in_12(in_1));
  not not_1 (not_1_out, finished);
  not not_2 (not_2_out, small_or_6_out_3);
  beq_bnq beq_bnq_1 (
    .R1(general_register_1_out_21), .in_4(general_register_1_out_22), .in_5(general_register_1_out_23),
    .in_6(general_register_1_out_24), .in_7(general_register_1_out_25), .in_8(general_register_1_out_26),
    .in_9(general_register_1_out_27), .in_10(general_register_1_out_28), .R2(R2_out_21), .in_12(R2_out_22),
    .in_13(R2_out_23), .in_14(R2_out_24), .in_15(R2_out_25), .in_16(R2_out_26), .in_17(R2_out_27),
    .in_18(R2_out_28), .in_19(instruction_chooser_1_out_17), .in_20(instruction_chooser_1_out_18),
    .in_1(instruction_chooser_1_out_11), .in_2(instruction_chooser_1_out_12),
    .in_21(instruction_chooser_1_out_13), .in_22(instruction_chooser_1_out_14),
    .in_23(instruction_chooser_1_out_15), .in_24(instruction_chooser_1_out_16), .out_27(beq_bnq_1_out_27),
    .out_28(beq_bnq_1_out_28), .out_29(beq_bnq_1_out_29), .out_30(beq_bnq_1_out_30),
    .out_26(beq_bnq_1_out_26), .clock(small_and_1_out_3), .out_31(beq_bnq_1_out_31), .out_32(beq_bnq_1_out_32));
  small_or small_or_2 (.in_1(small_or_7_out_3), .in_2(mult_1_out_18), .out_3(small_or_2_out_3));
  small_or small_or_3 (.in_1(add_sub_1_r2_output), .in_2(n3_or_2_out_4), .out_3(small_or_3_out_3));
  small_or small_or_4 (.in_1(small_or_8_out_3), .in_2(mult_1_out_17), .out_3(small_or_4_out_3));
  small_or small_or_5 (.in_1(add_sub_1_r1_output), .in_2(small_or_11_out_3), .out_3(small_or_5_out_3));
  output_alu output_alu_1 (
    .out_12(output_alu_1_out_12), .out_13(output_alu_1_out_13), .out_14(output_alu_1_out_14),
    .out_15(output_alu_1_out_15), .out_16(output_alu_1_out_16), .out_17(output_alu_1_out_17),
    .out_18(output_alu_1_out_18), .out_19(output_alu_1_out_19), .in_3(alu_1_a___0), .in_4(alu_1_a___1),
    .in_5(alu_1_a___2), .in_6(alu_1_a___3), .in_7(alu_1_a___4), .in_8(alu_1_a___5), .in_9(alu_1_a___6),
    .in_10(alu_1_a___7), .in_2(small_or_10_out_3), .in_1(small_or_26_out_3), .in_11(in_1));
  small_or small_or_6 (.in_1(get_next_instruction_1_out_3), .in_2(choose_inst_1_out_4), .out_3(small_or_6_out_3));
  small_or small_or_7 (.in_1(small_or_22_out_3), .in_2(actual_load_from_ram_1_r2_input), .out_3(small_or_7_out_3));
  small_or small_or_8 (.in_1(small_or_23_out_3), .in_2(actual_load_from_ram_1_r1_input), .out_3(small_or_8_out_3));
  small_or small_or_9 (
    .in_1(actual_load_from_ram_1_output_from_ram), .in_2(get_next_instruction_1_output_from_ram),
    .out_3(small_or_9_out_3));
  choose_inst choose_inst_1 (
    .out_4(choose_inst_1_out_4), .in_1(multiple_or_2_1_out_6), .in_2(add_sub_1_out_8), .in_3(beq_bnq_1_out_31));
  ALU alu_1 (
    .MULTIPLY(instruction_chooser_1_out_21), .R___0(R_out_20), .R___1(R_out_19), .R___2(R_out_18),
    .R___3(R_out_17), .R___4(R_out_16), .R___5(R_out_15), .R___6(R_out_14), .R___7(R_out_13),
    .SUBTRACT(instruction_chooser_1_out_23), .L___0(L_out_20), .L___1(L_out_19), .L___2(L_out_18),
    .L___3(L_out_17), .L___4(L_out_16), .L___5(L_out_15), .L___6(L_out_14), .L___7(L_out_13),
    .A___0(alu_1_a___0), .A___1(alu_1_a___1), .A___2(alu_1_a___2), .A___3(alu_1_a___3), .A___4(alu_1_a___4),
    .A___5(alu_1_a___5), .A___6(alu_1_a___6), .A___7(alu_1_a___7), .Zero(alu_1_zero),
    .Overflow(alu_1_overflow), .Negative(alu_1_negative));
  _3_or u_3_or_1 (
    .out_4(n3_or_1_out_4), .in_1(small_or_19_out_3), .in_2(get_next_instruction_1_ram_output),
    .in_3(display_1_out_12));
  switch switch_1 (
    .in_1(and_1_out), .in_2(get_next_instruction_1_out_3), .in_3(switch_choose_1_out_8),
    .out_4(switch_1_out_4));
  _3_or u_3_or_2 (.out_4(n3_or_2_out_4), .in_1(display_1_out_7), .in_2(mult_1_out_20), .in_3(load_from_ram_1_r2_ouput));
  small_or small_or_10 (.in_1(add_sub_1_alu_output), .in_2(mult_1_alu_output), .out_3(small_or_10_out_3));
  small_or small_or_11 (.in_1(mult_1_out_19), .in_2(load_from_ram_1_r1_output), .out_3(small_or_11_out_3));
  Status_Register status_register_1 (
    .in_2(alu_1_zero), .in_3(alu_1_overflow), .in_4(alu_1_negative), .out_6(zero), .out_7(overflow),
    .out_8(negative), .in_1(small_or_26_out_3), .in_5(in_1));
  small_or small_or_12 (.in_1(add_sub_1_l_input), .in_2(mult_1_out_16), .out_3(small_or_12_out_3));
  small_or small_or_13 (.in_1(add_sub_1_r_input), .in_2(mult_1_out_15), .out_3(small_or_13_out_3));
  IR ir_1 (
    .load(get_next_instruction_1_ir_input), .in_1(output_merger_1_out_50), .in_2(output_merger_1_out_51),
    .in_3(output_merger_1_out_52), .in_4(output_merger_1_out_53), .in_5(output_merger_1_out_54),
    .in_6(output_merger_1_out_55), .in_7(output_merger_1_out_56), .in_8(output_merger_1_out_57),
    .out_12(ir_1_out_12), .out_13(ir_1_out_13), .out_14(ir_1_out_14), .out_15(ir_1_out_15),
    .out_16(ir_1_out_16), .out_17(ir_1_out_17), .out_18(ir_1_out_18), .out_19(ir_1_out_19),
    .in_9(clock_1_out), .in_11(in_1));
  small_or small_or_14 (.in_1(small_or_18_out_3), .in_2(load_from_ram_1_mar_input), .out_3(small_or_14_out_3));
  small_or small_or_15 (.in_1(small_or_25_out_3), .in_2(actual_load_from_ram_1_out_15), .out_3(small_or_15_out_3));
  small_or small_or_16 (
    .in_1(actual_load_from_ram_1_mar_output), .in_2(load_from_ram_1_mar_output), .out_3(small_or_16_out_3));
  small_or small_or_17 (.in_1(small_or_16_out_3), .in_2(get_next_instruction_1_mar_output), .out_3(small_or_17_out_3));
  Add_Sub add_sub_1 (
    .clock(small_and_1_out_3), .add(instruction_chooser_1_out_22), .sub(instruction_chooser_1_out_23),
    ._1(instruction_chooser_1_out_15), ._2(instruction_chooser_1_out_16), .R_input(add_sub_1_r_input),
    .L_input(add_sub_1_l_input), .R1_output(add_sub_1_r1_output), .R2_output(add_sub_1_r2_output),
    .out_12(add_sub_1_out_12), .R2_input(add_sub_1_r2_input), .ALU_output(add_sub_1_alu_output),
    .out_8(add_sub_1_out_8), .out_6(add_sub_1_out_6), .out_7(add_sub_1_out_7));
  MULT mult_1 (
    .in_7(small_and_1_out_3), .out_8(mult_1_out_8), .out_9(mult_1_out_9),
    .in_1(instruction_chooser_1_out_21), .in_2(instruction_chooser_1_out_12),
    .in_3(instruction_chooser_1_out_13), .in_4(instruction_chooser_1_out_14),
    .in_5(instruction_chooser_1_out_15), .in_6(instruction_chooser_1_out_16), .out_15(mult_1_out_15),
    .out_16(mult_1_out_16), .out_17(mult_1_out_17), .out_18(mult_1_out_18), .out_19(mult_1_out_19),
    .out_20(mult_1_out_20), .alu_output(mult_1_alu_output), .out_11(mult_1_out_11), .out_12(mult_1_out_12),
    .out_13(mult_1_out_13), .out_14(mult_1_out_14), .out_10(mult_1_out_10));
  _4_or u_4_or_1 (
    .out_5(n4_or_1_out_5), .in_1(small_or_24_out_3), .in_2(load_from_ram_1_mbr_ouput),
    .in_3(get_input_1_mbr_output), .in_4(display_1_mbr_output));
  small_or small_or_18 (
    .in_1(get_next_instruction_1_mar_input), .in_2(actual_load_from_ram_1_mar_input),
    .out_3(small_or_18_out_3));
  small_or small_or_19 (
    .in_1(actual_load_from_ram_1_output_ram), .in_2(load_from_ram_1_output_ram), .out_3(small_or_19_out_3));
  small_or small_or_20 (
    .in_1(actual_load_from_ram_1_ar_input), .in_2(load_from_ram_1_ar_input), .out_3(small_or_20_out_3));
  small_or small_or_21 (.in_1(small_or_20_out_3), .in_2(get_next_instruction_1_ar_input), .out_3(small_or_21_out_3));
  PC pc_1 (
    .out_11(pc_1_out_11), .out_12(pc_1_out_12), .out_13(pc_1_out_13), .out_14(pc_1_out_14),
    .zero(clock_1_out), .clock(clock_1_out), .inc(get_next_instruction_1_out_4), .in_1(beq_bnq_1_out_30),
    .in_7(beq_bnq_1_out_28), .in_8(beq_bnq_1_out_27), .in_4(beq_bnq_1_out_29), .load(beq_bnq_1_out_26),
    .in_9(get_next_instruction_1_pc_output), .in_10(in_1));
  small_and small_and_2 (.in_1(not_3_out), .in_2(not_2_out), .out_3(small_and_2_out_3));
  not not_3 (not_3_out, finished);
  small_or small_or_22 (.in_1(add_sub_1_r2_input), .in_2(get_input_1_r2_input), .out_3(small_or_22_out_3));
  small_or small_or_23 (.in_1(add_sub_1_out_12), .in_2(get_input_1_r1_input), .out_3(small_or_23_out_3));
  _3_or u_3_or_3 (
    .out_4(n3_or_3_out_4), .in_1(get_input_1_mbr_r_c), .in_2(display_1_out_9), .in_3(load_from_ram_1_mbr_r_c));
  _4_or u_4_or_2 (
    .out_5(n4_or_2_out_5), .in_1(small_or_27_out_3), .in_2(get_next_instruction_1_mbr_input),
    .in_3(get_input_1_mbr_input), .in_4(display_1_out_8));
  small_or small_or_24 (
    .in_1(actual_load_from_ram_1_mbr_output), .in_2(get_next_instruction_1_mbr_output),
    .out_3(small_or_24_out_3));
  small_or small_or_25 (
    .in_1(load_from_ram_1_out_15), .in_2(get_next_instruction_1_mar_r_c), .out_3(small_or_25_out_3));
  get_next_instruction get_next_instruction_1 (
    .in_2(clock_1_out), .in_1(small_and_2_out_3), .MAR_input(get_next_instruction_1_mar_input),
    .PC_output(get_next_instruction_1_pc_output), .MAR_r_c(get_next_instruction_1_mar_r_c),
    .AR_input(get_next_instruction_1_ar_input), .MAR_output(get_next_instruction_1_mar_output),
    .RAM_output(get_next_instruction_1_ram_output), .output_from_RAM(get_next_instruction_1_output_from_ram),
    .MBR_input(get_next_instruction_1_mbr_input), .MBR_output(get_next_instruction_1_mbr_output),
    .IR_input(get_next_instruction_1_ir_input), .out_3(get_next_instruction_1_out_3),
    .out_4(get_next_instruction_1_out_4));
  Instruction_chooser instruction_chooser_1 (
    .out_11(instruction_chooser_1_out_11), .out_12(instruction_chooser_1_out_12),
    .out_13(instruction_chooser_1_out_13), .out_14(instruction_chooser_1_out_14),
    .out_15(instruction_chooser_1_out_15), .out_16(instruction_chooser_1_out_16), .in_1(ir_1_out_12),
    .in_2(ir_1_out_13), .in_3(ir_1_out_14), .in_4(ir_1_out_15), .in_5(ir_1_out_16), .in_6(ir_1_out_17),
    .in_7(ir_1_out_18), .in_8(ir_1_out_19), .out_17(instruction_chooser_1_out_17),
    .out_18(instruction_chooser_1_out_18), .out_19(instruction_chooser_1_out_19),
    .out_20(instruction_chooser_1_out_20), .out_21(instruction_chooser_1_out_21),
    .out_22(instruction_chooser_1_out_22), .out_23(instruction_chooser_1_out_23),
    .out_24(instruction_chooser_1_out_24), .out_25(instruction_chooser_1_out_25),
    .out_26(instruction_chooser_1_out_26), .stop(in_1), .do_inst(switch_1_out_4));
  Stop stop_1 (.in_1(instruction_chooser_1_out_26), .out_2(finished));
  small_or small_or_26 (.in_1(mult_1_out_10), .in_2(add_sub_1_out_7), .out_3(small_or_26_out_3));
  small_or small_or_27 (
    .in_1(load_from_ram_1_mbr_input), .in_2(actual_load_from_ram_1_mbr_input), .out_3(small_or_27_out_3));
  actual__load_from_ram actual_load_from_ram_1 (
    .in_7(small_and_1_out_3), .out_8(actual_load_from_ram_1_out_8), .out_9(actual_load_from_ram_1_out_9),
    .in_6(instruction_chooser_1_out_19), .in_1(instruction_chooser_1_out_12),
    .in_2(instruction_chooser_1_out_13), .in_3(instruction_chooser_1_out_14),
    .in_4(instruction_chooser_1_out_15), .in_5(instruction_chooser_1_out_16),
    .MAR_input(actual_load_from_ram_1_mar_input), .out_15(actual_load_from_ram_1_out_15),
    .output_ram(actual_load_from_ram_1_output_ram), .MAR_output(actual_load_from_ram_1_mar_output),
    .AR_input(actual_load_from_ram_1_ar_input), .MBR_input(actual_load_from_ram_1_mbr_input),
    .output_from_RAM(actual_load_from_ram_1_output_from_ram), .R1_input(actual_load_from_ram_1_r1_input),
    .R2_input(actual_load_from_ram_1_r2_input), .MBR_output(actual_load_from_ram_1_mbr_output),
    .out_10(actual_load_from_ram_1_out_10), .out_11(actual_load_from_ram_1_out_11),
    .out_12(actual_load_from_ram_1_out_12), .out_13(actual_load_from_ram_1_out_13));
  either either_1 (
    .out_9(either_1_out_9), .out_10(either_1_out_10), .out_11(either_1_out_11), .out_12(either_1_out_12),
    .in_1(actual_load_from_ram_1_out_10), .in_2(actual_load_from_ram_1_out_11),
    .in_3(actual_load_from_ram_1_out_12), .in_4(actual_load_from_ram_1_out_13),
    .in_5(load_from_ram_1_out_10), .in_6(load_from_ram_1_out_11), .in_7(load_from_ram_1_out_12),
    .in_8(load_from_ram_1_out_13));
  switch_choose switch_choose_1 (
    .out_8(switch_choose_1_out_8), .in_2(get_input_1_out_4), .in_3(add_sub_1_out_6), .in_4(mult_1_out_8),
    .in_5(beq_bnq_1_out_32), .in_6(load_from_ram_1_out_8), .in_7(actual_load_from_ram_1_out_8),
    .in_1(display_1_out_4));
  multiple_or_2 multiple_or_2_1 (
    .in_1(display_1_out_5), .out_6(multiple_or_2_1_out_6), .in_2(actual_load_from_ram_1_out_9),
    .in_3(load_from_ram_1_out_9), .in_4(get_input_1_out_5), .in_5(mult_1_out_9));
  get_input get_input_1 (
    .in_3(small_and_1_out_3), .out_4(get_input_1_out_4), .out_5(get_input_1_out_5),
    .in_1(instruction_chooser_1_out_25), .in_2(instruction_chooser_1_out_16),
    .MBR_input(get_input_1_mbr_input), .input_output(get_input_1_input_output),
    .MBR_output(get_input_1_mbr_output), .R1_input(get_input_1_r1_input), .R2_input(get_input_1_r2_input),
    .MBR_r_c(get_input_1_mbr_r_c));
  display display_1 (
    .in_3(small_and_1_out_3), .out_4(display_1_out_4), .out_5(display_1_out_5),
    .in_2(instruction_chooser_1_out_24), .in_1(instruction_chooser_1_out_16), .out_6(display_1_out_6),
    .out_7(display_1_out_7), .out_8(display_1_out_8), .out_9(display_1_out_9),
    .MBr_output(display_1_mbr_output), .out_11(display_1_out_11), .out_12(display_1_out_12));
  load_from_ram load_from_ram_1 (
    .in_7(small_and_1_out_3), .out_8(load_from_ram_1_out_8), .in_2(instruction_chooser_1_out_20),
    .in_1(instruction_chooser_1_out_12), .in_3(instruction_chooser_1_out_13),
    .in_4(instruction_chooser_1_out_14), .in_5(instruction_chooser_1_out_15),
    .in_6(instruction_chooser_1_out_16), .MAR_input(load_from_ram_1_mar_input),
    .out_15(load_from_ram_1_out_15), .MAR_output(load_from_ram_1_mar_output),
    .MBR_input(load_from_ram_1_mbr_input), .MBR_ouput(load_from_ram_1_mbr_ouput),
    .AR_input(load_from_ram_1_ar_input), .ram_r(load_from_ram_1_ram_r),
    .R1_output(load_from_ram_1_r1_output), .output_ram(load_from_ram_1_output_ram),
    .R2_ouput(load_from_ram_1_r2_ouput), .out_10(load_from_ram_1_out_10), .out_11(load_from_ram_1_out_11),
    .out_12(load_from_ram_1_out_12), .out_13(load_from_ram_1_out_13), .out_9(load_from_ram_1_out_9),
    .MBR_r_c(load_from_ram_1_mbr_r_c), .DR_input(load_from_ram_1_dr_input));

  // Notes on the sheet:
  //   CPU name: HAL
  //   Team: Josh Liu, Daniel Lutes, Holden Koivu
  //   Display
  //   binary to decimal
  //   register
  //   load
  //   from ROM
  //   To run, download program from
  //   ROM into RAM and then start
  //   clicking the clock (or set ticks
  //   enabled)
  //   To download ROM into RAM, set accept to 1
  //   flick download on and off (1 then 0)  then set
  //   accept to 0
  //   ALU flags
  //   Sometimes when you open the project, Logisim will have an error where 
  //   some wires are blue for no reason. If this happens just exit and reopen the 
  //   file until it works.
  //   and gate for RAM output
  //   keypad
  //   CU control wires
  //   Only one number 
  //   (decimal) should be 
  //   selected for the 
  //   input to make sense
  //   stop/reset (on/off)
  //   output merger 
  //   for system
  //   bus
  //   If you want to write your own program, go into the last black box "PROG
  //   RAM ROM" and modify the bit patterns to the desired instructions given
  //   in the text file
  //   System bus
  //   Takes number input with rom and multiplies it
  //   with the number in the keypad buffer
  //   wait for program to finish (finished flag is 1) to see
  //   the correct answer on the display
  //   clock
  //   Binary
  //   output
  //   merger
  //   CPU bus is hard to
  //   see but it is those
  //   vertical wires running
  //   below this
  //   R1
  //   R2
  //   and for stop inst
  //   R
  //   L
  //   circuit that switches from
  //   load inst and current inst
  //   after each is
  //   finished
  //   swi
  //   tch
  //   or
  //   or
  //   or
  //   CU
  //   or
  //   or
  //   or
endmodule

module PC (
  input  in_1,
  input  load,
  input  inc,
  input  in_4,
  input  zero,
  input  clock,
  input  in_7,
  input  in_8,
  input  in_9,
  input  in_10,
  output out_11,
  output out_12,
  output out_13,
  output out_14
);

  wire and_1_out, and_2_out, and_3_out, and_4_out, and_5_out, and_6_out, and_7_out, and_8_out, and_9_out,
       and_10_out, and_11_out, and_12_out, and_13_out, and_14_out, d_ff_1_q, d_ff_2_q, d_ff_3_q, d_ff_4_q,
       half_adder_1_out_3, half_adder_1_out_4, half_adder_2_out_3, half_adder_2_out_4, half_adder_3_out_3,
       half_adder_3_out_4, half_adder_4_out_3, not_1_out, not_2_out, not_3_out, or_1_out, or_2_out, or_3_out,
       or_4_out, or_5_out;

  not not_1 (not_1_out, 1'b0);
  and and_1 (and_1_out, not_1_out, inc);
  half_adder half_adder_1 (.in_1(and_1_out), .in_2(d_ff_1_q), .out_3(half_adder_1_out_3), .out_4(half_adder_1_out_4));
  half_adder half_adder_2 (
    .in_1(half_adder_1_out_4), .in_2(d_ff_2_q), .out_3(half_adder_2_out_3), .out_4(half_adder_2_out_4));
  half_adder half_adder_3 (
    .in_1(half_adder_2_out_4), .in_2(d_ff_3_q), .out_3(half_adder_3_out_3), .out_4(half_adder_3_out_4));
  half_adder half_adder_4 (.in_1(half_adder_3_out_4), .in_2(d_ff_4_q), .out_3(half_adder_4_out_3));  // open: out_4
  not not_2 (not_2_out, load);
  not not_3 (not_3_out, zero);
  and and_2 (and_2_out, clock, or_1_out);
  and and_3 (and_3_out, not_2_out, half_adder_1_out_3);
  and and_4 (and_4_out, not_2_out, half_adder_2_out_3);
  and and_5 (and_5_out, not_2_out, half_adder_3_out_3);
  and and_6 (and_6_out, not_2_out, half_adder_4_out_3);
  or or_1 (or_1_out, load, inc);
  and and_7 (and_7_out, in_1, load);
  and and_8 (and_8_out, in_4, load);
  and and_9 (and_9_out, in_7, load);
  and and_10 (and_10_out, in_8, load);
  and and_11 (and_11_out, not_3_out, and_7_out);
  and and_12 (and_12_out, not_3_out, and_8_out);
  and and_13 (and_13_out, not_3_out, and_9_out);
  and and_14 (and_14_out, not_3_out, and_10_out);
  or or_2 (or_2_out, and_3_out, and_11_out);
  or or_3 (or_3_out, and_4_out, and_12_out);
  or or_4 (or_4_out, and_5_out, and_13_out);
  or or_5 (or_5_out, and_6_out, and_14_out);
  D_Flip_Flop d_ff_1 (.clk(and_2_out), .D(or_2_out), .Q(d_ff_1_q), .reset(in_10));  // open: Qn, preset, en
  D_Flip_Flop d_ff_2 (.clk(and_2_out), .D(or_3_out), .Q(d_ff_2_q), .reset(in_10));  // open: Qn, preset, en
  D_Flip_Flop d_ff_3 (.clk(and_2_out), .D(or_4_out), .Q(d_ff_3_q), .reset(in_10));  // open: Qn, preset, en
  D_Flip_Flop d_ff_4 (.clk(and_2_out), .D(or_5_out), .Q(d_ff_4_q), .reset(in_10));  // open: Qn, preset, en
  and and_15 (out_11, in_9, d_ff_1_q);
  and and_16 (out_12, d_ff_2_q, in_9);
  and and_17 (out_13, d_ff_3_q, in_9);
  and and_18 (out_14, d_ff_4_q, in_9);

  // Notes on the sheet:
  //   Program counter
endmodule

module half_adder (
  input  in_1,
  input  in_2,
  output out_3,
  output out_4
);

  wire and_1_out, not_1_out, or_1_out;

  and and_1 (and_1_out, in_1, in_2);
  or or_1 (or_1_out, in_2, in_1);
  and and_2 (out_4, in_1, in_2);
  not not_1 (not_1_out, and_1_out);
  and and_3 (out_3, not_1_out, or_1_out);
endmodule

module IR (
  input  in_1,
  input  in_2,
  input  in_3,
  input  in_4,
  input  in_5,
  input  in_6,
  input  in_7,
  input  in_8,
  input  in_9,
  input  load,
  input  in_11,
  output out_12,
  output out_13,
  output out_14,
  output out_15,
  output out_16,
  output out_17,
  output out_18,
  output out_19
);

  wire and_1_out;

  and and_1 (and_1_out, in_9, load);
  D_Flip_Flop d_ff_1 (.clk(and_1_out), .D(in_8), .Q(out_19), .reset(in_11));  // open: Qn, preset, en
  D_Flip_Flop d_ff_2 (.clk(and_1_out), .D(in_7), .Q(out_18), .reset(in_11));  // open: Qn, preset, en
  D_Flip_Flop d_ff_3 (.clk(and_1_out), .D(in_6), .Q(out_17), .reset(in_11));  // open: Qn, preset, en
  D_Flip_Flop d_ff_4 (.clk(and_1_out), .D(in_5), .Q(out_16), .reset(in_11));  // open: Qn, preset, en
  D_Flip_Flop d_ff_5 (.clk(and_1_out), .D(in_4), .Q(out_15), .reset(in_11));  // open: Qn, preset, en
  D_Flip_Flop d_ff_6 (.clk(and_1_out), .D(in_3), .Q(out_14), .reset(in_11));  // open: Qn, preset, en
  D_Flip_Flop d_ff_7 (.clk(and_1_out), .D(in_2), .Q(out_13), .reset(in_11));  // open: Qn, preset, en
  D_Flip_Flop d_ff_8 (.clk(and_1_out), .D(in_1), .Q(out_12), .reset(in_11));  // open: Qn, preset, en

  // Notes on the sheet:
  //   Holds current instruction
endmodule

module byte_register (
  input  \output ,
  input  in_2,
  input  in_3,
  input  in_4,
  input  in_5,
  input  in_6,
  input  in_7,
  input  in_8,
  input  in_9,
  input  clock,
  input  load,
  input  in_12,
  output out_13,
  output out_14,
  output out_15,
  output out_16,
  output out_17,
  output out_18,
  output out_19,
  output out_20
);

  wire and_1_out, d_ff_1_q, d_ff_2_q, d_ff_3_q, d_ff_4_q, d_ff_5_q, d_ff_6_q, d_ff_7_q, d_ff_8_q;

  and and_1 (and_1_out, clock, load);
  D_Flip_Flop d_ff_1 (.clk(and_1_out), .D(in_9), .Q(d_ff_1_q), .reset(in_12));  // open: Qn, preset, en
  D_Flip_Flop d_ff_2 (.clk(and_1_out), .D(in_8), .Q(d_ff_2_q), .reset(in_12));  // open: Qn, preset, en
  D_Flip_Flop d_ff_3 (.clk(and_1_out), .D(in_7), .Q(d_ff_3_q), .reset(in_12));  // open: Qn, preset, en
  D_Flip_Flop d_ff_4 (.clk(and_1_out), .D(in_6), .Q(d_ff_4_q), .reset(in_12));  // open: Qn, preset, en
  D_Flip_Flop d_ff_5 (.clk(and_1_out), .D(in_5), .Q(d_ff_5_q), .reset(in_12));  // open: Qn, preset, en
  D_Flip_Flop d_ff_6 (.clk(and_1_out), .D(in_4), .Q(d_ff_6_q), .reset(in_12));  // open: Qn, preset, en
  D_Flip_Flop d_ff_7 (.clk(and_1_out), .D(in_3), .Q(d_ff_7_q), .reset(in_12));  // open: Qn, preset, en
  D_Flip_Flop d_ff_8 (.clk(and_1_out), .D(in_2), .Q(d_ff_8_q), .reset(in_12));  // open: Qn, preset, en
  and and_2 (out_20, \output , d_ff_1_q);
  and and_3 (out_19, \output , d_ff_2_q);
  and and_4 (out_18, \output , d_ff_3_q);
  and and_5 (out_17, \output , d_ff_4_q);
  and and_6 (out_16, \output , d_ff_5_q);
  and and_7 (out_15, \output , d_ff_6_q);
  and and_8 (out_14, \output , d_ff_7_q);
  and and_9 (out_13, \output , d_ff_8_q);
endmodule

module Instruction_chooser (
  input  in_1,
  input  in_2,
  input  in_3,
  input  in_4,
  input  in_5,
  input  in_6,
  input  in_7,
  input  in_8,
  input  stop,
  input  do_inst,
  output out_11,
  output out_12,
  output out_13,
  output out_14,
  output out_15,
  output out_16,
  output out_17,
  output out_18,
  output out_19,
  output out_20,
  output out_21,
  output out_22,
  output out_23,
  output out_24,
  output out_25,
  output out_26
);

  wire and_1_out, and_2_out, and_4_out, and_5_out, and_7_out, and_8_out, and_9_out, and_10_out, and_12_out,
       and_13_out, and_14_out, and_15_out, and_17_out, and_18_out, and_19_out, and_21_out, and_22_out,
       and_23_out, and_25_out, and_26_out, and_27_out, and_28_out, and_30_out, and_31_out, and_32_out,
       and_33_out, and_34_out, and_37_out, and_38_out, and_39_out, and_40_out, and_42_out, and_43_out,
       and_44_out, not_1_out, not_2_out, not_3_out, not_4_out, not_5_out, not_6_out, not_7_out, not_8_out,
       not_9_out, not_10_out, not_11_out, not_12_out, not_13_out, not_14_out, not_15_out, not_16_out,
       or_1_out;

  not not_1 (not_1_out, in_1);
  and and_1 (and_1_out, not_1_out, not_2_out);
  and and_2 (and_2_out, and_1_out, not_16_out);
  and and_3 (out_17, and_2_out, do_inst);
  not not_2 (not_2_out, in_2);
  not not_3 (not_3_out, in_1);
  and and_4 (and_4_out, not_3_out, in_2);
  and and_5 (and_5_out, and_4_out, not_16_out);
  and and_6 (out_18, and_5_out, do_inst);
  and and_7 (and_7_out, in_1, in_2);
  not not_4 (not_4_out, in_2);
  and and_8 (and_8_out, not_4_out, not_6_out);
  and and_9 (and_9_out, in_1, and_8_out);
  and and_10 (and_10_out, and_9_out, not_16_out);
  and and_11 (out_19, and_10_out, do_inst);
  and and_12 (and_12_out, and_7_out, in_3);
  not not_5 (not_5_out, in_2);
  not not_6 (not_6_out, in_3);
  and and_13 (and_13_out, not_5_out, in_3);
  and and_14 (and_14_out, in_1, and_13_out);
  and and_15 (and_15_out, and_14_out, not_16_out);
  and and_16 (out_20, and_15_out, do_inst);
  and and_17 (and_17_out, in_2, not_8_out);
  and and_18 (and_18_out, in_1, and_17_out);
  and and_19 (and_19_out, and_18_out, not_16_out);
  and and_20 (out_21, and_19_out, do_inst);
  not not_7 (not_7_out, in_4);
  and and_21 (and_21_out, not_7_out, not_10_out);
  not not_8 (not_8_out, in_3);
  and and_22 (and_22_out, and_12_out, and_26_out);
  and and_23 (and_23_out, and_22_out, not_16_out);
  and and_24 (out_22, and_23_out, do_inst);
  not not_9 (not_9_out, in_4);
  not not_10 (not_10_out, in_5);
  and and_25 (and_25_out, not_9_out, not_13_out);
  not not_11 (not_11_out, in_6);
  and and_26 (and_26_out, and_21_out, not_11_out);
  and and_27 (and_27_out, and_12_out, and_32_out);
  and and_28 (and_28_out, and_27_out, not_16_out);
  and and_29 (out_23, and_28_out, do_inst);
  not not_12 (not_12_out, in_4);
  not not_13 (not_13_out, in_5);
  and and_30 (and_30_out, not_12_out, in_5);
  and and_31 (and_31_out, and_30_out, in_6);
  and and_32 (and_32_out, and_25_out, in_6);
  and and_33 (and_33_out, and_12_out, and_31_out);
  and and_34 (and_34_out, and_33_out, not_16_out);
  and and_35 (out_24, and_34_out, do_inst);
  and and_36 (out_25, and_40_out, do_inst);
  not not_14 (not_14_out, in_4);
  and and_37 (and_37_out, not_14_out, in_5);
  and and_38 (and_38_out, and_37_out, not_15_out);
  and and_39 (and_39_out, and_12_out, and_38_out);
  and and_40 (and_40_out, and_39_out, not_16_out);
  and and_41 (out_26, or_1_out, do_inst);
  and and_42 (and_42_out, in_4, in_5);
  not not_15 (not_15_out, in_6);
  and and_43 (and_43_out, and_42_out, in_6);
  and and_44 (and_44_out, and_12_out, and_43_out);
  or or_1 (or_1_out, and_44_out, stop);
  not not_16 (not_16_out, stop);

  assign out_11 = in_3;
  assign out_12 = in_4;
  assign out_13 = in_5;
  assign out_14 = in_6;
  assign out_15 = in_7;
  assign out_16 = in_8;

  // Notes on the sheet:
  //   00 beq
  //   01 bnq
  //   100 load
  //   101 store
  //   110 mult
  //   111 000 add
  //   111 001 sub
  //   111 011 print
  //   111 010 input
  //   111 111 stop
  //   00
  //   01
  //   100
  //   101
  //   110
  //   111000
  //   111001
  //   111011
  //   111010
  //   111111
  //   decoder
endmodule

module beq_bnq (
  input  in_1,
  input  in_2,
  input  R1,
  input  in_4,
  input  in_5,
  input  in_6,
  input  in_7,
  input  in_8,
  input  in_9,
  input  in_10,
  input  R2,
  input  in_12,
  input  in_13,
  input  in_14,
  input  in_15,
  input  in_16,
  input  in_17,
  input  in_18,
  input  in_19,
  input  in_20,
  input  in_21,
  input  in_22,
  input  in_23,
  input  in_24,
  input  clock,
  output out_26,
  output out_27,
  output out_28,
  output out_29,
  output out_30,
  output out_31,
  output out_32
);

  wire and_2_out, and_3_out, and_4_out, and_5_out, and_6_out, and_7_out, and_8_out, and_9_out, and_10_out,
       and_11_out, and_12_out, count_from_0_1_out_4, count_from_0_1_out_5, count_from_0_1_out_6,
       input_picker_1_out_18, input_picker_1_out_19, input_picker_1_out_20, input_picker_1_out_21,
       input_picker_1_out_22, input_picker_1_out_23, input_picker_1_out_24, input_picker_1_out_25,
       input_picker_2_out_18, input_picker_2_out_19, input_picker_2_out_20, input_picker_2_out_21,
       input_picker_2_out_22, input_picker_2_out_23, input_picker_2_out_24, input_picker_2_out_25,
       n8_and_1_out_9, not_1_out, not_2_out, not_3_out, not_4_out, not_5_out, not_6_out, not_7_out,
       not_8_out, not_9_out, not_10_out, not_11_out, not_12_out, not_13_out, not_14_out, xor_1_out,
       xor_2_out, xor_3_out, xor_4_out, xor_5_out, xor_6_out, xor_7_out, xor_8_out, xor_9_out, xor_10_out,
       xor_11_out;

  count_from_0 count_from_0_1 (
    .out_4(count_from_0_1_out_4), .out_5(count_from_0_1_out_5), .out_6(count_from_0_1_out_6), .start(out_31),
    .clock(clock), .zer0(out_32));
  not not_1 (not_1_out, 1'b0);
  xor xor_1 (xor_1_out, count_from_0_1_out_5, not_1_out);
  xor xor_2 (xor_2_out, count_from_0_1_out_6, 1'b0);
  not not_2 (not_2_out, xor_1_out);
  not not_3 (not_3_out, xor_2_out);
  and and_1 (out_32, not_3_out, and_2_out);
  input_picker input_picker_1 (
    .in_2(R1), .in_3(in_4), .in_4(in_5), .in_5(in_6), .in_6(in_7), .in_7(in_8), .in_8(in_9), .in_9(in_10),
    .in_10(R2), .in_11(in_12), .in_12(in_13), .in_13(in_14), .in_14(in_15), .in_15(in_16), .in_16(in_17),
    .in_17(in_18), .out_18(input_picker_1_out_18), .out_19(input_picker_1_out_19),
    .out_20(input_picker_1_out_20), .out_21(input_picker_1_out_21), .out_22(input_picker_1_out_22),
    .out_23(input_picker_1_out_23), .out_24(input_picker_1_out_24), .out_25(input_picker_1_out_25),
    .in_1(in_1));
  or or_1 (out_31, in_19, in_20);
  not not_4 (not_4_out, 1'b0);
  xor xor_3 (xor_3_out, count_from_0_1_out_4, not_4_out);
  not not_5 (not_5_out, xor_3_out);
  and and_2 (and_2_out, not_2_out, not_5_out);
  and and_3 (and_3_out, in_20, not_6_out);
  input_picker input_picker_2 (
    .in_2(R1), .in_3(in_4), .in_4(in_5), .in_5(in_6), .in_6(in_7), .in_7(in_8), .in_8(in_9), .in_9(in_10),
    .in_10(R2), .in_11(in_12), .in_12(in_13), .in_13(in_14), .in_14(in_15), .in_15(in_16), .in_16(in_17),
    .in_17(in_18), .out_18(input_picker_2_out_18), .out_19(input_picker_2_out_19),
    .out_20(input_picker_2_out_20), .out_21(input_picker_2_out_21), .out_22(input_picker_2_out_22),
    .out_23(input_picker_2_out_23), .out_24(input_picker_2_out_24), .out_25(input_picker_2_out_25),
    .in_1(in_2));
  not not_6 (not_6_out, n8_and_1_out_9);
  and and_4 (and_4_out, in_19, n8_and_1_out_9);
  or or_2 (out_26, and_3_out, and_4_out);
  xor xor_4 (xor_4_out, input_picker_1_out_18, input_picker_2_out_18);
  not not_7 (not_7_out, xor_4_out);
  _8_and u_8_and_1 (
    .in_1(not_7_out), .in_2(not_8_out), .in_3(not_9_out), .in_4(not_10_out), .in_5(not_11_out),
    .in_6(not_12_out), .in_7(not_13_out), .in_8(not_14_out), .out_9(n8_and_1_out_9));
  and and_5 (and_5_out, and_4_out, in_21);
  xor xor_5 (xor_5_out, input_picker_1_out_19, input_picker_2_out_19);
  xor xor_6 (xor_6_out, input_picker_1_out_20, input_picker_2_out_20);
  not not_8 (not_8_out, xor_5_out);
  not not_9 (not_9_out, xor_6_out);
  and and_6 (and_6_out, and_4_out, in_22);
  or or_3 (out_27, and_5_out, and_9_out);
  xor xor_7 (xor_7_out, input_picker_1_out_21, input_picker_2_out_21);
  not not_10 (not_10_out, xor_7_out);
  and and_7 (and_7_out, and_4_out, in_24);
  and and_8 (and_8_out, and_4_out, in_23);
  or or_4 (out_28, and_6_out, and_10_out);
  xor xor_8 (xor_8_out, input_picker_1_out_22, input_picker_2_out_22);
  not not_11 (not_11_out, xor_8_out);
  and and_9 (and_9_out, and_3_out, in_21);
  or or_5 (out_29, and_8_out, and_12_out);
  xor xor_9 (xor_9_out, input_picker_1_out_23, input_picker_2_out_23);
  not not_12 (not_12_out, xor_9_out);
  and and_10 (and_10_out, and_3_out, in_22);
  or or_6 (out_30, and_7_out, and_11_out);
  xor xor_10 (xor_10_out, input_picker_1_out_24, input_picker_2_out_24);
  not not_13 (not_13_out, xor_10_out);
  and and_11 (and_11_out, and_3_out, in_24);
  and and_12 (and_12_out, and_3_out, in_23);
  xor xor_11 (xor_11_out, input_picker_1_out_25, input_picker_2_out_25);
  not not_14 (not_14_out, xor_11_out);

  // Notes on the sheet:
  //   Executing function
  //   branch
  //   Instruction for branching on equal or not equal
  //   gets direct input from R1 and R2
endmodule

module general_register (
  input  \output ,
  input  in_2,
  input  in_3,
  input  in_4,
  input  in_5,
  input  in_6,
  input  in_7,
  input  in_8,
  input  in_9,
  input  clock,
  input  load,
  input  in_12,
  output out_13,
  output out_14,
  output out_15,
  output out_16,
  output out_17,
  output out_18,
  output out_19,
  output out_20,
  output out_21,
  output out_22,
  output out_23,
  output out_24,
  output out_25,
  output out_26,
  output out_27,
  output out_28
);

  wire and_1_out;

  and and_1 (and_1_out, clock, load);
  D_Flip_Flop d_ff_1 (.clk(and_1_out), .D(in_9), .Q(out_21), .reset(in_12));  // open: Qn, preset, en
  D_Flip_Flop d_ff_2 (.clk(and_1_out), .D(in_8), .Q(out_22), .reset(in_12));  // open: Qn, preset, en
  D_Flip_Flop d_ff_3 (.clk(and_1_out), .D(in_7), .Q(out_23), .reset(in_12));  // open: Qn, preset, en
  D_Flip_Flop d_ff_4 (.clk(and_1_out), .D(in_6), .Q(out_24), .reset(in_12));  // open: Qn, preset, en
  D_Flip_Flop d_ff_5 (.clk(and_1_out), .D(in_5), .Q(out_25), .reset(in_12));  // open: Qn, preset, en
  D_Flip_Flop d_ff_6 (.clk(and_1_out), .D(in_4), .Q(out_26), .reset(in_12));  // open: Qn, preset, en
  D_Flip_Flop d_ff_7 (.clk(and_1_out), .D(in_3), .Q(out_27), .reset(in_12));  // open: Qn, preset, en
  D_Flip_Flop d_ff_8 (.clk(and_1_out), .D(in_2), .Q(out_28), .reset(in_12));  // open: Qn, preset, en
  and and_2 (out_20, \output , out_21);
  and and_3 (out_19, \output , out_22);
  and and_4 (out_18, \output , out_23);
  and and_5 (out_17, \output , out_24);
  and and_6 (out_16, \output , out_25);
  and and_7 (out_15, \output , out_26);
  and and_8 (out_14, \output , out_27);
  and and_9 (out_13, \output , out_28);
endmodule

module _8_and (
  input  in_1,
  input  in_2,
  input  in_3,
  input  in_4,
  input  in_5,
  input  in_6,
  input  in_7,
  input  in_8,
  output out_9
);

  wire and_1_out, and_2_out, and_3_out, and_5_out, and_6_out, and_7_out;

  and and_1 (and_1_out, in_1, in_2);
  and and_2 (and_2_out, and_1_out, and_3_out);
  and and_3 (and_3_out, in_3, in_4);
  and and_4 (out_9, and_2_out, and_7_out);
  and and_5 (and_5_out, in_5, in_6);
  and and_6 (and_6_out, in_7, in_8);
  and and_7 (and_7_out, and_5_out, and_6_out);
endmodule

module input_picker (
  input  in_1,
  input  in_2,
  input  in_3,
  input  in_4,
  input  in_5,
  input  in_6,
  input  in_7,
  input  in_8,
  input  in_9,
  input  in_10,
  input  in_11,
  input  in_12,
  input  in_13,
  input  in_14,
  input  in_15,
  input  in_16,
  input  in_17,
  output out_18,
  output out_19,
  output out_20,
  output out_21,
  output out_22,
  output out_23,
  output out_24,
  output out_25
);

  wire and_1_out, and_2_out, and_3_out, and_4_out, and_5_out, and_6_out, and_7_out, and_8_out, and_9_out,
       and_10_out, and_11_out, and_12_out, and_13_out, and_14_out, and_15_out, and_16_out, not_1_out;

  not not_1 (not_1_out, in_1);
  and and_1 (and_1_out, not_1_out, in_2);
  and and_2 (and_2_out, not_1_out, in_3);
  and and_3 (and_3_out, not_1_out, in_4);
  and and_4 (and_4_out, not_1_out, in_5);
  and and_5 (and_5_out, not_1_out, in_6);
  and and_6 (and_6_out, not_1_out, in_7);
  and and_7 (and_7_out, not_1_out, in_8);
  and and_8 (and_8_out, not_1_out, in_9);
  and and_9 (and_9_out, in_1, in_10);
  and and_10 (and_10_out, in_1, in_11);
  and and_11 (and_11_out, in_1, in_12);
  and and_12 (and_12_out, in_1, in_13);
  and and_13 (and_13_out, in_1, in_14);
  and and_14 (and_14_out, in_1, in_15);
  and and_15 (and_15_out, in_1, in_16);
  and and_16 (and_16_out, in_1, in_17);
  or or_1 (out_18, and_1_out, and_9_out);
  or or_2 (out_19, and_2_out, and_10_out);
  or or_3 (out_20, and_3_out, and_11_out);
  or or_4 (out_21, and_4_out, and_12_out);
  or or_5 (out_22, and_5_out, and_13_out);
  or or_6 (out_23, and_6_out, and_14_out);
  or or_7 (out_24, and_7_out, and_15_out);
  or or_8 (out_25, and_8_out, and_16_out);
endmodule

module Stop (
  input  in_1,
  output out_2
);


  assign out_2 = in_1;

  // Notes on the sheet:
  //   This BB is just to make it clear that stop is an instruction
endmodule

module count_from_0 (
  input  zer0,
  input  start,
  input  clock,
  output out_4,
  output out_5,
  output out_6
);

  wire and_1_out, and_2_out, and_3_out, half_adder_1_out_3, half_adder_1_out_4, half_adder_2_out_3,
       half_adder_2_out_4, half_adder_3_out_3, not_1_out;

  half_adder half_adder_1 (.in_1(start), .in_2(out_4), .out_3(half_adder_1_out_3), .out_4(half_adder_1_out_4));
  half_adder half_adder_2 (
    .in_1(half_adder_1_out_4), .in_2(out_5), .out_3(half_adder_2_out_3), .out_4(half_adder_2_out_4));
  half_adder half_adder_3 (.in_1(half_adder_2_out_4), .in_2(out_6), .out_3(half_adder_3_out_3));  // open: out_4
  not not_1 (not_1_out, zer0);
  and and_1 (and_1_out, not_1_out, half_adder_1_out_3);
  and and_2 (and_2_out, not_1_out, half_adder_2_out_3);
  and and_3 (and_3_out, not_1_out, half_adder_3_out_3);
  D_Flip_Flop d_ff_1 (.clk(clock), .D(and_1_out), .Q(out_4));  // open: Qn, preset, en, reset
  D_Flip_Flop d_ff_2 (.clk(clock), .D(and_2_out), .Q(out_5));  // open: Qn, preset, en, reset
  D_Flip_Flop d_ff_3 (.clk(clock), .D(and_3_out), .Q(out_6));  // open: Qn, preset, en, reset

  // Notes on the sheet:
  //   a self incrementing loop
endmodule

module small_and (
  input  in_1,
  input  in_2,
  output out_3
);

  and and_1 (out_3, in_1, in_2);
endmodule

module small_or (
  input  in_1,
  input  in_2,
  output out_3
);

  or or_1 (out_3, in_1, in_2);
endmodule

module _2COMP (
  input  ON_OFF,
  input  In___0,
  input  In___1,
  input  In___2,
  input  In___3,
  input  In___4,
  input  In___5,
  input  In___6,
  input  In___7,
  output Out___0,
  output Out___1,
  output Out___2,
  output Out___3,
  output Out___4,
  output Out___5,
  output Out___6,
  output Out___7
);

  wire adder_1_cout, adder_1_out, adder_2_cout, adder_2_out, adder_3_cout, adder_3_out, adder_4_cout,
       adder_4_out, adder_5_cout, adder_5_out, adder_6_cout, adder_6_out, adder_7_out, and_1_out, and_2_out,
       and_3_out, and_4_out, and_5_out, and_6_out, and_7_out, not_1_out, not_2_out, not_3_out, not_4_out,
       not_5_out, not_6_out, not_7_out, not_8_out;

  not not_1 (not_1_out, In___1);
  and and_1 (and_1_out, ON_OFF, not_1_out);
  not not_2 (not_2_out, In___2);
  not not_3 (not_3_out, In___0);
  Adder #(.width(1)) adder_1 (.a(not_3_out), .b(and_1_out), .out(adder_1_out), .cout(adder_1_cout));  // open: cin
  and and_2 (and_2_out, ON_OFF, not_2_out);
  and and_3 (and_3_out, ON_OFF, not_4_out);
  not not_4 (not_4_out, In___3);
  not not_5 (not_5_out, In___4);
  Adder #(.width(1)) adder_2 (.a(adder_1_cout), .b(and_2_out), .out(adder_2_out), .cout(adder_2_cout));  // open: cin
  and and_4 (and_4_out, ON_OFF, not_5_out);
  not not_6 (not_6_out, In___5);
  Multiplexer #(.enable("false")) multiplexer_1 (.in0(In___1), .in1(adder_1_out), .out(Out___1), .sel(ON_OFF));
  Multiplexer #(.enable("false")) multiplexer_2 (.in0(In___2), .in1(adder_2_out), .out(Out___2), .sel(ON_OFF));
  Adder #(.width(1)) adder_3 (.a(adder_2_cout), .b(and_3_out), .out(adder_3_out), .cout(adder_3_cout));  // open: cin
  Adder #(.width(1)) adder_4 (.a(adder_3_cout), .b(and_4_out), .out(adder_4_out), .cout(adder_4_cout));  // open: cin
  and and_5 (and_5_out, ON_OFF, not_6_out);
  not not_7 (not_7_out, In___6);
  Multiplexer #(.enable("false")) multiplexer_3 (.in0(In___3), .in1(adder_3_out), .out(Out___3), .sel(ON_OFF));
  Adder #(.width(1)) adder_5 (.a(adder_4_cout), .b(and_5_out), .out(adder_5_out), .cout(adder_5_cout));  // open: cin
  and and_6 (and_6_out, ON_OFF, not_7_out);
  and and_7 (and_7_out, ON_OFF, not_8_out);
  not not_8 (not_8_out, In___7);
  Multiplexer #(.enable("false")) multiplexer_4 (.in0(In___4), .in1(adder_4_out), .out(Out___4), .sel(ON_OFF));
  Adder #(.width(1)) adder_6 (.a(adder_5_cout), .b(and_6_out), .out(adder_6_out), .cout(adder_6_cout));  // open: cin
  Adder #(.width(1)) adder_7 (.a(adder_6_cout), .b(and_7_out), .out(adder_7_out));  // open: cin, cout
  Multiplexer #(.enable("false")) multiplexer_5 (.in0(In___5), .in1(adder_5_out), .out(Out___5), .sel(ON_OFF));
  Multiplexer #(.enable("false")) multiplexer_6 (.in0(In___6), .in1(adder_6_out), .out(Out___6), .sel(ON_OFF));
  Multiplexer #(.enable("false")) multiplexer_7 (.in0(In___7), .in1(adder_7_out), .out(Out___7), .sel(ON_OFF));

  assign Out___0 = In___0;
endmodule

module ALU (
  input  MULTIPLY,
  input  R___0,
  input  R___1,
  input  R___2,
  input  R___3,
  input  R___4,
  input  R___5,
  input  R___6,
  input  R___7,
  input  SUBTRACT,
  input  L___0,
  input  L___1,
  input  L___2,
  input  L___3,
  input  L___4,
  input  L___5,
  input  L___6,
  input  L___7,
  output A___0,
  output A___1,
  output A___2,
  output A___3,
  output A___4,
  output A___5,
  output A___6,
  output A___7,
  output Zero,
  output Overflow,
  output Negative
);

  wire adder_1_cout, adder_1_out, adder_2_cout, adder_2_out, adder_3_cout, adder_3_out, adder_4_cout,
       adder_4_out, adder_5_cout, adder_5_out, adder_6_cout, adder_6_out, adder_7_cout, adder_7_out,
       adder_8_cout, adder_8_out, adder_9_cout, adder_9_out, adder_10_cout, adder_10_out, adder_11_out,
       adder_12_cout, adder_12_out, adder_13_cout, adder_13_out, adder_14_cout, adder_14_out, adder_15_out,
       adder_16_cout, adder_16_out, adder_17_out, adder_18_cout, adder_18_out, adder_19_cout, adder_19_out,
       adder_20_cout, adder_20_out, adder_21_out, adder_22_out, adder_23_cout, adder_23_out, adder_24_cout,
       adder_24_out, adder_25_cout, adder_25_out, adder_26_cout, adder_26_out, adder_27_cout, adder_27_out,
       adder_28_cout, adder_28_out, adder_29_cout, adder_29_out, adder_30_out, adder_31_cout, adder_31_out,
       adder_32_cout, adder_32_out, adder_33_cout, adder_33_out, adder_34_cout, adder_34_out, adder_35_cout,
       adder_35_out, adder_36_out, and_1_out, and_2_out, and_3_out, and_4_out, and_5_out, and_6_out,
       and_7_out, and_8_out, and_9_out, and_10_out, and_11_out, and_12_out, and_13_out, and_14_out,
       and_15_out, and_16_out, and_17_out, and_18_out, and_19_out, and_20_out, and_21_out, and_22_out,
       and_23_out, and_24_out, and_25_out, and_27_out, and_28_out, and_29_out, and_30_out, and_31_out,
       and_32_out, and_33_out, and_34_out, and_35_out, and_36_out, and_37_out, and_38_out, and_39_out,
       and_40_out, and_41_out, and_42_out, and_43_out, and_45_out, and_46_out, and_47_out, and_48_out,
       and_50_out, and_51_out, and_52_out, and_53_out, and_54_out, and_55_out, and_56_out, and_57_out,
       n2comp_1_out___0, n2comp_1_out___1, n2comp_1_out___2, n2comp_1_out___3, n2comp_1_out___4,
       n2comp_1_out___5, n2comp_1_out___6, n2comp_1_out___7, n2comp_2_out___0, n2comp_2_out___1,
       n2comp_2_out___2, n2comp_2_out___3, n2comp_2_out___4, n2comp_2_out___5, n2comp_2_out___6,
       n2comp_2_out___7, not_1_out, not_2_out, not_3_out, not_4_out, not_5_out, not_6_out, not_7_out,
       not_8_out, not_9_out, not_10_out, not_11_out, not_12_out, not_13_out, not_14_out, not_15_out,
       not_16_out, not_17_out, not_18_out, not_19_out, or_1_out, or_2_out, or_3_out, or_4_out, or_5_out,
       or_6_out, or_7_out, or_8_out, or_9_out;

  not not_1 (not_1_out, MULTIPLY);
  not not_2 (not_2_out, R___7);
  and and_1 (and_1_out, L___7, not_2_out);
  or or_1 (or_1_out, L___7, not_2_out);
  not not_3 (not_3_out, and_1_out);
  and and_2 (and_2_out, not_3_out, or_1_out, and_3_out);
  not not_4 (not_4_out, R___6);
  and and_3 (and_3_out, L___6, not_4_out);
  or or_2 (or_2_out, L___6, not_4_out);
  not not_5 (not_5_out, and_2_out);
  and and_4 (and_4_out, not_5_out, or_2_out, and_5_out);
  or or_3 (or_3_out, and_15_out, and_13_out, and_11_out, and_9_out, and_6_out, and_4_out, and_2_out, and_1_out);
  not not_6 (not_6_out, R___5);
  and and_5 (and_5_out, L___5, not_6_out);
  or or_4 (or_4_out, L___5, not_6_out);
  not not_7 (not_7_out, and_4_out);
  and and_6 (and_6_out, not_7_out, or_4_out, and_8_out);
  not not_8 (not_8_out, R___3);
  not not_9 (not_9_out, R___4);
  and and_7 (and_7_out, L___3, not_8_out);
  and and_8 (and_8_out, L___4, not_9_out);
  or or_5 (or_5_out, L___4, not_9_out);
  not not_10 (not_10_out, and_6_out);
  and and_9 (and_9_out, not_10_out, or_5_out, and_7_out);
  not not_11 (not_11_out, R___2);
  or or_6 (or_6_out, L___3, not_8_out);
  and and_10 (and_10_out, L___2, not_11_out);
  or or_7 (or_7_out, L___2, not_11_out);
  not not_12 (not_12_out, and_9_out);
  and and_11 (and_11_out, not_12_out, or_6_out, and_10_out);
  not not_13 (not_13_out, R___0);
  not not_14 (not_14_out, R___1);
  and and_12 (and_12_out, L___1, not_14_out);
  or or_8 (or_8_out, L___1, not_14_out);
  not not_15 (not_15_out, and_11_out);
  and and_13 (and_13_out, not_15_out, or_7_out, and_12_out);
  and and_14 (and_14_out, L___0, not_13_out);
  not not_16 (not_16_out, and_13_out);
  and and_15 (and_15_out, not_16_out, or_8_out, and_14_out);
  _2COMP u_2comp_1 (
    .ON_OFF(SUBTRACT), .In___0(L___0), .In___1(L___1), .In___2(L___2), .In___3(L___3), .In___4(L___4),
    .In___5(L___5), .In___6(L___6), .In___7(L___7), .Out___0(n2comp_1_out___0), .Out___1(n2comp_1_out___1),
    .Out___2(n2comp_1_out___2), .Out___3(n2comp_1_out___3), .Out___4(n2comp_1_out___4),
    .Out___5(n2comp_1_out___5), .Out___6(n2comp_1_out___6), .Out___7(n2comp_1_out___7));
  and and_16 (and_16_out, SUBTRACT, or_3_out);
  Adder #(.width(1)) adder_1 (.a(R___0), .b(n2comp_1_out___0), .out(adder_1_out), .cout(adder_1_cout));  // open: cin
  Adder #(.width(1)) adder_2 (
    .a(R___1), .b(n2comp_1_out___1), .out(adder_2_out), .cin(adder_1_cout), .cout(adder_2_cout));
  Adder #(.width(1)) adder_3 (
    .a(R___2), .b(n2comp_1_out___2), .out(adder_3_out), .cin(adder_2_cout), .cout(adder_3_cout));
  Adder #(.width(1)) adder_4 (
    .a(R___3), .b(n2comp_1_out___3), .out(adder_4_out), .cin(adder_3_cout), .cout(adder_4_cout));
  Adder #(.width(1)) adder_5 (
    .a(R___4), .b(n2comp_1_out___4), .out(adder_5_out), .cin(adder_4_cout), .cout(adder_5_cout));
  Adder #(.width(1)) adder_6 (
    .a(R___5), .b(n2comp_1_out___5), .out(adder_6_out), .cin(adder_5_cout), .cout(adder_6_cout));
  Adder #(.width(1)) adder_7 (
    .a(R___6), .b(n2comp_1_out___6), .out(adder_7_out), .cin(adder_6_cout), .cout(adder_7_cout));
  Adder #(.width(1)) adder_8 (
    .a(R___7), .b(n2comp_1_out___7), .out(adder_8_out), .cin(adder_7_cout), .cout(adder_8_cout));
  not not_17 (not_17_out, not_1_out);
  not not_18 (not_18_out, SUBTRACT);
  and and_17 (and_17_out, R___0, L___0);
  and and_18 (and_18_out, L___0, R___1);
  and and_19 (and_19_out, R___4, L___0);
  and and_20 (and_20_out, R___3, L___1);
  and and_21 (and_21_out, R___6, L___0);
  and and_22 (and_22_out, R___5, L___1);
  and and_23 (and_23_out, R___7, L___0);
  and and_24 (and_24_out, R___6, L___1);
  Multiplexer #(.enable("false")) multiplexer_1 (
    .in0(n2comp_2_out___5), .in1(adder_6_out), .out(A___5), .sel(not_1_out));
  Multiplexer #(.enable("false")) multiplexer_2 (
    .in0(n2comp_2_out___6), .in1(adder_7_out), .out(A___6), .sel(not_1_out));
  Multiplexer #(.enable("false")) multiplexer_3 (
    .in0(n2comp_2_out___7), .in1(adder_8_out), .out(A___7), .sel(not_1_out));
  and and_25 (and_25_out, SUBTRACT, not_17_out);
  and and_26 (Overflow, adder_8_cout, not_1_out, not_18_out);
  and and_27 (and_27_out, L___1, R___0);
  and and_28 (and_28_out, R___2, L___2);
  and and_29 (and_29_out, R___4, L___2);
  and and_30 (and_30_out, R___5, L___2);
  Multiplexer #(.enable("false")) multiplexer_4 (
    .in0(n2comp_2_out___1), .in1(adder_2_out), .out(A___1), .sel(not_1_out));
  Multiplexer #(.enable("false")) multiplexer_5 (
    .in0(n2comp_2_out___2), .in1(adder_3_out), .out(A___2), .sel(not_1_out));
  Multiplexer #(.enable("false")) multiplexer_6 (
    .in0(n2comp_2_out___3), .in1(adder_4_out), .out(A___3), .sel(not_1_out));
  Multiplexer #(.enable("false")) multiplexer_7 (
    .in0(n2comp_2_out___4), .in1(adder_5_out), .out(A___4), .sel(not_1_out));
  and and_31 (and_31_out, SUBTRACT, Zero, not_17_out);
  or or_9 (or_9_out, and_25_out, and_16_out);
  Adder #(.width(1)) adder_9 (.a(and_18_out), .b(and_27_out), .out(adder_9_out), .cout(adder_9_cout));  // open: cin
  and and_32 (and_32_out, R___2, L___0);
  Adder #(.width(1)) adder_10 (
    .a(and_20_out), .b(and_28_out), .out(adder_10_out), .cin(and_19_out), .cout(adder_10_cout));
  and and_33 (and_33_out, R___1, L___3);
  and and_34 (and_34_out, R___3, L___3);
  Adder #(.width(1)) adder_11 (.a(and_24_out), .b(and_30_out), .out(adder_11_out), .cin(and_23_out));  // open: cout
  and and_35 (and_35_out, R___4, L___3);
  Multiplexer #(.enable("false")) multiplexer_8 (
    .in0(n2comp_2_out___0), .in1(adder_1_out), .out(A___0), .sel(not_1_out));
  Adder #(.width(1)) adder_12 (
    .a(and_32_out), .b(and_36_out), .out(adder_12_out), .cin(adder_9_cout), .cout(adder_12_cout));
  and and_36 (and_36_out, L___1, R___1);
  and and_37 (and_37_out, R___0, L___2);
  and and_38 (and_38_out, R___0, L___4);
  and and_39 (and_39_out, R___5, L___0);
  and and_40 (and_40_out, R___2, L___4);
  and and_41 (and_41_out, R___1, L___5);
  and and_42 (and_42_out, R___3, L___4);
  and and_43 (and_43_out, R___2, L___5);
  and and_44 (Zero, ~A___0, ~A___1, ~A___2, ~A___3, ~A___4, ~A___5, ~A___6, ~A___7, ~Overflow);  // AND_Gate
  not not_19 (not_19_out, and_31_out);
  Adder #(.width(1)) adder_13 (
    .a(adder_12_out), .b(and_37_out), .out(adder_13_out), .cout(adder_13_cout));  // open: cin
  and and_45 (and_45_out, R___3, L___0);
  Adder #(.width(1)) adder_14 (
    .a(and_33_out), .b(and_38_out), .out(adder_14_out), .cin(adder_10_out), .cout(adder_14_cout));
  and and_46 (and_46_out, R___4, L___1);
  and and_47 (and_47_out, R___0, L___6);
  Adder #(.width(1)) adder_15 (.a(and_35_out), .b(and_42_out), .out(adder_15_out), .cin(adder_11_out));  // open: cout
  and and_48 (and_48_out, R___1, L___6);
  and and_49 (Negative, not_19_out, or_9_out);
  and and_50 (and_50_out, R___2, L___1);
  and and_51 (and_51_out, R___3, L___2);
  Adder #(.width(1)) adder_16 (
    .a(and_41_out), .b(and_47_out), .out(adder_16_out), .cin(and_40_out), .cout(adder_16_cout));
  Adder #(.width(1)) adder_17 (
    .a(adder_16_cout), .b(adder_15_out), .out(adder_17_out), .cin(adder_20_cout));  // open: cout
  and and_52 (and_52_out, R___0, L___7);
  and and_53 (and_53_out, R___1, L___2);
  and and_54 (and_54_out, R___0, L___3);
  Adder #(.width(1)) adder_18 (
    .a(and_39_out), .b(and_46_out), .out(adder_18_out), .cin(adder_14_cout), .cout(adder_18_cout));
  and and_55 (and_55_out, R___2, L___3);
  and and_56 (and_56_out, R___1, L___4);
  Adder #(.width(1)) adder_19 (
    .a(and_22_out), .b(adder_20_out), .out(adder_19_out), .cin(and_21_out), .cout(adder_19_cout));
  Adder #(.width(1)) adder_20 (
    .a(and_34_out), .b(adder_16_out), .out(adder_20_out), .cin(and_29_out), .cout(adder_20_cout));
  Adder #(.width(1)) adder_21 (
    .a(adder_19_cout), .b(adder_17_out), .out(adder_21_out), .cin(adder_29_cout));  // open: cout
  Adder #(.width(1)) adder_22 (.a(and_48_out), .b(and_52_out), .out(adder_22_out), .cin(and_43_out));  // open: cout
  Adder #(.width(1)) adder_23 (
    .a(adder_13_cout), .b(adder_12_cout), .out(adder_23_out), .cout(adder_23_cout));  // open: cin
  Adder #(.width(1)) adder_24 (
    .a(and_45_out), .b(and_50_out), .out(adder_24_out), .cin(adder_23_out), .cout(adder_24_cout));
  Adder #(.width(1)) adder_25 (
    .a(and_53_out), .b(and_54_out), .out(adder_25_out), .cin(adder_24_out), .cout(adder_25_cout));
  Adder #(.width(1)) adder_26 (
    .a(adder_24_cout), .b(adder_23_cout), .out(adder_26_out), .cin(adder_25_cout), .cout(adder_26_cout));
  Adder #(.width(1)) adder_27 (
    .a(and_51_out), .b(and_55_out), .out(adder_27_out), .cin(adder_10_cout), .cout(adder_27_cout));
  Adder #(.width(1)) adder_28 (
    .a(adder_18_out), .b(and_56_out), .out(adder_28_out), .cin(adder_32_out), .cout(adder_28_cout));
  and and_57 (and_57_out, R___0, L___5);
  Adder #(.width(1)) adder_29 (
    .a(adder_27_cout), .b(adder_19_out), .out(adder_29_out), .cin(adder_18_cout), .cout(adder_29_cout));
  Adder #(.width(1)) adder_30 (
    .a(adder_21_out), .b(adder_22_out), .out(adder_30_out), .cin(adder_34_cout));  // open: cout
  _2COMP u_2comp_2 (
    .ON_OFF(SUBTRACT), .In___0(and_17_out), .In___1(adder_9_out), .In___2(adder_13_out),
    .In___3(adder_25_out), .In___4(adder_31_out), .In___5(adder_33_out), .In___6(adder_35_out),
    .In___7(adder_36_out), .Out___0(n2comp_2_out___0), .Out___1(n2comp_2_out___1),
    .Out___2(n2comp_2_out___2), .Out___3(n2comp_2_out___3), .Out___4(n2comp_2_out___4),
    .Out___5(n2comp_2_out___5), .Out___6(n2comp_2_out___6), .Out___7(n2comp_2_out___7));
  Adder #(.width(1)) adder_31 (
    .a(adder_14_out), .b(adder_26_out), .out(adder_31_out), .cout(adder_31_cout));  // open: cin
  Adder #(.width(1)) adder_32 (
    .a(adder_31_cout), .b(adder_27_out), .out(adder_32_out), .cin(adder_26_cout), .cout(adder_32_cout));
  Adder #(.width(1)) adder_33 (
    .a(adder_28_out), .b(and_57_out), .out(adder_33_out), .cout(adder_33_cout));  // open: cin
  Adder #(.width(1)) adder_34 (
    .a(adder_32_cout), .b(adder_29_out), .out(adder_34_out), .cin(adder_28_cout), .cout(adder_34_cout));
  Adder #(.width(1)) adder_35 (
    .a(adder_33_cout), .b(adder_34_out), .out(adder_35_out), .cout(adder_35_cout));  // open: cin
  Adder #(.width(1)) adder_36 (.a(adder_35_cout), .b(adder_30_out), .out(adder_36_out));  // open: cin, cout

  // Notes on the sheet:
  //   Note: Overflow does not get triggered when subtracting or multiplying
  //   Zero does not check past the first 8 bits with multiplication
endmodule

module MAR (
  input  in_1,
  input  \output ,
  input  in_3,
  input  in_4,
  input  in_5,
  input  in_6,
  input  in_7,
  input  in_8,
  input  in_9,
  input  in_10,
  input  in_11,
  input  clock,
  input  load,
  output out_14,
  output out_15,
  output out_16,
  output out_17
);

  wire and_1_out, and_2_out, and_3_out, and_4_out, and_5_out, and_6_out, and_7_out, and_8_out, and_9_out,
       d_ff_1_q, d_ff_2_q, d_ff_3_q, d_ff_4_q, not_1_out, or_1_out, or_2_out, or_3_out, or_4_out;

  and and_1 (and_1_out, clock, load);
  not not_1 (not_1_out, in_1);
  and and_2 (and_2_out, in_1, in_6);
  and and_3 (and_3_out, in_1, in_5);
  and and_4 (and_4_out, in_1, in_4);
  and and_5 (and_5_out, in_1, in_3);
  and and_6 (and_6_out, not_1_out, in_10);
  and and_7 (and_7_out, not_1_out, in_9);
  and and_8 (and_8_out, not_1_out, in_8);
  and and_9 (and_9_out, not_1_out, in_7);
  or or_1 (or_1_out, and_2_out, and_6_out);
  or or_2 (or_2_out, and_3_out, and_7_out);
  or or_3 (or_3_out, and_4_out, and_8_out);
  or or_4 (or_4_out, and_5_out, and_9_out);
  D_Flip_Flop d_ff_1 (.clk(and_1_out), .D(or_1_out), .Q(d_ff_1_q), .reset(in_11));  // open: Qn, preset, en
  D_Flip_Flop d_ff_2 (.clk(and_1_out), .D(or_2_out), .Q(d_ff_2_q), .reset(in_11));  // open: Qn, preset, en
  D_Flip_Flop d_ff_3 (.clk(and_1_out), .D(or_3_out), .Q(d_ff_3_q), .reset(in_11));  // open: Qn, preset, en
  D_Flip_Flop d_ff_4 (.clk(and_1_out), .D(or_4_out), .Q(d_ff_4_q), .reset(in_11));  // open: Qn, preset, en
  and and_10 (out_17, \output , d_ff_1_q);
  and and_11 (out_16, \output , d_ff_2_q);
  and and_12 (out_15, \output , d_ff_3_q);
  and and_13 (out_14, \output , d_ff_4_q);
endmodule

module MBR (
  input  in_1,
  input  in_2,
  input  in_3,
  input  in_4,
  input  in_5,
  input  in_6,
  input  in_7,
  input  in_8,
  input  in_9,
  input  in_10,
  input  in_11,
  input  in_12,
  input  in_13,
  input  in_14,
  input  in_15,
  input  in_16,
  input  in_17,
  input  \output ,
  input  clock,
  input  in_20,
  input  load,
  output out_22,
  output out_23,
  output out_24,
  output out_25,
  output out_26,
  output out_27,
  output out_28,
  output out_29
);

  wire and_1_out, and_2_out, and_3_out, and_4_out, and_5_out, and_6_out, and_7_out, and_8_out, and_9_out,
       and_10_out, and_11_out, and_12_out, and_13_out, and_14_out, and_15_out, and_16_out, and_17_out,
       d_ff_1_q, d_ff_2_q, d_ff_3_q, d_ff_4_q, d_ff_5_q, d_ff_6_q, d_ff_7_q, d_ff_8_q, not_1_out, or_1_out,
       or_2_out, or_3_out, or_4_out, or_5_out, or_6_out, or_7_out, or_8_out;

  not not_1 (not_1_out, in_1);
  and and_1 (and_1_out, in_1, in_17);
  and and_2 (and_2_out, in_1, in_16);
  and and_3 (and_3_out, in_1, in_15);
  and and_4 (and_4_out, in_1, in_14);
  and and_5 (and_5_out, in_1, in_13);
  and and_6 (and_6_out, in_1, in_12);
  and and_7 (and_7_out, in_1, in_11);
  and and_8 (and_8_out, in_1, in_10);
  and and_9 (and_9_out, not_1_out, in_9);
  and and_10 (and_10_out, not_1_out, in_8);
  and and_11 (and_11_out, not_1_out, in_7);
  and and_12 (and_12_out, not_1_out, in_6);
  and and_13 (and_13_out, not_1_out, in_5);
  and and_14 (and_14_out, not_1_out, in_4);
  and and_15 (and_15_out, not_1_out, in_3);
  and and_16 (and_16_out, not_1_out, in_2);
  or or_1 (or_1_out, and_1_out, and_9_out);
  or or_2 (or_2_out, and_2_out, and_10_out);
  or or_3 (or_3_out, and_3_out, and_11_out);
  or or_4 (or_4_out, and_4_out, and_12_out);
  or or_5 (or_5_out, and_5_out, and_13_out);
  or or_6 (or_6_out, and_6_out, and_14_out);
  or or_7 (or_7_out, and_7_out, and_15_out);
  or or_8 (or_8_out, and_8_out, and_16_out);
  and and_17 (and_17_out, clock, load);
  D_Flip_Flop d_ff_1 (.clk(and_17_out), .D(or_1_out), .Q(d_ff_1_q), .reset(in_20));  // open: Qn, preset, en
  D_Flip_Flop d_ff_2 (.clk(and_17_out), .D(or_2_out), .Q(d_ff_2_q), .reset(in_20));  // open: Qn, preset, en
  D_Flip_Flop d_ff_3 (.clk(and_17_out), .D(or_3_out), .Q(d_ff_3_q), .reset(in_20));  // open: Qn, preset, en
  D_Flip_Flop d_ff_4 (.clk(and_17_out), .D(or_4_out), .Q(d_ff_4_q), .reset(in_20));  // open: Qn, preset, en
  D_Flip_Flop d_ff_5 (.clk(and_17_out), .D(or_5_out), .Q(d_ff_5_q), .reset(in_20));  // open: Qn, preset, en
  D_Flip_Flop d_ff_6 (.clk(and_17_out), .D(or_6_out), .Q(d_ff_6_q), .reset(in_20));  // open: Qn, preset, en
  D_Flip_Flop d_ff_7 (.clk(and_17_out), .D(or_7_out), .Q(d_ff_7_q), .reset(in_20));  // open: Qn, preset, en
  D_Flip_Flop d_ff_8 (.clk(and_17_out), .D(or_8_out), .Q(d_ff_8_q), .reset(in_20));  // open: Qn, preset, en
  and and_18 (out_29, \output , d_ff_1_q);
  and and_19 (out_28, \output , d_ff_2_q);
  and and_20 (out_27, \output , d_ff_3_q);
  and and_21 (out_26, \output , d_ff_4_q);
  and and_22 (out_25, \output , d_ff_5_q);
  and and_23 (out_24, \output , d_ff_6_q);
  and and_24 (out_23, \output , d_ff_7_q);
  and and_25 (out_22, \output , d_ff_8_q);
endmodule

module output_merger (
  input  in_1,
  input  in_2,
  input  in_3,
  input  in_4,
  input  in_5,
  input  in_6,
  input  in_7,
  input  in_8,
  input  in_9,
  input  in_10,
  input  in_11,
  input  in_12,
  input  in_13,
  input  in_14,
  input  in_15,
  input  in_16,
  input  in_17,
  input  in_18,
  input  in_19,
  input  in_20,
  input  in_21,
  input  in_22,
  input  in_23,
  input  in_24,
  input  in_25,
  input  in_26,
  input  in_27,
  input  in_28,
  input  in_29,
  input  in_30,
  input  in_31,
  input  in_32,
  input  in_33,
  input  in_34,
  input  in_35,
  input  in_36,
  input  in_37,
  input  in_38,
  input  in_39,
  input  in_40,
  input  in_41,
  input  in_42,
  input  in_43,
  input  in_44,
  input  in_45,
  input  in_46,
  input  in_47,
  input  in_48,
  input  in_49,
  output out_50,
  output out_51,
  output out_52,
  output out_53,
  output out_54,
  output out_55,
  output out_56,
  output out_57,
  output out_58,
  output out_59,
  output out_60,
  output out_61,
  output out_62,
  output out_63,
  output out_64,
  output out_65
);

  wire or_9_out, or_10_out, or_11_out, or_12_out, or_13_out, or_14_out, or_15_out, or_16_out, or_17_out,
       or_18_out, or_19_out, or_20_out, or_21_out, or_22_out, or_23_out, or_24_out, or_25_out, or_26_out,
       or_27_out, or_28_out, or_29_out, or_30_out, or_31_out, or_32_out, or_33_out, or_34_out, or_35_out,
       or_36_out, or_37_out, or_38_out, or_39_out, or_40_out, or_41_out, or_42_out, or_43_out, or_44_out;

  and and_1 (out_59, out_51, in_45);
  and and_2 (out_58, out_50, in_45);
  or or_1 (out_51, in_6, or_11_out);
  or or_2 (out_50, in_5, or_10_out);
  and and_3 (out_61, out_53, in_45);
  and and_4 (out_60, out_52, in_45);
  or or_3 (out_52, in_7, or_12_out);
  and and_5 (out_62, out_54, in_45);
  or or_4 (out_53, in_8, or_13_out);
  or or_5 (out_54, in_9, or_14_out);
  and and_6 (out_64, out_56, in_45);
  and and_7 (out_63, out_55, in_45);
  or or_6 (out_56, in_11, or_16_out);
  or or_7 (out_55, in_10, or_15_out);
  and and_8 (out_65, out_57, in_45);
  or or_8 (out_57, in_12, or_17_out);
  or or_9 (or_9_out, in_25, in_33);
  or or_10 (or_10_out, or_25_out, or_9_out);
  or or_11 (or_11_out, or_26_out, or_18_out);
  or or_12 (or_12_out, or_27_out, or_19_out);
  or or_13 (or_13_out, or_28_out, or_20_out);
  or or_14 (or_14_out, or_29_out, or_21_out);
  or or_15 (or_15_out, or_30_out, or_22_out);
  or or_16 (or_16_out, or_31_out, or_23_out);
  or or_17 (or_17_out, or_32_out, or_24_out);
  or or_18 (or_18_out, in_34, in_26);
  or or_19 (or_19_out, in_35, in_27);
  or or_20 (or_20_out, in_28, in_36);
  or or_21 (or_21_out, in_29, in_37);
  or or_22 (or_22_out, in_30, in_38);
  or or_23 (or_23_out, in_31, in_39);
  or or_24 (or_24_out, in_32, in_40);
  or or_25 (or_25_out, 1'b0, in_17);
  or or_26 (or_26_out, 1'b0, in_18);
  or or_27 (or_27_out, 1'b0, in_19);
  or or_28 (or_28_out, 1'b0, in_20);
  or or_29 (or_29_out, or_34_out, in_21);
  or or_30 (or_30_out, or_38_out, in_22);
  or or_31 (or_31_out, or_43_out, in_23);
  or or_32 (or_32_out, or_42_out, in_24);
  or or_33 (or_33_out, in_41, in_46);
  or or_34 (or_34_out, or_33_out, or_37_out);
  or or_35 (or_35_out, in_42, in_47);
  or or_36 (or_36_out, in_43, in_48);
  or or_37 (or_37_out, in_1, in_13);
  or or_38 (or_38_out, or_35_out, or_41_out);
  or or_39 (or_39_out, in_49, in_44);
  or or_40 (or_40_out, in_3, in_15);
  or or_41 (or_41_out, in_14, in_2);
  or or_42 (or_42_out, or_39_out, or_44_out);
  or or_43 (or_43_out, or_36_out, or_40_out);
  or or_44 (or_44_out, in_4, in_16);

  // Notes on the sheet:
  //   merges output of CPU bus
endmodule

module output_alu (
  input  in_1,
  input  in_2,
  input  in_3,
  input  in_4,
  input  in_5,
  input  in_6,
  input  in_7,
  input  in_8,
  input  in_9,
  input  in_10,
  input  in_11,
  output out_12,
  output out_13,
  output out_14,
  output out_15,
  output out_16,
  output out_17,
  output out_18,
  output out_19
);

  wire d_ff_1_q, d_ff_2_q, d_ff_3_q, d_ff_4_q, d_ff_5_q, d_ff_6_q, d_ff_7_q, d_ff_8_q;

  and and_1 (out_12, in_2, d_ff_1_q);
  and and_2 (out_13, in_2, d_ff_2_q);
  and and_3 (out_14, in_2, d_ff_3_q);
  and and_4 (out_15, in_2, d_ff_4_q);
  and and_5 (out_16, in_2, d_ff_5_q);
  and and_6 (out_17, in_2, d_ff_6_q);
  and and_7 (out_18, in_2, d_ff_7_q);
  and and_8 (out_19, in_2, d_ff_8_q);
  D_Flip_Flop d_ff_1 (.clk(in_1), .D(in_3), .Q(d_ff_1_q), .reset(in_11));  // open: Qn, preset, en
  D_Flip_Flop d_ff_2 (.clk(in_1), .D(in_4), .Q(d_ff_2_q), .reset(in_11));  // open: Qn, preset, en
  D_Flip_Flop d_ff_3 (.clk(in_1), .D(in_5), .Q(d_ff_3_q), .reset(in_11));  // open: Qn, preset, en
  D_Flip_Flop d_ff_4 (.clk(in_1), .D(in_6), .Q(d_ff_4_q), .reset(in_11));  // open: Qn, preset, en
  D_Flip_Flop d_ff_5 (.clk(in_1), .D(in_7), .Q(d_ff_5_q), .reset(in_11));  // open: Qn, preset, en
  D_Flip_Flop d_ff_6 (.clk(in_1), .D(in_8), .Q(d_ff_6_q), .reset(in_11));  // open: Qn, preset, en
  D_Flip_Flop d_ff_7 (.clk(in_1), .D(in_9), .Q(d_ff_7_q), .reset(in_11));  // open: Qn, preset, en
  D_Flip_Flop d_ff_8 (.clk(in_1), .D(in_10), .Q(d_ff_8_q), .reset(in_11));  // open: Qn, preset, en

  // Notes on the sheet:
  //   alu register
endmodule

module Add_Sub (
  input  _1,
  input  _2,
  input  add,
  input  sub,
  input  clock,
  output out_6,
  output out_7,
  output out_8,
  output ALU_output,
  output R_input,
  output L_input,
  output out_12,
  output R2_input,
  output R1_output,
  output R2_output
);

  wire and_1_out, and_2_out, and_4_out, and_5_out, and_6_out, and_8_out, and_9_out, and_10_out, and_11_out,
       and_12_out, and_14_out, and_16_out, and_18_out, and_19_out, count_from_0_1_out_4,
       count_from_0_1_out_5, count_from_0_1_out_6, not_1_out, not_2_out, not_3_out, not_4_out, not_5_out,
       not_6_out, not_7_out, not_8_out, not_9_out, not_10_out, not_11_out, not_12_out, not_13_out,
       not_14_out, not_15_out, not_16_out, not_17_out, xor_1_out, xor_2_out, xor_3_out, xor_4_out, xor_5_out,
       xor_6_out, xor_7_out, xor_8_out, xor_9_out;

  not not_1 (not_1_out, clock);
  or or_1 (out_8, add, sub);
  count_from_0 count_from_0_1 (
    .out_4(count_from_0_1_out_4), .out_5(count_from_0_1_out_5), .out_6(count_from_0_1_out_6), .start(out_8),
    .clock(clock), .zer0(ALU_output));
  and and_1 (and_1_out, out_8, not_1_out);
  xor xor_1 (xor_1_out, count_from_0_1_out_6, 1'b0);
  xor xor_2 (xor_2_out, count_from_0_1_out_5, 1'b0);
  not not_2 (not_2_out, xor_1_out);
  not not_3 (not_3_out, xor_2_out);
  and and_2 (and_2_out, not_2_out, not_3_out);
  and and_3 (R_input, and_4_out, and_1_out);
  not not_4 (not_4_out, 1'b0);
  xor xor_3 (xor_3_out, count_from_0_1_out_4, not_4_out);
  not not_5 (not_5_out, xor_3_out);
  and and_4 (and_4_out, and_2_out, not_5_out);
  and and_5 (and_5_out, and_4_out, _1);
  not not_6 (not_6_out, _1);
  and and_6 (and_6_out, and_4_out, not_6_out);
  and and_7 (L_input, and_1_out, and_11_out);
  not not_7 (not_7_out, _2);
  and and_8 (and_8_out, and_11_out, _2);
  and and_9 (and_9_out, not_7_out, and_11_out);
  small_or small_or_1 (.in_1(and_6_out), .in_2(and_9_out), .out_3(R1_output));
  xor xor_4 (xor_4_out, count_from_0_1_out_5, not_10_out);
  xor xor_5 (xor_5_out, count_from_0_1_out_6, 1'b0);
  not not_8 (not_8_out, xor_5_out);
  not not_9 (not_9_out, xor_4_out);
  and and_10 (and_10_out, not_8_out, not_9_out);
  small_or small_or_2 (.in_1(and_5_out), .in_2(and_8_out), .out_3(R2_output));
  not not_10 (not_10_out, 1'b0);
  xor xor_6 (xor_6_out, count_from_0_1_out_4, 1'b0);
  not not_11 (not_11_out, xor_6_out);
  and and_11 (and_11_out, and_10_out, not_11_out);
  and and_12 (and_12_out, _1, ALU_output);
  and and_13 (out_12, and_1_out, and_14_out);
  not not_12 (not_12_out, _1);
  and and_14 (and_14_out, not_12_out, ALU_output);
  and and_15 (R2_input, and_1_out, and_12_out);
  xor xor_7 (xor_7_out, count_from_0_1_out_6, 1'b0);
  not not_13 (not_13_out, xor_7_out);
  and and_16 (and_16_out, not_13_out, not_16_out);
  not not_14 (not_14_out, 1'b0);
  xor xor_8 (xor_8_out, count_from_0_1_out_5, not_14_out);
  xor xor_9 (xor_9_out, count_from_0_1_out_4, not_17_out);
  not not_15 (not_15_out, xor_9_out);
  not not_16 (not_16_out, xor_8_out);
  and and_17 (ALU_output, and_16_out, not_15_out);
  not not_17 (not_17_out, 1'b0);
  and and_18 (and_18_out, and_11_out, and_1_out);
  and and_19 (and_19_out, ALU_output, and_1_out);
  or or_2 (out_7, and_18_out, and_19_out);

  assign out_6 = ALU_output;

  // Notes on the sheet:
  //   Instruction for add/subtract
  //   R1 input
  //   ALU/STATUs input
endmodule

module multiple_and (
  input  in_1,
  input  in_2,
  input  in_3,
  output out_4
);

  wire and_1_out;

  and and_1 (and_1_out, in_1, in_2);
  and and_2 (out_4, and_1_out, in_3);
endmodule

module choose_inst (
  input  in_1,
  input  in_2,
  input  in_3,
  output out_4
);

  wire or_2_out;

  or or_1 (out_4, in_3, or_2_out);
  or or_2 (or_2_out, in_2, in_1);
endmodule

module switch (
  input  in_1,
  input  in_2,
  input  in_3,
  output out_4
);

  wire or_1_out;

  T_Flip_Flop t_ff_1 (.clk(in_1), .T(or_1_out), .Q(out_4));  // open: Qn, preset, reset, en
  or or_1 (or_1_out, in_2, in_3);

  // Notes on the sheet:
  //   The T flip flop changes whenever there is an input, i.e. when the CPU should switch from load inst to execute inst
endmodule
module MULT (
  input  in_1,
  input  in_2,
  input  in_3,
  input  in_4,
  input  in_5,
  input  in_6,
  input  in_7,
  output out_8,
  output out_9,
  output out_10,
  output out_11,
  output out_12,
  output out_13,
  output out_14,
  output out_15,
  output out_16,
  output out_17,
  output out_18,
  output out_19,
  output out_20,
  output alu_output
);

  wire and_1_out, and_3_out, and_4_out, and_7_out, and_10_out, and_12_out, and_13_out, and_14_out,
       and_15_out, and_17_out, and_18_out, count_from_0_1_out_4, count_from_0_1_out_5, not_1_out, not_2_out,
       not_3_out, not_4_out, not_5_out, not_6_out, not_7_out, not_8_out, not_9_out, not_10_out, not_11_out,
       not_12_out, not_13_out, not_14_out, not_15_out, not_16_out, not_17_out, xor_1_out, xor_2_out,
       xor_3_out, xor_4_out, xor_5_out, xor_6_out;

  not not_1 (not_1_out, in_7);
  count_from_0 count_from_0_1 (
    .out_4(count_from_0_1_out_4), .out_5(count_from_0_1_out_5), .start(in_1), .clock(in_7), .zer0(alu_output));  // open: out_6
  and and_1 (and_1_out, in_1, not_1_out);
  and and_2 (out_15, and_3_out, and_1_out);
  xor xor_1 (xor_1_out, 1'b0, count_from_0_1_out_5);
  not not_2 (not_2_out, xor_1_out);
  and and_3 (and_3_out, not_2_out, not_4_out);
  not not_3 (not_3_out, 1'b0);
  xor xor_2 (xor_2_out, not_3_out, count_from_0_1_out_4);
  not not_4 (not_4_out, xor_2_out);
  not not_5 (not_5_out, in_2);
  and and_4 (and_4_out, not_5_out, not_6_out);
  and and_5 (out_19, and_3_out, and_4_out);
  not not_6 (not_6_out, 1'b0);
  and and_6 (out_16, and_10_out, and_1_out);
  not not_7 (not_7_out, 1'b0);
  and and_7 (and_7_out, in_2, not_7_out);
  and and_8 (out_20, and_3_out, and_7_out);
  not not_8 (not_8_out, 1'b0);
  xor xor_3 (xor_3_out, not_8_out, count_from_0_1_out_5);
  not not_9 (not_9_out, xor_3_out);
  and and_9 (out_17, and_1_out, and_1_out, and_13_out);
  xor xor_4 (xor_4_out, 1'b0, count_from_0_1_out_4);
  not not_10 (not_10_out, xor_4_out);
  and and_10 (and_10_out, not_9_out, not_10_out);
  and and_11 (out_18, and_15_out, and_1_out);
  not not_11 (not_11_out, in_2);
  not not_12 (not_12_out, 1'b0);
  and and_12 (and_12_out, not_11_out, not_12_out);
  and and_13 (and_13_out, alu_output, and_12_out);
  not not_13 (not_13_out, 1'b0);
  not not_14 (not_14_out, 1'b0);
  and and_14 (and_14_out, in_2, not_14_out);
  and and_15 (and_15_out, alu_output, and_14_out);
  not not_15 (not_15_out, 1'b0);
  xor xor_5 (xor_5_out, not_15_out, count_from_0_1_out_4);
  xor xor_6 (xor_6_out, not_13_out, count_from_0_1_out_5);
  not not_16 (not_16_out, xor_6_out);
  not not_17 (not_17_out, xor_5_out);
  and and_16 (alu_output, not_16_out, not_17_out);
  and and_17 (and_17_out, and_1_out, and_10_out);
  and and_18 (and_18_out, and_1_out, alu_output);
  or or_1 (out_10, and_17_out, and_18_out);
  and and_19 (out_12, and_10_out, in_4);
  and and_20 (out_11, in_3, and_10_out);
  and and_21 (out_13, in_5, and_10_out);
  and and_22 (out_14, in_6, and_10_out);

  assign out_8 = alu_output;
  assign out_9 = in_1;

  // Notes on the sheet:
  //   R input
  //   L input
  //   R1 input
  //   Instruction for multiplication 
  //   R2 input
  //   R1 ouput
  //   R2 output
  //   ALU/STATUS input
endmodule

module input_pins (
  input  in_1,
  input  in_2,
  input  in_3,
  input  in_4,
  input  in_5,
  input  in_6,
  input  in_7,
  input  in_8,
  input  in_9,
  input  in_10,
  input  in_11,
  input  in_12,
  input  in_13,
  output out_14,
  output out_15,
  output out_16,
  output out_17
);

  wire and_1_out, d_ff_1_q, d_ff_2_q, d_ff_3_q, d_ff_4_q, not_1_out, or_1_out, or_2_out, or_3_out, or_4_out;

  not not_1 (not_1_out, in_10);
  and and_1 (and_1_out, in_10, not_1_out);
  or or_1 (or_1_out, and_1_out, in_3, in_2);
  D_Flip_Flop d_ff_1 (.clk(in_12), .D(or_1_out), .Q(d_ff_1_q), .reset(in_11));  // open: Qn, preset, en
  and and_2 (out_14, d_ff_1_q, in_13);
  or or_2 (or_2_out, in_1, in_6, in_5, in_4);
  D_Flip_Flop d_ff_2 (.clk(in_12), .D(or_2_out), .Q(d_ff_2_q), .reset(in_11));  // open: Qn, preset, en
  and and_3 (out_15, d_ff_2_q, in_13);
  or or_3 (or_3_out, in_3, in_1, in_5, in_9, in_7);
  or or_4 (or_4_out, in_1, in_6, in_9, in_8);
  D_Flip_Flop d_ff_3 (.clk(in_12), .D(or_4_out), .Q(d_ff_3_q), .reset(in_11));  // open: Qn, preset, en
  and and_4 (out_16, d_ff_3_q, in_13);
  D_Flip_Flop d_ff_4 (.clk(in_12), .D(or_3_out), .Q(d_ff_4_q), .reset(in_11));  // open: Qn, preset, en
  and and_5 (out_17, d_ff_4_q, in_13);

  // Notes on the sheet:
  //   input keypad + buffer
endmodule

module system_bus_chooser (
  input  in_1,
  input  in_2,
  input  in_3,
  input  in_4,
  input  in_5,
  input  in_6,
  input  in_7,
  input  in_8,
  input  in_9,
  input  in_10,
  input  in_11,
  input  in_12,
  input  in_13,
  input  in_14,
  input  in_15,
  input  in_16,
  input  in_17,
  input  in_18,
  input  in_19,
  input  in_20,
  output out_21,
  output out_22,
  output out_23,
  output out_24,
  output out_25,
  output out_26,
  output out_27,
  output out_28
);

  wire or_3_out, or_4_out, or_7_out, or_8_out, or_10_out, or_13_out, or_14_out, or_16_out;

  or or_1 (out_22, 1'b0, or_4_out);
  or or_2 (out_21, 1'b0, or_3_out);
  or or_3 (or_3_out, in_13, in_1);
  or or_4 (or_4_out, in_14, in_2);
  or or_5 (out_23, 1'b0, or_8_out);
  or or_6 (out_24, 1'b0, or_7_out);
  or or_7 (or_7_out, in_16, in_4);
  or or_8 (or_8_out, in_15, in_3);
  or or_9 (out_25, in_5, or_10_out);
  or or_10 (or_10_out, in_17, in_6);
  or or_11 (out_27, in_9, or_14_out);
  or or_12 (out_26, in_7, or_13_out);
  or or_13 (or_13_out, in_18, in_8);
  or or_14 (or_14_out, in_19, in_10);
  or or_15 (out_28, in_11, or_16_out);
  or or_16 (or_16_out, in_20, in_12);

  // Notes on the sheet:
  //   merges all outputs of periperals
endmodule

module get_input (
  input  in_1,
  input  in_2,
  input  in_3,
  output out_4,
  output out_5,
  output MBR_input,
  output input_output,
  output MBR_output,
  output R1_input,
  output R2_input,
  output MBR_r_c
);

  wire and_1_out, and_4_out, and_5_out, and_6_out, and_10_out, count_from_0_1_out_4, count_from_0_1_out_5,
       count_from_0_1_out_6, not_1_out, not_2_out, not_3_out, not_4_out, not_5_out, not_6_out, not_7_out,
       not_8_out, not_9_out, not_10_out, not_11_out, xor_1_out, xor_2_out, xor_3_out, xor_4_out, xor_5_out,
       xor_6_out;

  not not_1 (not_1_out, in_3);
  and and_1 (and_1_out, in_1, not_1_out);
  count_from_0 count_from_0_1 (
    .out_4(count_from_0_1_out_4), .out_5(count_from_0_1_out_5), .out_6(count_from_0_1_out_6), .start(in_1),
    .clock(in_3), .zer0(MBR_output));
  xor xor_1 (xor_1_out, 1'b0, count_from_0_1_out_6);
  not not_2 (not_2_out, xor_1_out);
  and and_2 (MBR_input, and_1_out, input_output);
  not not_3 (not_3_out, 1'b0);
  xor xor_2 (xor_2_out, not_3_out, count_from_0_1_out_4);
  xor xor_3 (xor_3_out, 1'b0, count_from_0_1_out_5);
  not not_4 (not_4_out, xor_3_out);
  not not_5 (not_5_out, xor_2_out);
  and and_3 (input_output, not_2_out, not_4_out, not_5_out);
  not not_6 (not_6_out, in_2);
  and and_4 (and_4_out, not_6_out, 1'b1);
  and and_5 (and_5_out, in_2, 1'b1);
  and and_6 (and_6_out, and_4_out, MBR_output);
  xor xor_4 (xor_4_out, 1'b0, count_from_0_1_out_6);
  not not_7 (not_7_out, xor_4_out);
  and and_7 (R1_input, and_6_out, and_1_out);
  not not_8 (not_8_out, 1'b0);
  xor xor_5 (xor_5_out, not_8_out, count_from_0_1_out_5);
  not not_9 (not_9_out, xor_5_out);
  and and_8 (MBR_output, not_7_out, not_9_out, not_10_out);
  and and_9 (R2_input, and_1_out, and_10_out);
  xor xor_6 (xor_6_out, 1'b0, count_from_0_1_out_4);
  not not_10 (not_10_out, xor_6_out);
  and and_10 (and_10_out, MBR_output, and_5_out);
  not not_11 (not_11_out, input_output);
  and and_11 (MBR_r_c, not_11_out, in_1);

  assign out_4 = MBR_output;
  assign out_5 = in_1;

  // Notes on the sheet:
  //   Instruction for getting the value in the keypad buffer
endmodule

module switch_choose (
  input  in_1,
  input  in_2,
  input  in_3,
  input  in_4,
  input  in_5,
  input  in_6,
  input  in_7,
  output out_8
);

  wire or_1_out, or_2_out, or_4_out, or_5_out, or_6_out;

  or or_1 (or_1_out, in_2, in_3);
  or or_2 (or_2_out, or_1_out, or_5_out);
  or or_3 (out_8, or_2_out, in_1);
  or or_4 (or_4_out, in_4, in_5);
  or or_5 (or_5_out, or_6_out, in_7);
  or or_6 (or_6_out, or_4_out, in_6);

  // Notes on the sheet:
  //   multiple or gate
endmodule

module load_from_ram (
  input  in_1,
  input  in_2,
  input  in_3,
  input  in_4,
  input  in_5,
  input  in_6,
  input  in_7,
  output out_8,
  output out_9,
  output out_10,
  output out_11,
  output out_12,
  output out_13,
  output MAR_input,
  output out_15,
  output MAR_output,
  output MBR_input,
  output MBR_ouput,
  output AR_input,
  output MBR_r_c,
  output ram_r,
  output R1_output,
  output output_ram,
  output R2_ouput,
  output DR_input
);

  wire and_1_out, and_3_out, and_5_out, and_6_out, and_8_out, and_10_out, and_14_out, and_17_out,
       count_from_0_1_out_4, count_from_0_1_out_5, count_from_0_1_out_6, not_1_out, not_2_out, not_3_out,
       not_4_out, not_5_out, not_6_out, not_7_out, not_8_out, not_9_out, not_10_out, not_11_out, not_12_out,
       not_13_out, not_14_out, not_15_out, not_16_out, not_17_out, not_18_out, not_19_out, not_20_out,
       not_21_out, not_22_out, not_23_out, not_24_out, xor_1_out, xor_2_out, xor_3_out, xor_4_out, xor_5_out,
       xor_6_out, xor_7_out, xor_8_out, xor_9_out, xor_10_out, xor_11_out, xor_12_out, xor_13_out,
       xor_14_out, xor_15_out;

  not not_1 (not_1_out, in_7);
  count_from_0 count_from_0_1 (
    .out_4(count_from_0_1_out_4), .out_5(count_from_0_1_out_5), .out_6(count_from_0_1_out_6), .start(in_2),
    .clock(in_7), .zer0(out_8));
  and and_1 (and_1_out, in_2, not_1_out);
  and and_2 (MAR_input, and_1_out, out_15);
  xor xor_1 (xor_1_out, count_from_0_1_out_6, 1'b0);
  not not_2 (not_2_out, xor_1_out);
  and and_3 (and_3_out, not_2_out, not_4_out);
  not not_3 (not_3_out, 1'b0);
  xor xor_2 (xor_2_out, count_from_0_1_out_5, 1'b0);
  xor xor_3 (xor_3_out, count_from_0_1_out_4, not_3_out);
  not not_4 (not_4_out, xor_2_out);
  not not_5 (not_5_out, xor_3_out);
  and and_4 (out_15, and_3_out, not_5_out);
  not not_6 (not_6_out, in_1);
  and and_5 (and_5_out, not_6_out, 1'b1);
  xor xor_4 (xor_4_out, count_from_0_1_out_6, 1'b0);
  xor xor_5 (xor_5_out, count_from_0_1_out_5, not_9_out);
  not not_7 (not_7_out, xor_5_out);
  not not_8 (not_8_out, xor_4_out);
  and and_6 (and_6_out, not_8_out, not_7_out);
  and and_7 (MBR_input, and_1_out, MBR_r_c);
  and and_8 (and_8_out, in_1, 1'b1);
  not not_9 (not_9_out, 1'b0);
  xor xor_6 (xor_6_out, count_from_0_1_out_4, 1'b0);
  not not_10 (not_10_out, xor_6_out);
  and and_9 (MAR_output, and_6_out, not_10_out);
  not not_11 (not_11_out, 1'b0);
  xor xor_7 (xor_7_out, count_from_0_1_out_5, not_11_out);
  xor xor_8 (xor_8_out, count_from_0_1_out_6, 1'b0);
  not not_12 (not_12_out, xor_7_out);
  not not_13 (not_13_out, xor_8_out);
  and and_10 (and_10_out, not_13_out, not_12_out);
  and and_11 (AR_input, and_1_out, MAR_output);
  not not_14 (not_14_out, 1'b0);
  xor xor_9 (xor_9_out, count_from_0_1_out_4, not_14_out);
  not not_15 (not_15_out, xor_9_out);
  and and_12 (MBR_r_c, and_10_out, not_15_out);
  and and_13 (R1_output, and_5_out, MBR_r_c);
  not not_16 (not_16_out, 1'b0);
  xor xor_10 (xor_10_out, count_from_0_1_out_6, not_16_out);
  not not_17 (not_17_out, xor_10_out);
  and and_14 (and_14_out, not_17_out, not_18_out);
  or or_1 (output_ram, MAR_output, MBR_ouput);
  xor xor_11 (xor_11_out, count_from_0_1_out_4, 1'b0);
  xor xor_12 (xor_12_out, count_from_0_1_out_5, 1'b0);
  not not_18 (not_18_out, xor_12_out);
  not not_19 (not_19_out, xor_11_out);
  and and_15 (MBR_ouput, and_14_out, not_19_out);
  and and_16 (R2_ouput, MBR_r_c, and_8_out);
  not not_20 (not_20_out, 1'b0);
  xor xor_13 (xor_13_out, count_from_0_1_out_6, not_20_out);
  not not_21 (not_21_out, xor_13_out);
  and and_17 (and_17_out, not_21_out, not_24_out);
  and and_18 (DR_input, MBR_ouput, and_1_out);
  not not_22 (not_22_out, 1'b0);
  xor xor_14 (xor_14_out, count_from_0_1_out_4, not_22_out);
  xor xor_15 (xor_15_out, count_from_0_1_out_5, 1'b0);
  not not_23 (not_23_out, xor_14_out);
  not not_24 (not_24_out, xor_15_out);
  and and_19 (out_8, and_17_out, not_23_out);
  and and_20 (out_11, out_15, in_4);
  and and_21 (out_10, out_15, in_3);
  and and_22 (out_12, out_15, in_5);
  and and_23 (out_13, out_15, in_6);

  assign out_9 = in_2;
  assign ram_r = out_8;

  // Notes on the sheet:
  //   Should be called store into RAM
  //   Instruction for saving a reg value into RAM
  //   MAR r/c
endmodule

module Status_Register (
  input  in_1,
  input  in_2,
  input  in_3,
  input  in_4,
  input  in_5,
  output out_6,
  output out_7,
  output out_8
);

  D_Flip_Flop d_ff_1 (.clk(in_1), .D(in_2), .Q(out_6), .reset(in_5));  // open: Qn, preset, en
  D_Flip_Flop d_ff_2 (.clk(in_1), .D(in_3), .Q(out_7), .reset(in_5));  // open: Qn, preset, en
  D_Flip_Flop d_ff_3 (.clk(in_1), .D(in_4), .Q(out_8), .reset(in_5));  // open: Qn, preset, en
endmodule

module multiple_or_2 (
  input  in_1,
  input  in_2,
  input  in_3,
  input  in_4,
  input  in_5,
  output out_6
);

  wire or_2_out, or_3_out, or_4_out;

  or or_1 (out_6, or_3_out, in_1);
  or or_2 (or_2_out, in_3, in_2);
  or or_3 (or_3_out, or_2_out, or_4_out);
  or or_4 (or_4_out, in_4, in_5);

  // Notes on the sheet:
  //   5 input or
endmodule

module ram_output (
  input  in_1,
  input  in_2,
  input  in_3,
  input  in_4,
  input  in_5,
  input  in_6,
  input  in_7,
  input  in_8,
  input  in_9,
  output out_10,
  output out_11,
  output out_12,
  output out_13,
  output out_14,
  output out_15,
  output out_16,
  output out_17
);

  and and_1 (out_10, in_2, in_1);
  and and_2 (out_11, in_3, in_1);
  and and_3 (out_12, in_4, in_1);
  and and_4 (out_13, in_5, in_1);
  and and_5 (out_14, in_6, in_1);
  and and_6 (out_15, in_7, in_1);
  and and_7 (out_16, in_8, in_1);
  and and_8 (out_17, in_1, in_9);
endmodule

module actual__load_from_ram (
  input  in_1,
  input  in_2,
  input  in_3,
  input  in_4,
  input  in_5,
  input  in_6,
  input  in_7,
  output out_8,
  output out_9,
  output out_10,
  output out_11,
  output out_12,
  output out_13,
  output MAR_input,
  output out_15,
  output output_ram,
  output MAR_output,
  output AR_input,
  output MBR_input,
  output output_from_RAM,
  output R1_input,
  output R2_input,
  output MBR_output
);

  wire and_1_out, and_2_out, and_5_out, and_6_out, and_7_out, and_11_out, and_14_out, and_15_out, and_17_out,
       count_from_0_1_out_4, count_from_0_1_out_5, count_from_0_1_out_6, not_1_out, not_2_out, not_3_out,
       not_4_out, not_5_out, not_6_out, not_7_out, not_8_out, not_9_out, not_10_out, not_11_out, not_12_out,
       not_13_out, not_14_out, not_15_out, not_16_out, not_17_out, not_18_out, not_19_out, xor_1_out,
       xor_2_out, xor_3_out, xor_4_out, xor_5_out, xor_6_out, xor_7_out, xor_8_out, xor_9_out, xor_10_out,
       xor_11_out, xor_12_out;

  not not_1 (not_1_out, in_7);
  count_from_0 count_from_0_1 (
    .out_4(count_from_0_1_out_4), .out_5(count_from_0_1_out_5), .out_6(count_from_0_1_out_6), .start(in_6),
    .clock(in_7), .zer0(MBR_output));
  and and_1 (and_1_out, in_6, not_1_out);
  xor xor_1 (xor_1_out, count_from_0_1_out_6, 1'b0);
  not not_2 (not_2_out, xor_1_out);
  and and_2 (and_2_out, not_2_out, not_4_out);
  and and_3 (MAR_input, and_1_out, out_15);
  not not_3 (not_3_out, 1'b0);
  xor xor_2 (xor_2_out, count_from_0_1_out_5, 1'b0);
  xor xor_3 (xor_3_out, count_from_0_1_out_4, not_3_out);
  not not_4 (not_4_out, xor_2_out);
  not not_5 (not_5_out, xor_3_out);
  and and_4 (out_15, and_2_out, not_5_out);
  not not_6 (not_6_out, in_1);
  and and_5 (and_5_out, not_6_out, 1'b1);
  xor xor_4 (xor_4_out, count_from_0_1_out_6, 1'b0);
  not not_7 (not_7_out, xor_4_out);
  and and_6 (and_6_out, not_7_out, not_10_out);
  and and_7 (and_7_out, in_1, 1'b1);
  not not_8 (not_8_out, 1'b0);
  xor xor_5 (xor_5_out, count_from_0_1_out_5, not_8_out);
  xor xor_6 (xor_6_out, count_from_0_1_out_4, 1'b0);
  not not_9 (not_9_out, xor_6_out);
  not not_10 (not_10_out, xor_5_out);
  and and_8 (MAR_output, and_6_out, not_9_out);
  and and_9 (AR_input, and_1_out, MAR_output);
  and and_10 (MBR_input, and_1_out, output_from_RAM);
  not not_11 (not_11_out, 1'b0);
  xor xor_7 (xor_7_out, count_from_0_1_out_6, not_11_out);
  xor xor_8 (xor_8_out, count_from_0_1_out_5, 1'b0);
  not not_12 (not_12_out, xor_8_out);
  not not_13 (not_13_out, xor_7_out);
  and and_11 (and_11_out, not_13_out, not_12_out);
  xor xor_9 (xor_9_out, count_from_0_1_out_4, 1'b0);
  not not_14 (not_14_out, xor_9_out);
  and and_12 (output_from_RAM, and_11_out, not_14_out);
  and and_13 (R1_input, and_1_out, and_14_out);
  and and_14 (and_14_out, and_5_out, MBR_output);
  and and_15 (and_15_out, MBR_output, and_7_out);
  and and_16 (R2_input, and_1_out, and_15_out);
  not not_15 (not_15_out, 1'b0);
  xor xor_10 (xor_10_out, count_from_0_1_out_6, not_15_out);
  not not_16 (not_16_out, xor_10_out);
  and and_17 (and_17_out, not_16_out, not_19_out);
  not not_17 (not_17_out, 1'b0);
  xor xor_11 (xor_11_out, count_from_0_1_out_5, 1'b0);
  xor xor_12 (xor_12_out, count_from_0_1_out_4, not_17_out);
  not not_18 (not_18_out, xor_12_out);
  not not_19 (not_19_out, xor_11_out);
  and and_18 (MBR_output, and_17_out, not_18_out);
  and and_19 (out_10, out_15, in_2);
  and and_20 (out_11, out_15, in_3);
  and and_21 (out_12, out_15, in_4);
  and and_22 (out_13, out_15, in_5);

  assign out_8 = MBR_output;
  assign out_9 = in_6;
  assign output_ram = MAR_output;

  // Notes on the sheet:
  //   Instruction for loading a value from RAM into a reg
  //   MAR r/c
endmodule

module either (
  input  in_1,
  input  in_2,
  input  in_3,
  input  in_4,
  input  in_5,
  input  in_6,
  input  in_7,
  input  in_8,
  output out_9,
  output out_10,
  output out_11,
  output out_12
);

  or or_1 (out_9, in_1, in_5);
  or or_2 (out_10, in_2, in_6);
  or or_3 (out_11, in_3, in_7);
  or or_4 (out_12, in_4, in_8);
endmodule

module _3_or (
  input  in_1,
  input  in_2,
  input  in_3,
  output out_4
);

  wire or_2_out;

  or or_1 (out_4, or_2_out, in_3);
  or or_2 (or_2_out, in_1, in_2);
endmodule

module get_next_instruction (
  input  in_1,
  input  in_2,
  output out_3,
  output out_4,
  output MAR_input,
  output PC_output,
  output MAR_r_c,
  output AR_input,
  output MAR_output,
  output RAM_output,
  output output_from_RAM,
  output MBR_input,
  output MBR_output,
  output IR_input
);

  wire and_1_out, and_3_out, and_5_out, and_8_out, and_10_out, and_13_out, count_from_0_1_out_4,
       count_from_0_1_out_5, count_from_0_1_out_6, not_1_out, not_2_out, not_3_out, not_4_out, not_5_out,
       not_6_out, not_7_out, not_8_out, not_9_out, not_10_out, not_11_out, not_12_out, not_13_out,
       not_14_out, not_15_out, not_16_out, not_17_out, not_18_out, not_19_out, not_20_out, not_21_out,
       not_22_out, not_23_out, xor_1_out, xor_2_out, xor_3_out, xor_4_out, xor_5_out, xor_6_out, xor_7_out,
       xor_8_out, xor_9_out, xor_10_out, xor_11_out, xor_12_out, xor_13_out, xor_14_out, xor_15_out;

  not not_1 (not_1_out, in_2);
  count_from_0 count_from_0_1 (
    .out_4(count_from_0_1_out_4), .out_5(count_from_0_1_out_5), .out_6(count_from_0_1_out_6), .start(in_1),
    .clock(in_2), .zer0(out_3));
  and and_1 (and_1_out, in_1, not_1_out);
  xor xor_1 (xor_1_out, count_from_0_1_out_6, 1'b0);
  not not_2 (not_2_out, xor_1_out);
  and and_2 (MAR_input, MAR_r_c, and_1_out);
  xor xor_2 (xor_2_out, count_from_0_1_out_5, 1'b0);
  not not_3 (not_3_out, xor_2_out);
  and and_3 (and_3_out, not_2_out, not_3_out);
  and and_4 (MAR_r_c, and_3_out, not_5_out);
  not not_4 (not_4_out, 1'b0);
  xor xor_3 (xor_3_out, count_from_0_1_out_4, not_4_out);
  not not_5 (not_5_out, xor_3_out);
  xor xor_4 (xor_4_out, count_from_0_1_out_5, not_8_out);
  xor xor_5 (xor_5_out, count_from_0_1_out_6, 1'b0);
  not not_6 (not_6_out, xor_5_out);
  not not_7 (not_7_out, xor_4_out);
  and and_5 (and_5_out, not_6_out, not_7_out);
  not not_8 (not_8_out, 1'b0);
  xor xor_6 (xor_6_out, count_from_0_1_out_4, 1'b0);
  not not_9 (not_9_out, xor_6_out);
  and and_6 (MAR_output, and_5_out, not_9_out);
  buf and_7 (AR_input, MAR_output);  // AND_Gate
  xor xor_7 (xor_7_out, count_from_0_1_out_6, not_11_out);
  not not_10 (not_10_out, xor_7_out);
  not not_11 (not_11_out, 1'b0);
  xor xor_8 (xor_8_out, count_from_0_1_out_5, 1'b0);
  not not_12 (not_12_out, xor_8_out);
  and and_8 (and_8_out, not_10_out, not_12_out);
  xor xor_9 (xor_9_out, count_from_0_1_out_4, 1'b0);
  not not_13 (not_13_out, xor_9_out);
  and and_9 (out_4, and_8_out, not_13_out);
  not not_14 (not_14_out, 1'b0);
  xor xor_10 (xor_10_out, count_from_0_1_out_6, not_14_out);
  not not_15 (not_15_out, xor_10_out);
  and and_10 (and_10_out, not_15_out, not_17_out);
  not not_16 (not_16_out, 1'b0);
  xor xor_11 (xor_11_out, count_from_0_1_out_5, 1'b0);
  xor xor_12 (xor_12_out, count_from_0_1_out_4, not_16_out);
  not not_17 (not_17_out, xor_11_out);
  not not_18 (not_18_out, xor_12_out);
  and and_11 (MBR_output, and_10_out, not_18_out);
  and and_12 (MBR_input, and_1_out, out_4);
  not not_19 (not_19_out, 1'b0);
  xor xor_13 (xor_13_out, count_from_0_1_out_6, not_19_out);
  not not_20 (not_20_out, xor_13_out);
  not not_21 (not_21_out, 1'b0);
  xor xor_14 (xor_14_out, count_from_0_1_out_5, not_21_out);
  not not_22 (not_22_out, xor_14_out);
  and and_13 (and_13_out, not_20_out, not_22_out);
  and and_14 (out_3, and_13_out, not_23_out);
  and and_15 (IR_input, and_1_out, MBR_output);
  xor xor_15 (xor_15_out, count_from_0_1_out_4, 1'b0);
  not not_23 (not_23_out, xor_15_out);

  assign output_from_RAM = out_4;
  assign PC_output = MAR_r_c;
  assign RAM_output = MAR_output;

  // Notes on the sheet:
  //   Loads inst at PC into the IR
endmodule

module number_to_display (
  input  in_1,
  input  in_2,
  input  in_3,
  input  in_4,
  output out_5,
  output out_6,
  output out_7,
  output out_8,
  output out_9,
  output out_10,
  output out_11,
  output out_12
);

  wire and_1_out, and_2_out, and_3_out, and_4_out, and_5_out, and_6_out, and_7_out, and_8_out, and_9_out,
       and_10_out, and_11_out, and_12_out, and_13_out, and_14_out, and_15_out, and_16_out, and_17_out,
       and_18_out, and_19_out, and_20_out, and_21_out, and_22_out, and_23_out, and_24_out, and_25_out,
       and_26_out, and_27_out, and_28_out, and_29_out, and_30_out, not_1_out, not_2_out, not_3_out,
       not_4_out, not_5_out, not_6_out, not_7_out, not_8_out, not_9_out, not_10_out, not_11_out, not_12_out,
       not_13_out, not_14_out, not_15_out, not_16_out, not_17_out, not_18_out, not_19_out, not_20_out,
       not_21_out, not_22_out, not_23_out, not_24_out, not_25_out;

  not not_1 (not_1_out, in_1);
  _10_or u_10_or_1 (
    .out_11(out_5), .in_1(and_7_out), .in_2(and_10_out), .in_3(and_13_out), .in_4(and_16_out),
    .in_5(and_28_out), .in_6(and_19_out), .in_7(and_25_out), .in_8(1'b0), .in_9(1'b0), .in_10(1'b0));
  and and_1 (and_1_out, and_2_out, and_3_out);
  and and_2 (and_2_out, not_1_out, not_3_out);
  not not_2 (not_2_out, in_3);
  not not_3 (not_3_out, in_2);
  and and_3 (and_3_out, not_2_out, not_4_out);
  not not_4 (not_4_out, in_4);
  not not_5 (not_5_out, in_1);
  _10_or u_10_or_2 (
    .out_11(out_6), .in_1(and_1_out), .in_2(and_13_out), .in_3(and_16_out), .in_4(and_25_out),
    .in_5(and_19_out), .in_6(and_28_out), .in_7(1'b0), .in_8(1'b0), .in_9(1'b0), .in_10(1'b0));
  and and_4 (and_4_out, and_5_out, and_6_out);
  and and_5 (and_5_out, not_5_out, not_6_out);
  not not_6 (not_6_out, in_2);
  not not_7 (not_7_out, in_3);
  and and_6 (and_6_out, not_7_out, in_4);
  not not_8 (not_8_out, in_1);
  _10_or u_10_or_3 (
    .out_11(out_7), .in_1(and_1_out), .in_2(and_16_out), .in_3(and_7_out), .in_4(and_10_out),
    .in_5(and_19_out), .in_6(and_22_out), .in_7(and_25_out), .in_8(and_28_out), .in_9(1'b0), .in_10(1'b0));
  and and_7 (and_7_out, and_8_out, and_9_out);
  and and_8 (and_8_out, not_8_out, not_9_out);
  not not_9 (not_9_out, in_2);
  and and_9 (and_9_out, in_3, not_11_out);
  not not_10 (not_10_out, in_1);
  not not_11 (not_11_out, in_4);
  _10_or u_10_or_4 (
    .out_11(out_8), .in_1(and_1_out), .in_2(and_4_out), .in_3(and_7_out), .in_4(and_10_out),
    .in_5(and_13_out), .in_6(and_22_out), .in_7(and_25_out), .in_8(and_28_out), .in_9(1'b0), .in_10(1'b0));
  and and_10 (and_10_out, and_11_out, and_12_out);
  and and_11 (and_11_out, not_10_out, not_12_out);
  not not_12 (not_12_out, in_2);
  and and_12 (and_12_out, in_3, in_4);
  not not_13 (not_13_out, in_1);
  _10_or u_10_or_5 (
    .out_11(out_9), .in_1(and_1_out), .in_2(and_7_out), .in_3(and_19_out), .in_4(and_25_out), .in_5(1'b0),
    .in_6(1'b0), .in_7(1'b0), .in_8(1'b0), .in_9(1'b0), .in_10(1'b0));
  and and_13 (and_13_out, and_14_out, and_15_out);
  and and_14 (and_14_out, not_13_out, in_2);
  not not_14 (not_14_out, in_3);
  and and_15 (and_15_out, not_14_out, not_16_out);
  not not_15 (not_15_out, in_1);
  not not_16 (not_16_out, in_4);
  _10_or u_10_or_6 (
    .out_11(out_10), .in_1(and_1_out), .in_2(and_7_out), .in_3(and_10_out), .in_4(and_16_out),
    .in_5(and_25_out), .in_6(and_19_out), .in_7(and_28_out), .in_8(1'b0), .in_9(1'b0), .in_10(1'b0));
  and and_16 (and_16_out, and_17_out, and_18_out);
  and and_17 (and_17_out, not_15_out, in_2);
  not not_17 (not_17_out, in_3);
  and and_18 (and_18_out, not_17_out, in_4);
  not not_18 (not_18_out, in_1);
  _10_or u_10_or_7 (
    .out_11(out_11), .in_1(and_1_out), .in_2(and_4_out), .in_3(and_10_out), .in_4(and_13_out),
    .in_5(and_16_out), .in_6(and_19_out), .in_7(and_22_out), .in_8(and_25_out), .in_9(and_28_out),
    .in_10(1'b0));
  and and_19 (and_19_out, and_20_out, and_21_out);
  and and_20 (and_20_out, not_18_out, in_2);
  and and_21 (and_21_out, in_3, not_20_out);
  not not_19 (not_19_out, in_1);
  not not_20 (not_20_out, in_4);
  and and_22 (and_22_out, and_23_out, and_24_out);
  and and_23 (and_23_out, not_19_out, in_2);
  and and_24 (and_24_out, in_3, in_4);
  and and_25 (and_25_out, and_26_out, and_27_out);
  and and_26 (and_26_out, in_1, not_22_out);
  not not_21 (not_21_out, in_3);
  not not_22 (not_22_out, in_2);
  and and_27 (and_27_out, not_21_out, not_23_out);
  not not_23 (not_23_out, in_4);
  and and_28 (and_28_out, and_29_out, and_30_out);
  and and_29 (and_29_out, in_1, not_24_out);
  not not_24 (not_24_out, in_2);
  not not_25 (not_25_out, in_3);
  and and_30 (and_30_out, not_25_out, in_4);

  assign out_12 = 1'b0;

  // Notes on the sheet:
  //   turns a 4 bit binary number into the correct number on a 7 segment digit dislpay
endmodule

module _10_or (
  input  in_1,
  input  in_2,
  input  in_3,
  input  in_4,
  input  in_5,
  input  in_6,
  input  in_7,
  input  in_8,
  input  in_9,
  input  in_10,
  output out_11
);

  wire or_1_out, or_2_out, or_3_out, or_4_out, or_5_out, or_7_out, or_8_out, or_9_out;

  or or_1 (or_1_out, in_1, in_2);
  or or_2 (or_2_out, or_3_out, or_7_out);
  or or_3 (or_3_out, or_1_out, or_4_out);
  or or_4 (or_4_out, in_3, in_4);
  or or_5 (or_5_out, in_5, in_6);
  or or_6 (out_11, or_2_out, or_9_out);
  or or_7 (or_7_out, or_5_out, or_8_out);
  or or_8 (or_8_out, in_7, in_8);
  or or_9 (or_9_out, in_9, in_10);
endmodule

module number_to_digits (
  input  in_1,
  input  in_2,
  input  in_3,
  input  in_4,
  input  in_5,
  input  in_6,
  input  in_7,
  input  in_8,
  output out_9,
  output out_10,
  output out_11,
  output out_12,
  output out_13,
  output out_14,
  output out_15,
  output out_16,
  output out_17,
  output out_18,
  output out_19,
  output out_20
);

  wire shift_and_add_2_out_21, shift_and_add_2_out_22, shift_and_add_2_out_23, shift_and_add_2_out_24,
       shift_and_add_2_out_25, shift_and_add_2_out_26, shift_and_add_2_out_27, shift_and_add_2_out_28,
       shift_and_add_2_out_29, shift_and_add_2_out_30, shift_and_add_2_out_31, shift_and_add_2_out_32,
       shift_and_add_2_out_33, shift_and_add_2_out_34, shift_and_add_2_out_35, shift_and_add_2_out_36,
       shift_and_add_2_out_37, shift_and_add_2_out_38, shift_and_add_2_out_39, shift_and_add_2_out_40,
       shift_and_add_3_out_21, shift_and_add_3_out_22, shift_and_add_3_out_23, shift_and_add_3_out_24,
       shift_and_add_3_out_25, shift_and_add_3_out_26, shift_and_add_3_out_27, shift_and_add_3_out_28,
       shift_and_add_3_out_29, shift_and_add_3_out_30, shift_and_add_3_out_31, shift_and_add_3_out_32,
       shift_and_add_3_out_33, shift_and_add_3_out_34, shift_and_add_3_out_35, shift_and_add_3_out_36,
       shift_and_add_3_out_37, shift_and_add_3_out_38, shift_and_add_3_out_39, shift_and_add_3_out_40,
       shift_and_add_4_out_21, shift_and_add_4_out_22, shift_and_add_4_out_23, shift_and_add_4_out_24,
       shift_and_add_4_out_25, shift_and_add_4_out_26, shift_and_add_4_out_27, shift_and_add_4_out_28,
       shift_and_add_4_out_29, shift_and_add_4_out_30, shift_and_add_4_out_31, shift_and_add_4_out_32,
       shift_and_add_4_out_33, shift_and_add_4_out_34, shift_and_add_4_out_35, shift_and_add_4_out_36,
       shift_and_add_4_out_37, shift_and_add_4_out_38, shift_and_add_4_out_39, shift_and_add_4_out_40,
       shift_and_add_5_out_21, shift_and_add_5_out_22, shift_and_add_5_out_23, shift_and_add_5_out_24,
       shift_and_add_5_out_25, shift_and_add_5_out_26, shift_and_add_5_out_27, shift_and_add_5_out_28,
       shift_and_add_5_out_29, shift_and_add_5_out_30, shift_and_add_5_out_31, shift_and_add_5_out_32,
       shift_and_add_5_out_33, shift_and_add_5_out_34, shift_and_add_5_out_35, shift_and_add_5_out_36,
       shift_and_add_5_out_37, shift_and_add_5_out_38, shift_and_add_5_out_39, shift_and_add_5_out_40,
       shift_and_add_6_out_21, shift_and_add_6_out_22, shift_and_add_6_out_23, shift_and_add_6_out_24,
       shift_and_add_6_out_25, shift_and_add_6_out_26, shift_and_add_6_out_27, shift_and_add_6_out_28,
       shift_and_add_6_out_29, shift_and_add_6_out_30, shift_and_add_6_out_31, shift_and_add_6_out_32,
       shift_and_add_6_out_33, shift_and_add_6_out_34, shift_and_add_6_out_35, shift_and_add_6_out_36,
       shift_and_add_6_out_37, shift_and_add_6_out_38, shift_and_add_6_out_39, shift_and_add_6_out_40,
       shift_and_add_7_out_21, shift_and_add_7_out_22, shift_and_add_7_out_23, shift_and_add_7_out_24,
       shift_and_add_7_out_25, shift_and_add_7_out_26, shift_and_add_7_out_27, shift_and_add_7_out_28,
       shift_and_add_7_out_29, shift_and_add_7_out_30, shift_and_add_7_out_31, shift_and_add_7_out_32,
       shift_and_add_7_out_33, shift_and_add_7_out_34, shift_and_add_7_out_35, shift_and_add_7_out_36,
       shift_and_add_7_out_37, shift_and_add_7_out_38, shift_and_add_7_out_39, shift_and_add_7_out_40,
       shift_and_add_8_out_21, shift_and_add_8_out_22, shift_and_add_8_out_23, shift_and_add_8_out_24,
       shift_and_add_8_out_25, shift_and_add_8_out_26, shift_and_add_8_out_27, shift_and_add_8_out_28,
       shift_and_add_8_out_29, shift_and_add_8_out_30, shift_and_add_8_out_31, shift_and_add_8_out_32,
       shift_and_add_8_out_33, shift_and_add_8_out_34, shift_and_add_8_out_35, shift_and_add_8_out_36,
       shift_and_add_8_out_37, shift_and_add_8_out_38, shift_and_add_8_out_39, shift_and_add_8_out_40;

  shift_and_add shift_and_add_1 (
    .out_22(out_10), .out_23(out_11), .out_24(out_12), .out_25(out_13), .out_26(out_14), .out_27(out_15),
    .out_28(out_16), .out_29(out_17), .out_30(out_18), .out_31(out_19), .out_32(out_20),
    .in_2(shift_and_add_2_out_22), .in_3(shift_and_add_2_out_23), .in_4(shift_and_add_2_out_24),
    .in_5(shift_and_add_2_out_25), .in_6(shift_and_add_2_out_26), .in_7(shift_and_add_2_out_27),
    .in_8(shift_and_add_2_out_28), .in_9(shift_and_add_2_out_29), .in_10(shift_and_add_2_out_30),
    .in_11(shift_and_add_2_out_31), .in_13(shift_and_add_2_out_33), .in_14(shift_and_add_2_out_34),
    .in_15(shift_and_add_2_out_35), .in_16(shift_and_add_2_out_36), .in_17(shift_and_add_2_out_37),
    .in_18(shift_and_add_2_out_38), .in_19(shift_and_add_2_out_39), .in_20(shift_and_add_2_out_40),
    .in_1(shift_and_add_2_out_21), .out_21(out_9), .in_12(shift_and_add_2_out_32));  // open: out_33, out_34, out_35, out_36, out_37, out_38, out_39, out_40
  shift_and_add shift_and_add_2 (
    .out_22(shift_and_add_2_out_22), .out_23(shift_and_add_2_out_23), .out_24(shift_and_add_2_out_24),
    .out_25(shift_and_add_2_out_25), .out_26(shift_and_add_2_out_26), .out_27(shift_and_add_2_out_27),
    .out_28(shift_and_add_2_out_28), .out_29(shift_and_add_2_out_29), .out_30(shift_and_add_2_out_30),
    .out_31(shift_and_add_2_out_31), .out_32(shift_and_add_2_out_32), .out_33(shift_and_add_2_out_33),
    .out_34(shift_and_add_2_out_34), .out_35(shift_and_add_2_out_35), .out_36(shift_and_add_2_out_36),
    .out_37(shift_and_add_2_out_37), .out_38(shift_and_add_2_out_38), .out_39(shift_and_add_2_out_39),
    .out_40(shift_and_add_2_out_40), .in_2(shift_and_add_3_out_22), .in_3(shift_and_add_3_out_23),
    .in_4(shift_and_add_3_out_24), .in_5(shift_and_add_3_out_25), .in_6(shift_and_add_3_out_26),
    .in_7(shift_and_add_3_out_27), .in_8(shift_and_add_3_out_28), .in_9(shift_and_add_3_out_29),
    .in_10(shift_and_add_3_out_30), .in_11(shift_and_add_3_out_31), .in_13(shift_and_add_3_out_33),
    .in_14(shift_and_add_3_out_34), .in_15(shift_and_add_3_out_35), .in_16(shift_and_add_3_out_36),
    .in_17(shift_and_add_3_out_37), .in_18(shift_and_add_3_out_38), .in_19(shift_and_add_3_out_39),
    .in_20(shift_and_add_3_out_40), .in_1(shift_and_add_3_out_21), .out_21(shift_and_add_2_out_21),
    .in_12(shift_and_add_3_out_32));
  shift_and_add shift_and_add_3 (
    .out_22(shift_and_add_3_out_22), .out_23(shift_and_add_3_out_23), .out_24(shift_and_add_3_out_24),
    .out_25(shift_and_add_3_out_25), .out_26(shift_and_add_3_out_26), .out_27(shift_and_add_3_out_27),
    .out_28(shift_and_add_3_out_28), .out_29(shift_and_add_3_out_29), .out_30(shift_and_add_3_out_30),
    .out_31(shift_and_add_3_out_31), .out_32(shift_and_add_3_out_32), .out_33(shift_and_add_3_out_33),
    .out_34(shift_and_add_3_out_34), .out_35(shift_and_add_3_out_35), .out_36(shift_and_add_3_out_36),
    .out_37(shift_and_add_3_out_37), .out_38(shift_and_add_3_out_38), .out_39(shift_and_add_3_out_39),
    .out_40(shift_and_add_3_out_40), .in_2(shift_and_add_4_out_22), .in_3(shift_and_add_4_out_23),
    .in_4(shift_and_add_4_out_24), .in_5(shift_and_add_4_out_25), .in_6(shift_and_add_4_out_26),
    .in_7(shift_and_add_4_out_27), .in_8(shift_and_add_4_out_28), .in_9(shift_and_add_4_out_29),
    .in_10(shift_and_add_4_out_30), .in_11(shift_and_add_4_out_31), .in_13(shift_and_add_4_out_33),
    .in_14(shift_and_add_4_out_34), .in_15(shift_and_add_4_out_35), .in_16(shift_and_add_4_out_36),
    .in_17(shift_and_add_4_out_37), .in_18(shift_and_add_4_out_38), .in_19(shift_and_add_4_out_39),
    .in_20(shift_and_add_4_out_40), .in_1(shift_and_add_4_out_21), .out_21(shift_and_add_3_out_21),
    .in_12(shift_and_add_4_out_32));
  shift_and_add shift_and_add_4 (
    .out_22(shift_and_add_4_out_22), .out_23(shift_and_add_4_out_23), .out_24(shift_and_add_4_out_24),
    .out_25(shift_and_add_4_out_25), .out_26(shift_and_add_4_out_26), .out_27(shift_and_add_4_out_27),
    .out_28(shift_and_add_4_out_28), .out_29(shift_and_add_4_out_29), .out_30(shift_and_add_4_out_30),
    .out_31(shift_and_add_4_out_31), .out_32(shift_and_add_4_out_32), .out_33(shift_and_add_4_out_33),
    .out_34(shift_and_add_4_out_34), .out_35(shift_and_add_4_out_35), .out_36(shift_and_add_4_out_36),
    .out_37(shift_and_add_4_out_37), .out_38(shift_and_add_4_out_38), .out_39(shift_and_add_4_out_39),
    .out_40(shift_and_add_4_out_40), .in_2(shift_and_add_5_out_22), .in_3(shift_and_add_5_out_23),
    .in_4(shift_and_add_5_out_24), .in_5(shift_and_add_5_out_25), .in_6(shift_and_add_5_out_26),
    .in_7(shift_and_add_5_out_27), .in_8(shift_and_add_5_out_28), .in_9(shift_and_add_5_out_29),
    .in_10(shift_and_add_5_out_30), .in_11(shift_and_add_5_out_31), .in_13(shift_and_add_5_out_33),
    .in_14(shift_and_add_5_out_34), .in_15(shift_and_add_5_out_35), .in_16(shift_and_add_5_out_36),
    .in_17(shift_and_add_5_out_37), .in_18(shift_and_add_5_out_38), .in_19(shift_and_add_5_out_39),
    .in_20(shift_and_add_5_out_40), .in_1(shift_and_add_5_out_21), .out_21(shift_and_add_4_out_21),
    .in_12(shift_and_add_5_out_32));
  shift_and_add shift_and_add_5 (
    .out_22(shift_and_add_5_out_22), .out_23(shift_and_add_5_out_23), .out_24(shift_and_add_5_out_24),
    .out_25(shift_and_add_5_out_25), .out_26(shift_and_add_5_out_26), .out_27(shift_and_add_5_out_27),
    .out_28(shift_and_add_5_out_28), .out_29(shift_and_add_5_out_29), .out_30(shift_and_add_5_out_30),
    .out_31(shift_and_add_5_out_31), .out_32(shift_and_add_5_out_32), .out_33(shift_and_add_5_out_33),
    .out_34(shift_and_add_5_out_34), .out_35(shift_and_add_5_out_35), .out_36(shift_and_add_5_out_36),
    .out_37(shift_and_add_5_out_37), .out_38(shift_and_add_5_out_38), .out_39(shift_and_add_5_out_39),
    .out_40(shift_and_add_5_out_40), .in_2(shift_and_add_6_out_22), .in_3(shift_and_add_6_out_23),
    .in_4(shift_and_add_6_out_24), .in_5(shift_and_add_6_out_25), .in_6(shift_and_add_6_out_26),
    .in_7(shift_and_add_6_out_27), .in_8(shift_and_add_6_out_28), .in_9(shift_and_add_6_out_29),
    .in_10(shift_and_add_6_out_30), .in_11(shift_and_add_6_out_31), .in_13(shift_and_add_6_out_33),
    .in_14(shift_and_add_6_out_34), .in_15(shift_and_add_6_out_35), .in_16(shift_and_add_6_out_36),
    .in_17(shift_and_add_6_out_37), .in_18(shift_and_add_6_out_38), .in_19(shift_and_add_6_out_39),
    .in_20(shift_and_add_6_out_40), .in_1(shift_and_add_6_out_21), .out_21(shift_and_add_5_out_21),
    .in_12(shift_and_add_6_out_32));
  shift_and_add shift_and_add_6 (
    .out_22(shift_and_add_6_out_22), .out_23(shift_and_add_6_out_23), .out_24(shift_and_add_6_out_24),
    .out_25(shift_and_add_6_out_25), .out_26(shift_and_add_6_out_26), .out_27(shift_and_add_6_out_27),
    .out_28(shift_and_add_6_out_28), .out_29(shift_and_add_6_out_29), .out_30(shift_and_add_6_out_30),
    .out_31(shift_and_add_6_out_31), .out_32(shift_and_add_6_out_32), .out_33(shift_and_add_6_out_33),
    .out_34(shift_and_add_6_out_34), .out_35(shift_and_add_6_out_35), .out_36(shift_and_add_6_out_36),
    .out_37(shift_and_add_6_out_37), .out_38(shift_and_add_6_out_38), .out_39(shift_and_add_6_out_39),
    .out_40(shift_and_add_6_out_40), .in_2(shift_and_add_7_out_22), .in_3(shift_and_add_7_out_23),
    .in_4(shift_and_add_7_out_24), .in_5(shift_and_add_7_out_25), .in_6(shift_and_add_7_out_26),
    .in_7(shift_and_add_7_out_27), .in_8(shift_and_add_7_out_28), .in_9(shift_and_add_7_out_29),
    .in_10(shift_and_add_7_out_30), .in_11(shift_and_add_7_out_31), .in_13(shift_and_add_7_out_33),
    .in_14(shift_and_add_7_out_34), .in_15(shift_and_add_7_out_35), .in_16(shift_and_add_7_out_36),
    .in_17(shift_and_add_7_out_37), .in_18(shift_and_add_7_out_38), .in_19(shift_and_add_7_out_39),
    .in_20(shift_and_add_7_out_40), .in_1(shift_and_add_7_out_21), .out_21(shift_and_add_6_out_21),
    .in_12(shift_and_add_7_out_32));
  shift_and_add shift_and_add_7 (
    .out_22(shift_and_add_7_out_22), .out_23(shift_and_add_7_out_23), .out_24(shift_and_add_7_out_24),
    .out_25(shift_and_add_7_out_25), .out_26(shift_and_add_7_out_26), .out_27(shift_and_add_7_out_27),
    .out_28(shift_and_add_7_out_28), .out_29(shift_and_add_7_out_29), .out_30(shift_and_add_7_out_30),
    .out_31(shift_and_add_7_out_31), .out_32(shift_and_add_7_out_32), .out_33(shift_and_add_7_out_33),
    .out_34(shift_and_add_7_out_34), .out_35(shift_and_add_7_out_35), .out_36(shift_and_add_7_out_36),
    .out_37(shift_and_add_7_out_37), .out_38(shift_and_add_7_out_38), .out_39(shift_and_add_7_out_39),
    .out_40(shift_and_add_7_out_40), .in_2(shift_and_add_8_out_22), .in_3(shift_and_add_8_out_23),
    .in_4(shift_and_add_8_out_24), .in_5(shift_and_add_8_out_25), .in_6(shift_and_add_8_out_26),
    .in_7(shift_and_add_8_out_27), .in_8(shift_and_add_8_out_28), .in_9(shift_and_add_8_out_29),
    .in_10(shift_and_add_8_out_30), .in_11(shift_and_add_8_out_31), .in_13(shift_and_add_8_out_33),
    .in_14(shift_and_add_8_out_34), .in_15(shift_and_add_8_out_35), .in_16(shift_and_add_8_out_36),
    .in_17(shift_and_add_8_out_37), .in_18(shift_and_add_8_out_38), .in_19(shift_and_add_8_out_39),
    .in_20(shift_and_add_8_out_40), .in_1(shift_and_add_8_out_21), .out_21(shift_and_add_7_out_21),
    .in_12(shift_and_add_8_out_32));
  shift_and_add shift_and_add_8 (
    .out_22(shift_and_add_8_out_22), .out_23(shift_and_add_8_out_23), .out_24(shift_and_add_8_out_24),
    .out_25(shift_and_add_8_out_25), .out_26(shift_and_add_8_out_26), .out_27(shift_and_add_8_out_27),
    .out_28(shift_and_add_8_out_28), .out_29(shift_and_add_8_out_29), .out_30(shift_and_add_8_out_30),
    .out_31(shift_and_add_8_out_31), .out_32(shift_and_add_8_out_32), .out_33(shift_and_add_8_out_33),
    .out_34(shift_and_add_8_out_34), .out_35(shift_and_add_8_out_35), .out_36(shift_and_add_8_out_36),
    .out_37(shift_and_add_8_out_37), .out_38(shift_and_add_8_out_38), .out_39(shift_and_add_8_out_39),
    .out_40(shift_and_add_8_out_40), .in_2(1'b0), .in_3(1'b0), .in_4(1'b0), .in_5(1'b0), .in_6(1'b0),
    .in_7(1'b0), .in_8(1'b0), .in_9(1'b0), .in_10(1'b0), .in_11(1'b0), .in_13(in_1), .in_14(in_2),
    .in_15(in_3), .in_16(in_4), .in_17(in_5), .in_18(in_6), .in_19(in_7), .in_20(in_8), .in_1(1'b0),
    .out_21(shift_and_add_8_out_21), .in_12(1'b0));

  // Notes on the sheet:
  //   converts binary to decimal using the double dabble algorithm
endmodule

module shift_and_add (
  input  in_1,
  input  in_2,
  input  in_3,
  input  in_4,
  input  in_5,
  input  in_6,
  input  in_7,
  input  in_8,
  input  in_9,
  input  in_10,
  input  in_11,
  input  in_12,
  input  in_13,
  input  in_14,
  input  in_15,
  input  in_16,
  input  in_17,
  input  in_18,
  input  in_19,
  input  in_20,
  output out_21,
  output out_22,
  output out_23,
  output out_24,
  output out_25,
  output out_26,
  output out_27,
  output out_28,
  output out_29,
  output out_30,
  output out_31,
  output out_32,
  output out_33,
  output out_34,
  output out_35,
  output out_36,
  output out_37,
  output out_38,
  output out_39,
  output out_40
);

  wire check_bigger_4_1_out_5, check_bigger_4_2_out_5, check_bigger_4_3_out_5;

  check_bigger_4 check_bigger_4_1 (.out_5(check_bigger_4_1_out_5), .in_1(in_1), .in_2(in_2), .in_3(in_3), .in_4(in_4));
  add_3 add_3_1 (
    .in_1(check_bigger_4_1_out_5), .out_7(out_21), .out_8(out_22), .out_9(out_23), .in_2(in_1), .in_3(in_2),
    .in_4(in_3), .in_5(in_4));  // open: out_6
  check_bigger_4 check_bigger_4_2 (.out_5(check_bigger_4_2_out_5), .in_1(in_5), .in_2(in_6), .in_3(in_7), .in_4(in_8));
  add_3 add_3_2 (
    .in_1(check_bigger_4_2_out_5), .out_6(out_24), .out_7(out_25), .out_8(out_26), .out_9(out_27),
    .in_2(in_5), .in_3(in_6), .in_4(in_7), .in_5(in_8));
  check_bigger_4 check_bigger_4_3 (
    .out_5(check_bigger_4_3_out_5), .in_1(in_9), .in_2(in_10), .in_3(in_11), .in_4(in_12));
  add_3 add_3_3 (
    .in_1(check_bigger_4_3_out_5), .out_6(out_28), .out_7(out_29), .out_8(out_30), .out_9(out_31),
    .in_2(in_9), .in_3(in_10), .in_4(in_11), .in_5(in_12));

  assign out_32 = in_13;
  assign out_33 = in_14;
  assign out_34 = in_15;
  assign out_35 = in_16;
  assign out_36 = in_17;
  assign out_37 = in_18;
  assign out_38 = in_19;
  assign out_39 = in_20;
  assign out_40 = 1'b0;
endmodule

module add_3 (
  input  in_1,
  input  in_2,
  input  in_3,
  input  in_4,
  input  in_5,
  output out_6,
  output out_7,
  output out_8,
  output out_9
);

  wire and_1_out, and_2_out, and_3_out, and_4_out, and_5_out, and_6_out, and_7_out, and_8_out,
       full_adder_1_out_4, full_adder_2_out_4, full_adder_2_out_5, full_adder_3_out_4, full_adder_3_out_5,
       half_adder_1_out_3, half_adder_1_out_4, not_1_out, not_2_out, not_3_out, not_4_out;

  and and_1 (and_1_out, in_2, not_1_out);
  not not_1 (not_1_out, in_1);
  and and_2 (and_2_out, in_3, not_2_out);
  not not_2 (not_2_out, in_1);
  or or_1 (out_6, and_1_out, and_5_out);
  and and_3 (and_3_out, in_4, not_3_out);
  not not_3 (not_3_out, in_1);
  or or_2 (out_7, and_2_out, and_6_out);
  and and_4 (and_4_out, in_5, not_4_out);
  not not_4 (not_4_out, in_1);
  or or_3 (out_8, and_3_out, and_7_out);
  or or_4 (out_9, and_4_out, and_8_out);
  and and_5 (and_5_out, full_adder_1_out_4, in_1);
  full_adder full_adder_1 (
    .in_1(1'b0), .in_2(full_adder_2_out_5), .in_3(in_2), .out_4(full_adder_1_out_4));  // open: out_5
  and and_6 (and_6_out, full_adder_2_out_4, in_1);
  full_adder full_adder_2 (
    .in_1(1'b0), .in_2(full_adder_3_out_5), .in_3(in_3), .out_4(full_adder_2_out_4),
    .out_5(full_adder_2_out_5));
  and and_7 (and_7_out, full_adder_3_out_4, in_1);
  full_adder full_adder_3 (
    .in_1(1'b1), .in_2(half_adder_1_out_4), .in_3(in_4), .out_4(full_adder_3_out_4),
    .out_5(full_adder_3_out_5));
  and and_8 (and_8_out, half_adder_1_out_3, in_1);
  half_adder half_adder_1 (.in_1(in_5), .in_2(1'b1), .out_3(half_adder_1_out_3), .out_4(half_adder_1_out_4));
endmodule

module full_adder (
  input  in_1,
  input  in_2,
  input  in_3,
  output out_4,
  output out_5
);

  wire and_1_out, and_2_out, xor_1_out;

  xor xor_1 (xor_1_out, in_1, in_2);
  and and_1 (and_1_out, xor_1_out, in_3);
  and and_2 (and_2_out, in_1, in_2);
  xor xor_2 (out_4, xor_1_out, in_3);
  or or_1 (out_5, and_1_out, and_2_out);
endmodule

module check_bigger_4 (
  input  in_1,
  input  in_2,
  input  in_3,
  input  in_4,
  output out_5
);

  wire and_1_out, or_2_out;

  or or_1 (out_5, in_1, and_1_out);
  and and_1 (and_1_out, in_2, or_2_out);
  or or_2 (or_2_out, in_3, in_4);
endmodule

module out_reg (
  input  in_1,
  input  in_2,
  input  in_3,
  input  in_4,
  input  in_5,
  input  in_6,
  input  in_7,
  input  in_8,
  input  in_9,
  input  in_10,
  input  in_11,
  output out_12,
  output out_13,
  output out_14,
  output out_15,
  output out_16,
  output out_17,
  output out_18,
  output out_19
);

  wire and_1_out;

  and and_1 (and_1_out, in_1, in_2);
  D_Flip_Flop d_ff_1 (.clk(and_1_out), .D(in_3), .Q(out_12), .reset(in_11));  // open: Qn, preset, en
  D_Flip_Flop d_ff_2 (.clk(and_1_out), .D(in_4), .Q(out_13), .reset(in_11));  // open: Qn, preset, en
  D_Flip_Flop d_ff_3 (.clk(and_1_out), .D(in_5), .Q(out_14), .reset(in_11));  // open: Qn, preset, en
  D_Flip_Flop d_ff_4 (.clk(and_1_out), .D(in_6), .Q(out_15), .reset(in_11));  // open: Qn, preset, en
  D_Flip_Flop d_ff_5 (.clk(and_1_out), .D(in_7), .Q(out_16), .reset(in_11));  // open: Qn, preset, en
  D_Flip_Flop d_ff_6 (.clk(and_1_out), .D(in_8), .Q(out_17), .reset(in_11));  // open: Qn, preset, en
  D_Flip_Flop d_ff_7 (.clk(and_1_out), .D(in_9), .Q(out_18), .reset(in_11));  // open: Qn, preset, en
  D_Flip_Flop d_ff_8 (.clk(and_1_out), .D(in_10), .Q(out_19), .reset(in_11));  // open: Qn, preset, en
endmodule

module display (
  input  in_1,
  input  in_2,
  input  in_3,
  output out_4,
  output out_5,
  output out_6,
  output out_7,
  output out_8,
  output out_9,
  output MBr_output,
  output out_11,
  output out_12
);

  wire and_1_out, and_2_out, and_6_out, and_8_out, and_10_out, count_from_0_1_out_4, count_from_0_1_out_5,
       count_from_0_1_out_6, not_1_out, not_2_out, not_3_out, not_4_out, not_5_out, not_6_out, not_7_out,
       not_8_out, not_9_out, not_10_out, xor_1_out, xor_2_out, xor_3_out, xor_4_out, xor_5_out, xor_6_out;

  not not_1 (not_1_out, in_3);
  count_from_0 count_from_0_1 (
    .out_4(count_from_0_1_out_4), .out_5(count_from_0_1_out_5), .out_6(count_from_0_1_out_6), .start(in_2),
    .clock(in_3), .zer0(MBr_output));
  and and_1 (and_1_out, in_2, not_1_out);
  xor xor_1 (xor_1_out, count_from_0_1_out_5, 1'b0);
  xor xor_2 (xor_2_out, count_from_0_1_out_6, 1'b0);
  not not_2 (not_2_out, xor_1_out);
  not not_3 (not_3_out, xor_2_out);
  and and_2 (and_2_out, not_3_out, not_2_out);
  and and_3 (out_9, and_2_out, not_5_out);
  and and_4 (out_6, and_6_out, out_9);
  not not_4 (not_4_out, 1'b0);
  xor xor_3 (xor_3_out, count_from_0_1_out_4, not_4_out);
  not not_5 (not_5_out, xor_3_out);
  and and_5 (out_7, and_10_out, out_9);
  not not_6 (not_6_out, in_1);
  and and_6 (and_6_out, not_6_out, 1'b1);
  and and_7 (out_8, and_1_out, out_9);
  xor xor_4 (xor_4_out, count_from_0_1_out_5, not_9_out);
  xor xor_5 (xor_5_out, count_from_0_1_out_6, 1'b0);
  not not_7 (not_7_out, xor_4_out);
  not not_8 (not_8_out, xor_5_out);
  and and_8 (and_8_out, not_8_out, not_7_out);
  and and_9 (MBr_output, and_8_out, not_10_out);
  not not_9 (not_9_out, 1'b0);
  xor xor_6 (xor_6_out, count_from_0_1_out_4, 1'b0);
  not not_10 (not_10_out, xor_6_out);
  and and_10 (and_10_out, in_1, 1'b1);
  and and_11 (out_11, and_1_out, MBr_output);

  assign out_4 = MBr_output;
  assign out_5 = in_2;
  assign out_12 = MBr_output;

  // Notes on the sheet:
  //   R1 output
  //   R2 output
  //   MBR input
  //   MBR r/c
  //   Display input
  //   instruction to display from reg
  //   output RAM?
endmodule

module _4_or (
  input  in_1,
  input  in_2,
  input  in_3,
  input  in_4,
  output out_5
);

  wire or_1_out, or_3_out;

  or or_1 (or_1_out, in_1, in_2);
  or or_2 (out_5, or_1_out, or_3_out);
  or or_3 (or_3_out, in_3, in_4);
endmodule

module PROGRAM_ROM (
  input  in_1,
  input  in_2,
  input  in_3,
  input  in_4,
  input  in_5,
  input  in_6,
  input  in_7,
  input  in_8,
  output out_9,
  output out_10,
  output out_11,
  output out_12,
  output out_13,
  output out_14,
  output out_15,
  output out_16,
  output out_17,
  output out_18,
  output out_19,
  output out_20,
  output out_21,
  output out_22,
  output out_23,
  output out_24,
  output out_25,
  output out_26,
  output out_27,
  output out_28,
  output out_29,
  output out_30,
  output out_31,
  output out_32,
  output out_33,
  output out_34,
  output out_35,
  output out_36,
  output out_37,
  output out_38,
  output out_39,
  output out_40,
  output out_41,
  output out_42,
  output out_43,
  output out_44,
  output out_45,
  output out_46,
  output out_47,
  output out_48,
  output out_49,
  output out_50,
  output out_51,
  output out_52,
  output out_53,
  output out_54,
  output out_55,
  output out_56,
  output out_57,
  output out_58,
  output out_59,
  output out_60,
  output out_61,
  output out_62,
  output out_63,
  output out_64,
  output out_65,
  output out_66,
  output out_67,
  output out_68,
  output out_69,
  output out_70,
  output out_71,
  output out_72,
  output out_73,
  output out_74,
  output out_75,
  output out_76,
  output out_77,
  output out_78,
  output out_79,
  output out_80,
  output out_81,
  output out_82,
  output out_83,
  output out_84,
  output out_85,
  output out_86,
  output out_87,
  output out_88,
  output out_89,
  output out_90,
  output out_91,
  output out_92,
  output out_93,
  output out_94,
  output out_95,
  output out_96,
  output out_97,
  output out_98,
  output out_99,
  output out_100,
  output out_101,
  output out_102,
  output out_103,
  output out_104,
  output out_105,
  output out_106,
  output out_107,
  output out_108,
  output out_109,
  output out_110,
  output out_111,
  output out_112,
  output out_113,
  output out_114,
  output out_115,
  output out_116,
  output out_117,
  output out_118,
  output out_119,
  output out_120,
  output out_121,
  output out_122,
  output out_123,
  output out_124,
  output out_125,
  output out_126,
  output out_127,
  output out_128,
  output out_129,
  output out_130,
  output out_131,
  output out_132,
  output out_133,
  output out_134,
  output out_135,
  output out_136
);

  not not_1 (out_9, 1'b0);
  not not_2 (out_25, 1'b0);
  not not_3 (out_41, 1'b0);
  not not_4 (out_43, 1'b0);
  not not_5 (out_57, 1'b0);
  not not_6 (out_59, 1'b0);
  not not_7 (out_73, 1'b0);
  not not_8 (out_89, 1'b0);
  not not_9 (out_105, 1'b0);
  not not_10 (out_123, 1'b0);
  not not_11 (out_121, 1'b0);
  not not_12 (out_31, 1'b0);
  not not_13 (out_45, 1'b0);
  not not_14 (out_61, 1'b0);
  not not_15 (out_79, 1'b0);
  not not_16 (out_77, 1'b0);
  not not_17 (out_111, 1'b0);
  not not_18 (out_125, 1'b0);
  not not_19 (out_17, 1'b0);
  not not_20 (out_19, 1'b0);
  not not_21 (out_33, 1'b0);
  not not_22 (out_35, 1'b0);
  not not_23 (out_49, 1'b0);
  not not_24 (out_51, 1'b0);
  not not_25 (out_83, 1'b0);
  not not_26 (out_81, 1'b0);
  not not_27 (out_99, 1'b0);
  not not_28 (out_97, 1'b0);
  not not_29 (out_115, 1'b0);
  not not_30 (out_113, 1'b0);
  not not_31 (out_23, 1'b0);
  not not_32 (out_21, 1'b0);
  not not_33 (out_37, 1'b0);
  not not_34 (out_55, 1'b0);
  not not_35 (out_69, 1'b0);
  not not_36 (out_85, 1'b0);
  not not_37 (out_119, 1'b0);
  not not_38 (out_133, 1'b0);
  not not_39 (out_12, 1'b0);
  not not_40 (out_10, 1'b0);
  not not_41 (out_26, 1'b0);
  not not_42 (out_44, 1'b0);
  not not_43 (out_60, 1'b0);
  not not_44 (out_58, 1'b0);
  not not_45 (out_90, 1'b0);
  not not_46 (out_92, 1'b0);
  not not_47 (out_14, 1'b0);
  not not_48 (out_30, 1'b0);
  not not_49 (out_32, 1'b0);
  not not_50 (out_48, 1'b0);
  not not_51 (out_62, 1'b0);
  not not_52 (out_64, 1'b0);
  not not_53 (out_94, 1'b0);
  not not_54 (out_96, 1'b0);
  not not_55 (out_18, 1'b0);
  not not_56 (out_36, 1'b0);
  not not_57 (out_34, 1'b0);
  not not_58 (out_66, 1'b0);
  not not_59 (out_68, 1'b0);
  not not_60 (out_100, 1'b0);
  not not_61 (out_98, 1'b0);
  not not_62 (out_40, 1'b0);
  not not_63 (out_72, 1'b0);
  not not_64 (out_70, 1'b0);
  not not_65 (out_88, 1'b0);
  not not_66 (out_102, 1'b0);
  not not_67 (out_104, 1'b0);

  assign out_11 = 1'b0;
  assign out_13 = 1'b0;
  assign out_15 = 1'b0;
  assign out_16 = 1'b0;
  assign out_20 = 1'b0;
  assign out_22 = 1'b0;
  assign out_24 = 1'b0;
  assign out_27 = 1'b0;
  assign out_28 = 1'b0;
  assign out_29 = 1'b0;
  assign out_38 = 1'b0;
  assign out_39 = 1'b0;
  assign out_42 = 1'b0;
  assign out_46 = 1'b0;
  assign out_47 = 1'b0;
  assign out_50 = 1'b0;
  assign out_52 = 1'b0;
  assign out_53 = 1'b0;
  assign out_54 = 1'b0;
  assign out_56 = 1'b0;
  assign out_63 = 1'b0;
  assign out_65 = 1'b0;
  assign out_67 = 1'b0;
  assign out_71 = 1'b0;
  assign out_74 = 1'b0;
  assign out_75 = 1'b0;
  assign out_76 = 1'b0;
  assign out_78 = 1'b0;
  assign out_80 = 1'b0;
  assign out_82 = 1'b0;
  assign out_84 = 1'b0;
  assign out_86 = 1'b0;
  assign out_87 = 1'b0;
  assign out_91 = 1'b0;
  assign out_93 = 1'b0;
  assign out_95 = 1'b0;
  assign out_101 = 1'b0;
  assign out_103 = 1'b0;
  assign out_106 = 1'b0;
  assign out_107 = 1'b0;
  assign out_108 = 1'b0;
  assign out_109 = 1'b0;
  assign out_110 = 1'b0;
  assign out_112 = 1'b0;
  assign out_114 = 1'b0;
  assign out_116 = 1'b0;
  assign out_117 = 1'b0;
  assign out_118 = 1'b0;
  assign out_120 = 1'b0;
  assign out_122 = in_1;
  assign out_124 = in_2;
  assign out_126 = in_3;
  assign out_127 = 1'b0;
  assign out_128 = in_4;
  assign out_129 = 1'b0;
  assign out_130 = in_5;
  assign out_131 = 1'b0;
  assign out_132 = in_6;
  assign out_134 = in_7;
  assign out_135 = 1'b0;
  assign out_136 = in_8;

  // Notes on the sheet:
  //   most significant --> least significant
  //   0
  //   1
  //   2
  //   3
  //   4
  //   5
  //   6
  //   7
  //   Numbers of the address in RAM
  //   A not gate gives a 1 and nothing gives a zero
  //   8
  //   9
  //   10
  //   11
  //   12
  //   13
  //   14
  //   15
endmodule
